// Logisim project XOR.circ as structural Verilog: 1 circuit, main circuit main
module main (
  input  X,
  input  Y,
  output O
);

  wire AND1_out, AND2_out, not_1_out, not_2_out;

  not not_1 (not_1_out, Y);
  not not_2 (not_2_out, X);
  and AND1 (AND1_out, X, not_1_out);
  and AND2 (AND2_out, not_2_out, Y);
  or OR1 (O, AND1_out, AND2_out);

  // Notes on the sheet:
  //   XOR
endmodule
