// Logisim project 4bitFA_DigitalSeg.circ as structural Verilog: 2 circuits, main circuit FourbitFA_DigitalSegHex
module FourbitFA_DigitalSegHex (
  input  C0,
  input  B0,
  input  A0,
  input  B1,
  input  A1,
  input  B2,
  input  A2,
  input  B3,
  input  A3
);

  wire digitalseghex_1_a, digitalseghex_1_b, digitalseghex_1_c, digitalseghex_1_d, digitalseghex_1_e,
       digitalseghex_1_f, digitalseghex_1_g, fa_1_cout, fa_1_sum, fa_2_cout, fa_2_sum, fa_3_cout, fa_3_sum,
       fa_4_cout, fa_4_sum;

  FA fa_1 (.A(A0), .B(B0), .Cin(C0), .Sum(fa_1_sum), .Cout(fa_1_cout));
  FA fa_2 (.A(A1), .B(B1), .Cin(fa_1_cout), .Sum(fa_2_sum), .Cout(fa_2_cout));
  FA fa_3 (.A(A2), .B(B2), .Cin(fa_2_cout), .Sum(fa_3_sum), .Cout(fa_3_cout));
  DigitalSegHex digitalseghex_1 (
    .D0(fa_1_sum), .D1(fa_2_sum), .D2(fa_3_sum), .D3(fa_4_sum), .A(digitalseghex_1_a), .B(digitalseghex_1_b),
    .C(digitalseghex_1_c), .D(digitalseghex_1_d), .E(digitalseghex_1_e), .F(digitalseghex_1_f),
    .G(digitalseghex_1_g));
  FA fa_4 (.A(A3), .B(B3), .Cin(fa_3_cout), .Sum(fa_4_sum), .Cout(fa_4_cout));
  _7_Segment_Display u_7_segment_display_1 (
    .g(digitalseghex_1_g), .f(digitalseghex_1_f), .a(digitalseghex_1_a), .b(digitalseghex_1_b),
    .e(digitalseghex_1_e), .d(digitalseghex_1_d), .c(digitalseghex_1_c), .dp(1'b0));
  LED led_1 (.in(fa_4_cout));
endmodule

module DigitalSegHex (
  input  D0,
  input  D1,
  input  D2,
  input  D3,
  output A,
  output B,
  output C,
  output D,
  output E,
  output F,
  output G
);

  wire decoder_1_out0, decoder_1_out1, decoder_1_out2, decoder_1_out3, decoder_1_out4, decoder_1_out5,
       decoder_1_out6, decoder_1_out7, decoder_1_out8, decoder_1_out9, decoder_1_out10, decoder_1_out11,
       decoder_1_out12, decoder_1_out13, decoder_1_out14, decoder_1_out15;

  Decoder #(.select(4)) decoder_1 (
    .out0(decoder_1_out0), .out1(decoder_1_out1), .out2(decoder_1_out2), .out3(decoder_1_out3),
    .out4(decoder_1_out4), .out5(decoder_1_out5), .out6(decoder_1_out6), .out7(decoder_1_out7),
    .out8(decoder_1_out8), .out9(decoder_1_out9), .out10(decoder_1_out10), .out11(decoder_1_out11),
    .out12(decoder_1_out12), .out13(decoder_1_out13), .out14(decoder_1_out14), .out15(decoder_1_out15),
    .sel({D3, D2, D1, D0}), .en(1'b1));
  or or_1 (A, decoder_1_out0, decoder_1_out2, decoder_1_out3, decoder_1_out5, decoder_1_out6, decoder_1_out7, decoder_1_out8, decoder_1_out9, decoder_1_out10, decoder_1_out12, decoder_1_out14, decoder_1_out15);
  or or_2 (B, decoder_1_out0, decoder_1_out1, decoder_1_out2, decoder_1_out3, decoder_1_out4, decoder_1_out7, decoder_1_out8, decoder_1_out9, decoder_1_out10, decoder_1_out13);
  or or_3 (C, decoder_1_out0, decoder_1_out1, decoder_1_out3, decoder_1_out4, decoder_1_out5, decoder_1_out6, decoder_1_out7, decoder_1_out8, decoder_1_out9, decoder_1_out10, decoder_1_out11, decoder_1_out13);
  or or_4 (D, decoder_1_out0, decoder_1_out2, decoder_1_out3, decoder_1_out5, decoder_1_out6, decoder_1_out8, decoder_1_out9, decoder_1_out11, decoder_1_out12, decoder_1_out13, decoder_1_out14);
  or or_5 (E, decoder_1_out0, decoder_1_out2, decoder_1_out6, decoder_1_out8, decoder_1_out10, decoder_1_out11, decoder_1_out12, decoder_1_out13, decoder_1_out14, decoder_1_out15);
  or or_6 (F, decoder_1_out0, decoder_1_out4, decoder_1_out5, decoder_1_out6, decoder_1_out8, decoder_1_out9, decoder_1_out10, decoder_1_out11, decoder_1_out12, decoder_1_out14, decoder_1_out15);
  or or_7 (G, decoder_1_out2, decoder_1_out3, decoder_1_out4, decoder_1_out5, decoder_1_out6, decoder_1_out8, decoder_1_out9, decoder_1_out10, decoder_1_out11, decoder_1_out13, decoder_1_out14, decoder_1_out15);

  // Notes on the sheet:
  //   A
  //   B
  //   C
  //   D
  //   E
  //   F
  //   G
endmodule
