// Logisim project FA_with_HA.circ as structural Verilog: 1 circuit, main circuit main
module main (
  input  A,
  input  B,
  input  Cin,
  output Cout,
  output S
);

  wire ha_1_c, ha_1_s, ha_2_c;

  HA ha_1 (.A(A), .B(B), .S(ha_1_s), .C(ha_1_c));
  HA ha_2 (.A(ha_1_s), .B(Cin), .S(S), .C(ha_2_c));
  or or_1 (Cout, ha_1_c, ha_2_c);
endmodule
