// Logisim project Half_Adder.circ as structural Verilog: 1 circuit, main circuit HA
module HA (
  input  A,
  input  B,
  output S,
  output C
);

  xor xor_1 (S, A, B);
  and and_1 (C, A, B);
endmodule
