// Logisim project Subtractor.circ as structural Verilog: 3 circuits, main circuit fourBitSubtractor
module fourBitSubtractor (
  input  Bin,
  input  B0,
  input  A0,
  input  B1,
  input  A1,
  input  B2,
  input  A2,
  input  B3,
  input  A3,
  output D0,
  output D1,
  output D2,
  output D3,
  output Bout
);

  wire onebitsubtractor_1_bout, onebitsubtractor_2_bout, onebitsubtractor_3_bout;

  oneBitSubtractor onebitsubtractor_1 (.Bin(Bin), .A(A0), .B(B0), .D(D0), .Bout(onebitsubtractor_1_bout));
  oneBitSubtractor onebitsubtractor_2 (
    .Bin(onebitsubtractor_1_bout), .A(A1), .B(B1), .D(D1), .Bout(onebitsubtractor_2_bout));
  oneBitSubtractor onebitsubtractor_3 (
    .Bin(onebitsubtractor_2_bout), .A(A2), .B(B2), .D(D2), .Bout(onebitsubtractor_3_bout));
  oneBitSubtractor onebitsubtractor_4 (.Bin(onebitsubtractor_3_bout), .A(A3), .B(B3), .D(D3), .Bout(Bout));
endmodule

module oneBitSubtractor (
  input  Bin,
  input  A,
  input  B,
  output D,
  output Bout
);

  wire and_1_out, and_2_out, and_3_out, xor_1_out;

  and and_1 (and_1_out, Bin, B);
  and and_2 (and_2_out, ~A, Bin);  // AND_Gate
  and and_3 (and_3_out, ~A, B);  // AND_Gate
  xor xor_1 (xor_1_out, Bin, A);
  or or_1 (Bout, and_1_out, and_2_out, and_3_out);
  xor xor_2 (D, xor_1_out, B);
endmodule

module fourBitSub_digitalSeg (
);

  wire digitalseghex_1_a, digitalseghex_1_b, digitalseghex_1_c, digitalseghex_1_d, digitalseghex_1_e,
       digitalseghex_1_f, digitalseghex_1_g, digitalseghex_2_a, digitalseghex_2_b, digitalseghex_2_c,
       digitalseghex_2_d, digitalseghex_2_e, digitalseghex_2_f, digitalseghex_2_g, digitalseghex_3_a,
       digitalseghex_3_b, digitalseghex_3_c, digitalseghex_3_d, digitalseghex_3_e, digitalseghex_3_f,
       digitalseghex_3_g, dipswitch_1_sw1, dipswitch_1_sw2, dipswitch_1_sw3, dipswitch_1_sw4, dipswitch_2_p1,
       dipswitch_2_p2, dipswitch_2_p3, dipswitch_2_p4, fourbitsubtractor_1_bout, fourbitsubtractor_1_d0,
       fourbitsubtractor_1_d1, fourbitsubtractor_1_d2, fourbitsubtractor_1_d3;

  DipSwitch #(.number(4)) dipswitch_1 (
    .sw1(dipswitch_1_sw1), .sw2(dipswitch_1_sw2), .sw3(dipswitch_1_sw3), .sw4(dipswitch_1_sw4));
  // DipSwitch #(.number(4)) dipswitch_2: pin names not known; wires that end beside it: dipswitch_2_p1, dipswitch_2_p2, dipswitch_2_p3, dipswitch_2_p4, dipswitch_2_p2
  DigitalSegHex digitalseghex_1 (
    .D0(dipswitch_2_p1), .D1(dipswitch_2_p2), .D2(dipswitch_2_p3), .D3(dipswitch_2_p4),
    .A(digitalseghex_1_a), .B(digitalseghex_1_b), .C(digitalseghex_1_c), .D(digitalseghex_1_d),
    .E(digitalseghex_1_e), .F(digitalseghex_1_f), .G(digitalseghex_1_g));
  DigitalSegHex digitalseghex_2 (
    .D0(dipswitch_1_sw1), .D1(dipswitch_1_sw2), .D2(dipswitch_1_sw3), .D3(dipswitch_1_sw4),
    .A(digitalseghex_2_a), .B(digitalseghex_2_b), .C(digitalseghex_2_c), .D(digitalseghex_2_d),
    .E(digitalseghex_2_e), .F(digitalseghex_2_f), .G(digitalseghex_2_g));
  _7_Segment_Display u_7_segment_display_1 (
    .g(digitalseghex_1_g), .f(digitalseghex_1_f), .a(digitalseghex_1_a), .b(digitalseghex_1_b),
    .e(digitalseghex_1_e), .d(digitalseghex_1_d), .c(digitalseghex_1_c), .dp(1'b0));
  _7_Segment_Display u_7_segment_display_2 (
    .g(digitalseghex_2_g), .f(digitalseghex_2_f), .a(digitalseghex_2_a), .b(digitalseghex_2_b),
    .e(digitalseghex_2_e), .d(digitalseghex_2_d), .c(digitalseghex_2_c), .dp(1'b0));
  fourBitSubtractor fourbitsubtractor_1 (
    .Bin(1'b0), .B0(dipswitch_1_sw1), .A0(dipswitch_2_p1), .B1(dipswitch_1_sw2), .A1(dipswitch_2_p2),
    .B2(dipswitch_1_sw3), .A2(dipswitch_2_p3), .B3(dipswitch_1_sw4), .A3(dipswitch_2_p4),
    .D0(fourbitsubtractor_1_d0), .D1(fourbitsubtractor_1_d1), .D2(fourbitsubtractor_1_d2),
    .D3(fourbitsubtractor_1_d3), .Bout(fourbitsubtractor_1_bout));
  LED led_1 (.in(fourbitsubtractor_1_bout));
  _7_Segment_Display u_7_segment_display_3 (
    .g(digitalseghex_3_g), .f(digitalseghex_3_f), .a(digitalseghex_3_a), .b(digitalseghex_3_b),
    .e(digitalseghex_3_e), .d(digitalseghex_3_d), .c(digitalseghex_3_c), .dp(1'b0));
  DigitalSegHex digitalseghex_3 (
    .D0(fourbitsubtractor_1_d0), .D1(fourbitsubtractor_1_d1), .D2(fourbitsubtractor_1_d2),
    .D3(fourbitsubtractor_1_d3), .A(digitalseghex_3_a), .B(digitalseghex_3_b), .C(digitalseghex_3_c),
    .D(digitalseghex_3_d), .E(digitalseghex_3_e), .F(digitalseghex_3_f), .G(digitalseghex_3_g));

  // Notes on the sheet:
  //   A
  //   B
  //   D
endmodule
