// Logisim project onesComplementAdder.circ as structural Verilog: 3 circuits, main circuit onesComplementAdder
module onesComplementAdder (
  input  A0,
  input  A1,
  input  A2,
  input  A3,
  input  B0,
  input  B1,
  input  B2,
  input  B3,
  output S0,
  output S1,
  output S2,
  output S3
);

  wire decoderhex_1_a, decoderhex_1_b, decoderhex_1_c, decoderhex_1_d, decoderhex_1_e, decoderhex_1_f,
       decoderhex_1_g, decoderhex_1_h, decoderhex_2_a, decoderhex_2_b, decoderhex_2_c, decoderhex_2_d,
       decoderhex_2_e, decoderhex_2_f, decoderhex_2_g, decoderhex_2_h, decoderhex_3_a, decoderhex_3_b,
       decoderhex_3_c, decoderhex_3_d, decoderhex_3_e, decoderhex_3_f, decoderhex_3_g, decoderhex_3_h;
  wire [2:0] not_1_out, not_4_out, not_7_out;
  wire [3:0] multiplexer_1_out, multiplexer_2_out, signandmagnitude4bitadder_1_s0;

  not not_1 (not_1_out[0], A0);
  not not_2 (not_1_out[1], A1);
  not not_3 (not_1_out[2], A2);
  not not_4 (not_4_out[0], B0);
  not not_5 (not_4_out[1], B1);
  not not_6 (not_4_out[2], B2);
  DecoderHex decoderhex_1 (
    .I0(A0), .I1(A1), .I2(A2), .I3(1'b0), .A(decoderhex_1_a), .B(decoderhex_1_b), .C(decoderhex_1_c),
    .D(decoderhex_1_d), .E(decoderhex_1_e), .F(decoderhex_1_f), .G(decoderhex_1_g), .H(decoderhex_1_h));
  DecoderHex decoderhex_2 (
    .I0(B0), .I1(B1), .I2(B2), .I3(1'b0), .A(decoderhex_2_a), .B(decoderhex_2_b), .C(decoderhex_2_c),
    .D(decoderhex_2_d), .E(decoderhex_2_e), .F(decoderhex_2_f), .G(decoderhex_2_g), .H(decoderhex_2_h));
  Multiplexer #(.width(4)) multiplexer_1 (
    .in0({A3, A2, A1, A0}), .in1({A3, not_1_out}), .out(multiplexer_1_out), .sel(A3));
  Multiplexer #(.width(4)) multiplexer_2 (
    .in0({B3, B2, B1, B0}), .in1({B3, not_4_out}), .out(multiplexer_2_out), .sel(B3));
  _7_Segment_Display u_7_segment_display_1 (.g(A3));  // open: f, a, b, e, d, c, dp
  _7_Segment_Display u_7_segment_display_2 (.g(B3));  // open: f, a, b, e, d, c, dp
  _7_Segment_Display u_7_segment_display_3 (
    .g(decoderhex_1_g), .f(decoderhex_1_f), .a(decoderhex_1_a), .b(decoderhex_1_b), .e(decoderhex_1_e),
    .d(decoderhex_1_d), .c(decoderhex_1_c), .dp(decoderhex_1_h));
  _7_Segment_Display u_7_segment_display_4 (
    .g(decoderhex_2_g), .f(decoderhex_2_f), .a(decoderhex_2_a), .b(decoderhex_2_b), .e(decoderhex_2_e),
    .d(decoderhex_2_d), .c(decoderhex_2_c), .dp(decoderhex_2_h));
  signAndMagnitude4bitAdder signandmagnitude4bitadder_1 (
    .A0(multiplexer_1_out[0]), .A1(multiplexer_1_out[1]), .A2(multiplexer_1_out[2]),
    .A3(multiplexer_1_out[3]), .B0(multiplexer_2_out[0]), .B1(multiplexer_2_out[1]),
    .B2(multiplexer_2_out[2]), .B3(multiplexer_2_out[3]), .S0(signandmagnitude4bitadder_1_s0[0]),
    .S1(signandmagnitude4bitadder_1_s0[1]), .S2(signandmagnitude4bitadder_1_s0[2]),
    .S3(signandmagnitude4bitadder_1_s0[3]));
  not not_7 (not_7_out[0], signandmagnitude4bitadder_1_s0[0]);
  not not_8 (not_7_out[1], signandmagnitude4bitadder_1_s0[1]);
  not not_9 (not_7_out[2], signandmagnitude4bitadder_1_s0[2]);
  Multiplexer #(.width(4)) multiplexer_3 (
    .in0(signandmagnitude4bitadder_1_s0), .in1({signandmagnitude4bitadder_1_s0[3], not_7_out}),
    .out({S3, S2, S1, S0}), .sel(signandmagnitude4bitadder_1_s0[3]));
  DecoderHex decoderhex_3 (
    .I0(signandmagnitude4bitadder_1_s0[0]), .I1(signandmagnitude4bitadder_1_s0[1]),
    .I2(signandmagnitude4bitadder_1_s0[2]), .A(decoderhex_3_a), .B(decoderhex_3_b), .C(decoderhex_3_c),
    .D(decoderhex_3_d), .E(decoderhex_3_e), .F(decoderhex_3_f), .G(decoderhex_3_g), .H(decoderhex_3_h));  // open: I3
  _7_Segment_Display u_7_segment_display_5 (.g(signandmagnitude4bitadder_1_s0[3]));  // open: f, a, b, e, d, c, dp
  _7_Segment_Display u_7_segment_display_6 (
    .g(decoderhex_3_g), .f(decoderhex_3_f), .a(decoderhex_3_a), .b(decoderhex_3_b), .e(decoderhex_3_e),
    .d(decoderhex_3_d), .c(decoderhex_3_c), .dp(decoderhex_3_h));

  // Notes on the sheet:
  //   B
  //   A
endmodule

module signAndMagnitude4bitAdder (
  input  A0,
  input  A1,
  input  A2,
  input  A3,
  input  B0,
  input  B1,
  input  B2,
  input  B3,
  output S0,
  output S1,
  output S2,
  output S3
);

  wire AminusB_bout, and_1_out, and_2_out, and_3_out, and_4_out, BminusA_bout, decoderhex_1_a,
       decoderhex_1_b, decoderhex_1_c, decoderhex_1_d, decoderhex_1_e, decoderhex_1_f, decoderhex_1_g,
       decoderhex_1_h, decoderhex_2_a, decoderhex_2_b, decoderhex_2_c, decoderhex_2_d, decoderhex_2_e,
       decoderhex_2_f, decoderhex_2_g, decoderhex_2_h, decoderhex_3_a, decoderhex_3_b, decoderhex_3_c,
       decoderhex_3_d, decoderhex_3_e, decoderhex_3_f, decoderhex_3_g, decoderhex_3_h, fa_4bit_2_cout,
       not_2_out, or_2_out, xnor_1_out;
  wire [1:0] or_1_out;
  wire [2:0] AminusB_d1, BminusA_d1;
  wire [3:0] fa_4bit_1_s3, multiplexer_1_out;
  wire [3:3] not_1_out;

  xnor xnor_1 (xnor_1_out, B3, A3);
  DecoderHex decoderhex_1 (
    .I0(B0), .I1(B1), .I2(B2), .A(decoderhex_1_a), .B(decoderhex_1_b), .C(decoderhex_1_c),
    .D(decoderhex_1_d), .E(decoderhex_1_e), .F(decoderhex_1_f), .G(decoderhex_1_g), .H(decoderhex_1_h));  // open: I3
  DecoderHex decoderhex_2 (
    .I0(A0), .I1(A1), .I2(A2), .A(decoderhex_2_a), .B(decoderhex_2_b), .C(decoderhex_2_c),
    .D(decoderhex_2_d), .E(decoderhex_2_e), .F(decoderhex_2_f), .G(decoderhex_2_g), .H(decoderhex_2_h));  // open: I3
  _7_Segment_Display u_7_segment_display_1 (.g(B3));  // open: f, a, b, e, d, c, dp
  _7_Segment_Display u_7_segment_display_2 (.g(A3));  // open: f, a, b, e, d, c, dp
  _7_Segment_Display u_7_segment_display_3 (
    .g(decoderhex_1_g), .f(decoderhex_1_f), .a(decoderhex_1_a), .b(decoderhex_1_b), .e(decoderhex_1_e),
    .d(decoderhex_1_d), .c(decoderhex_1_c), .dp(decoderhex_1_h));
  _7_Segment_Display u_7_segment_display_4 (
    .g(decoderhex_2_g), .f(decoderhex_2_f), .a(decoderhex_2_a), .b(decoderhex_2_b), .e(decoderhex_2_e),
    .d(decoderhex_2_d), .c(decoderhex_2_c), .dp(decoderhex_2_h));
  FA_4bit fa_4bit_1 (
    .Cin(1'b0), .B0(B0), .A0(A0), .B1(B1), .A1(A1), .B2(B2), .A2(A2), .B3(B3), .A3(A3), .S0(fa_4bit_1_s3[0]),
    .S1(fa_4bit_1_s3[1]), .S2(fa_4bit_1_s3[2]), .S3(fa_4bit_1_s3[3]));  // open: Cout
  FS_4bit AminusB (
    .Bin(1'b0), .B0(1'b0), .A0(1'b0), .B1(B0), .A1(A0), .B2(B1), .A2(A1), .B3(B2), .A3(A2),
    .D1(AminusB_d1[0]), .D2(AminusB_d1[1]), .D3(AminusB_d1[2]), .Bout(AminusB_bout));  // open: D0
  FS_4bit BminusA (
    .Bin(1'b0), .B0(1'b0), .A0(1'b0), .B1(A0), .A1(B0), .B2(A1), .A2(B1), .B3(A2), .A3(B2),
    .D1(BminusA_d1[0]), .D2(BminusA_d1[1]), .D3(BminusA_d1[2]), .Bout(BminusA_bout));  // open: D0
  FA_4bit fa_4bit_2 (
    .Cin(1'b0), .B0(1'b0), .A0(1'b0), .B1(B0), .A1(A0), .B2(B1), .A2(A1), .B3(B2), .A3(A2),
    .Cout(fa_4bit_2_cout));  // open: S0, S1, S2, S3
  and and_1 (and_1_out, A3, AminusB_bout);
  and and_2 (and_2_out, B3, AminusB_bout);
  or or_1 (or_1_out[0], and_1_out, and_2_out, and_3_out);
  and and_3 (and_3_out, A3, B3);
  and and_4 (and_4_out, fa_4bit_2_cout, xnor_1_out);
  xor xor_1 (or_1_out[1], A3, B3);
  not not_1 (not_1_out[3], fa_4bit_1_s3[3]);
  LED led_1 (.in(and_4_out));
  not not_2 (not_2_out, and_4_out);
  Multiplexer #(.select(2), .width(4)) multiplexer_1 (
    .in0(fa_4bit_1_s3), .in1({not_1_out[3], fa_4bit_1_s3[2:0]}), .in2({A3, AminusB_d1}),
    .in3({B3, BminusA_d1}), .out(multiplexer_1_out), .sel(or_1_out));
  and and_5 (S0, multiplexer_1_out[0], not_2_out);
  and and_6 (S1, multiplexer_1_out[1], not_2_out);
  and and_7 (S2, multiplexer_1_out[2], not_2_out);
  or or_2 (or_2_out, S0, S1, S2);
  DecoderHex decoderhex_3 (
    .I0(S0), .I1(S1), .I2(S2), .I3(1'b0), .A(decoderhex_3_a), .B(decoderhex_3_b), .C(decoderhex_3_c),
    .D(decoderhex_3_d), .E(decoderhex_3_e), .F(decoderhex_3_f), .G(decoderhex_3_g), .H(decoderhex_3_h));
  and and_8 (S3, multiplexer_1_out[3], or_2_out);
  _7_Segment_Display u_7_segment_display_5 (.g(S3));  // open: f, a, b, e, d, c, dp
  _7_Segment_Display u_7_segment_display_6 (
    .g(decoderhex_3_g), .f(decoderhex_3_f), .a(decoderhex_3_a), .b(decoderhex_3_b), .e(decoderhex_3_e),
    .d(decoderhex_3_d), .c(decoderhex_3_c), .dp(decoderhex_3_h));

  // Notes on the sheet:
  //   B
  //   A
  //   溢出检测
  //   正数+正数
  //   负数+负数
  //   Bout
  //   Bout输出为1说明A绝对值<B绝对值
  //   Bout输出为0说明A绝对值>B绝对值
  //   LED指示溢出
  //   此时符号位取决于B，数值为B的绝对值减A的绝对值
  //   此时符号位取决于A，数值为A的绝对值减B的绝对值
  //   选择信号00为正数+正数 01为负数加负数
  //   选择信号10为有一负数且A的绝对值大于B的绝对值 11为有一负数且A的绝对值小于B的绝对值
  //   输出0时不显示负号
endmodule

module simple (
  input  A0,
  input  A1,
  input  A2,
  input  A3,
  input  B0,
  input  B1,
  input  B2,
  input  B3,
  output S0,
  output S1,
  output S2,
  output S3
);

  wire [2:0] not_1_out, not_4_out, not_7_out;
  wire [3:0] multiplexer_1_out, multiplexer_2_out, signandmagnitude4bitadder_1_s0;

  not not_1 (not_1_out[0], A0);
  not not_2 (not_1_out[1], A1);
  not not_3 (not_1_out[2], A2);
  not not_4 (not_4_out[0], B0);
  not not_5 (not_4_out[1], B1);
  not not_6 (not_4_out[2], B2);
  Multiplexer #(.width(4)) multiplexer_1 (
    .in0({A3, A2, A1, A0}), .in1({A3, not_1_out}), .out(multiplexer_1_out), .sel(A3));
  Multiplexer #(.width(4)) multiplexer_2 (
    .in0({B3, B2, B1, B0}), .in1({B3, not_4_out}), .out(multiplexer_2_out), .sel(B3));
  signAndMagnitude4bitAdder signandmagnitude4bitadder_1 (
    .A0(multiplexer_1_out[0]), .A1(multiplexer_1_out[1]), .A2(multiplexer_1_out[2]),
    .A3(multiplexer_1_out[3]), .B0(multiplexer_2_out[0]), .B1(multiplexer_2_out[1]),
    .B2(multiplexer_2_out[2]), .B3(multiplexer_2_out[3]), .S0(signandmagnitude4bitadder_1_s0[0]),
    .S1(signandmagnitude4bitadder_1_s0[1]), .S2(signandmagnitude4bitadder_1_s0[2]),
    .S3(signandmagnitude4bitadder_1_s0[3]));
  not not_7 (not_7_out[0], signandmagnitude4bitadder_1_s0[0]);
  not not_8 (not_7_out[1], signandmagnitude4bitadder_1_s0[1]);
  not not_9 (not_7_out[2], signandmagnitude4bitadder_1_s0[2]);
  Multiplexer #(.width(4)) multiplexer_3 (
    .in0(signandmagnitude4bitadder_1_s0), .in1({signandmagnitude4bitadder_1_s0[3], not_7_out}),
    .out({S3, S2, S1, S0}), .sel(signandmagnitude4bitadder_1_s0[3]));
endmodule
