// Logisim project onesComplementAdder2.circ as structural Verilog: 3 circuits, main circuit ComplementAdder2
module ComplementAdder2 (
  output S3,
  output S2,
  output S1,
  output S0
);

  wire A_sw1, A_sw2, A_sw3, A_sw4, B_sw1, B_sw2, B_sw3, B_sw4, fa4bit_1_cout, fa4bit_1_s0, fa4bit_1_s1,
       fa4bit_1_s2, fa4bit_1_s3;

  DipSwitch #(.number(4)) A (.sw1(A_sw1), .sw2(A_sw2), .sw3(A_sw3), .sw4(A_sw4));
  DipSwitch #(.number(4)) B (.sw1(B_sw1), .sw2(B_sw2), .sw3(B_sw3), .sw4(B_sw4));
  FA4bit fa4bit_1 (
    .Cin(1'b0), .B0(B_sw1), .A0(A_sw1), .B1(B_sw2), .A1(A_sw2), .B2(B_sw3), .A2(A_sw3), .B3(B_sw4),
    .A3(A_sw4), .S0(fa4bit_1_s0), .S1(fa4bit_1_s1), .S2(fa4bit_1_s2), .S3(fa4bit_1_s3), .Cout(fa4bit_1_cout));
  FA4bit fa4bit_2 (
    .Cin(1'b0), .B0(fa4bit_1_cout), .A0(fa4bit_1_s0), .B1(1'b0), .A1(fa4bit_1_s1), .B2(1'b0),
    .A2(fa4bit_1_s2), .B3(1'b0), .A3(fa4bit_1_s3), .S0(S0), .S1(S1), .S2(S2), .S3(S3));  // open: Cout
endmodule

module FA1bit (
  input  A,
  input  B,
  input  Cin,
  output Sum,
  output Cout
);

  wire and_1_out, and_2_out, xor_1_out;

  xor xor_1 (xor_1_out, A, B);
  and and_1 (and_1_out, A, B);
  xor xor_2 (Sum, xor_1_out, Cin);
  and and_2 (and_2_out, xor_1_out, Cin);
  or or_1 (Cout, and_2_out, and_1_out);
endmodule

module FA4bit (
  input  Cin,
  input  B0,
  input  A0,
  input  B1,
  input  A1,
  input  B2,
  input  A2,
  input  B3,
  input  A3,
  output S0,
  output S1,
  output S2,
  output S3,
  output Cout
);

  wire fa1bit_1_cout, fa1bit_2_cout, fa1bit_3_cout;

  FA1bit fa1bit_1 (.A(A0), .B(B0), .Cin(Cin), .Sum(S0), .Cout(fa1bit_1_cout));
  FA1bit fa1bit_2 (.A(A1), .B(B1), .Cin(fa1bit_1_cout), .Sum(S1), .Cout(fa1bit_2_cout));
  FA1bit fa1bit_3 (.A(A2), .B(B2), .Cin(fa1bit_2_cout), .Sum(S2), .Cout(fa1bit_3_cout));
  FA1bit fa1bit_4 (.A(A3), .B(B3), .Cin(fa1bit_3_cout), .Sum(S3), .Cout(Cout));
endmodule
