// Logisim project signAndMagnitudeAdder.circ as structural Verilog: 6 circuits, main circuit FA_4bit
module FA_4bit (
  input  Cin,
  input  B0,
  input  A0,
  input  B1,
  input  A1,
  input  B2,
  input  A2,
  input  B3,
  input  A3,
  output S0,
  output S1,
  output S2,
  output S3,
  output Cout
);

  wire fa_1bit_1_cout, fa_1bit_2_cout, fa_1bit_3_cout;

  FA_1bit fa_1bit_1 (.A(A0), .B(B0), .Cin(Cin), .Sum(S0), .Cout(fa_1bit_1_cout));
  FA_1bit fa_1bit_2 (.A(A1), .B(B1), .Cin(fa_1bit_1_cout), .Sum(S1), .Cout(fa_1bit_2_cout));
  FA_1bit fa_1bit_3 (.A(A2), .B(B2), .Cin(fa_1bit_2_cout), .Sum(S2), .Cout(fa_1bit_3_cout));
  FA_1bit fa_1bit_4 (.A(A3), .B(B3), .Cin(fa_1bit_3_cout), .Sum(S3), .Cout(Cout));
endmodule

module FS_1bit (
  input  Bin,
  input  A,
  input  B,
  output D,
  output Bout
);

  wire and_1_out, and_2_out, and_3_out, xor_1_out;

  and and_1 (and_1_out, Bin, B);
  and and_2 (and_2_out, ~A, Bin);  // AND_Gate
  and and_3 (and_3_out, ~A, B);  // AND_Gate
  xor xor_1 (xor_1_out, Bin, A);
  or or_1 (Bout, and_1_out, and_2_out, and_3_out);
  xor xor_2 (D, xor_1_out, B);
endmodule

module FS_4bit (
  input  Bin,
  input  B0,
  input  A0,
  input  B1,
  input  A1,
  input  B2,
  input  A2,
  input  B3,
  input  A3,
  output D0,
  output D1,
  output D2,
  output D3,
  output Bout
);

  wire fs_1bit_1_bout, fs_1bit_2_bout, fs_1bit_3_bout;

  FS_1bit fs_1bit_1 (.Bin(Bin), .A(A0), .B(B0), .D(D0), .Bout(fs_1bit_1_bout));
  FS_1bit fs_1bit_2 (.Bin(fs_1bit_1_bout), .A(A1), .B(B1), .D(D1), .Bout(fs_1bit_2_bout));
  FS_1bit fs_1bit_3 (.Bin(fs_1bit_2_bout), .A(A2), .B(B2), .D(D2), .Bout(fs_1bit_3_bout));
  FS_1bit fs_1bit_4 (.Bin(fs_1bit_3_bout), .A(A3), .B(B3), .D(D3), .Bout(Bout));
endmodule

module FA_1bit (
  input  A,
  input  B,
  input  Cin,
  output Sum,
  output Cout
);

  wire and_1_out, and_2_out, xor_1_out;

  xor xor_1 (xor_1_out, A, B);
  and and_1 (and_1_out, A, B);
  xor xor_2 (Sum, xor_1_out, Cin);
  and and_2 (and_2_out, xor_1_out, Cin);
  or or_1 (Cout, and_2_out, and_1_out);
endmodule

module signAndMagnitudeAdder (
);

  wire AminusB_bout, and_1_out, and_2_out, and_3_out, and_4_out, and_5_out, and_6_out, and_7_out, and_8_out,
       BminusA_bout, decoderhex_1_a, decoderhex_1_b, decoderhex_1_c, decoderhex_1_d, decoderhex_1_e,
       decoderhex_1_f, decoderhex_1_g, decoderhex_1_h, decoderhex_2_a, decoderhex_2_b, decoderhex_2_c,
       decoderhex_2_d, decoderhex_2_e, decoderhex_2_f, decoderhex_2_g, decoderhex_2_h, decoderhex_3_a,
       decoderhex_3_b, decoderhex_3_c, decoderhex_3_d, decoderhex_3_e, decoderhex_3_f, decoderhex_3_g,
       decoderhex_3_h, fa_4bit_2_cout, inputA_p1, inputA_p2, inputA_p3, inputA_p5, inputB_p1, inputB_p2,
       not_2_out, or_2_out, xnor_1_out;
  wire [1:0] or_1_out;
  wire [3:0] AminusB_d1, BminusA_d1, fa_4bit_1_s3, multiplexer_1_out;
  wire [3:3] not_1_out;

  // DipSwitch #(.number(4)) inputA: pin names not known; wires that end beside it: inputA_p1, inputA_p2, inputA_p3, AminusB_d1[3], inputA_p5
  // DipSwitch #(.number(4)) inputB: pin names not known; wires that end beside it: inputB_p1, inputB_p2, BminusA_d1[3]
  xnor xnor_1 (xnor_1_out, BminusA_d1[3], AminusB_d1[3]);
  DecoderHex decoderhex_1 (
    .I0(inputA_p5), .I1(inputB_p1), .I2(inputB_p2), .A(decoderhex_1_a), .B(decoderhex_1_b),
    .C(decoderhex_1_c), .D(decoderhex_1_d), .E(decoderhex_1_e), .F(decoderhex_1_f), .G(decoderhex_1_g),
    .H(decoderhex_1_h));  // open: I3
  DecoderHex decoderhex_2 (
    .I0(inputA_p1), .I1(inputA_p2), .I2(inputA_p3), .A(decoderhex_2_a), .B(decoderhex_2_b),
    .C(decoderhex_2_c), .D(decoderhex_2_d), .E(decoderhex_2_e), .F(decoderhex_2_f), .G(decoderhex_2_g),
    .H(decoderhex_2_h));  // open: I3
  _7_Segment_Display u_7_segment_display_1 (.g(BminusA_d1[3]));  // open: f, a, b, e, d, c, dp
  _7_Segment_Display u_7_segment_display_2 (.g(AminusB_d1[3]));  // open: f, a, b, e, d, c, dp
  _7_Segment_Display u_7_segment_display_3 (
    .g(decoderhex_1_g), .f(decoderhex_1_f), .a(decoderhex_1_a), .b(decoderhex_1_b), .e(decoderhex_1_e),
    .d(decoderhex_1_d), .c(decoderhex_1_c), .dp(decoderhex_1_h));
  _7_Segment_Display u_7_segment_display_4 (
    .g(decoderhex_2_g), .f(decoderhex_2_f), .a(decoderhex_2_a), .b(decoderhex_2_b), .e(decoderhex_2_e),
    .d(decoderhex_2_d), .c(decoderhex_2_c), .dp(decoderhex_2_h));
  FA_4bit fa_4bit_1 (
    .Cin(1'b0), .B0(inputA_p5), .A0(inputA_p1), .B1(inputB_p1), .A1(inputA_p2), .B2(inputB_p2),
    .A2(inputA_p3), .B3(BminusA_d1[3]), .A3(AminusB_d1[3]), .S0(fa_4bit_1_s3[0]), .S1(fa_4bit_1_s3[1]),
    .S2(fa_4bit_1_s3[2]), .S3(fa_4bit_1_s3[3]));  // open: Cout
  FS_4bit AminusB (
    .Bin(1'b0), .B0(1'b0), .A0(1'b0), .B1(inputA_p5), .A1(inputA_p1), .B2(inputB_p1), .A2(inputA_p2),
    .B3(inputB_p2), .A3(inputA_p3), .D1(AminusB_d1[0]), .D2(AminusB_d1[1]), .D3(AminusB_d1[2]),
    .Bout(AminusB_bout));  // open: D0
  FS_4bit BminusA (
    .Bin(1'b0), .B0(1'b0), .A0(1'b0), .B1(inputA_p1), .A1(inputA_p5), .B2(inputA_p2), .A2(inputB_p1),
    .B3(inputA_p3), .A3(inputB_p2), .D1(BminusA_d1[0]), .D2(BminusA_d1[1]), .D3(BminusA_d1[2]),
    .Bout(BminusA_bout));  // open: D0
  FA_4bit fa_4bit_2 (
    .Cin(1'b0), .B0(1'b0), .A0(1'b0), .B1(inputA_p5), .A1(inputA_p1), .B2(inputB_p1), .A2(inputA_p2),
    .B3(inputB_p2), .A3(inputA_p3), .Cout(fa_4bit_2_cout));  // open: S0, S1, S2, S3
  and and_1 (and_1_out, AminusB_d1[3], AminusB_bout);
  and and_2 (and_2_out, BminusA_d1[3], AminusB_bout);
  or or_1 (or_1_out[0], and_1_out, and_2_out, and_3_out);
  and and_3 (and_3_out, AminusB_d1[3], BminusA_d1[3]);
  and and_4 (and_4_out, fa_4bit_2_cout, xnor_1_out);
  xor xor_1 (or_1_out[1], AminusB_d1[3], BminusA_d1[3]);
  not not_1 (not_1_out[3], fa_4bit_1_s3[3]);
  LED led_1 (.in(and_4_out));
  not not_2 (not_2_out, and_4_out);
  Multiplexer #(.select(2), .width(4)) multiplexer_1 (
    .in0(fa_4bit_1_s3), .in1({not_1_out[3], fa_4bit_1_s3[2:0]}), .in2(AminusB_d1), .in3(BminusA_d1),
    .out(multiplexer_1_out), .sel(or_1_out));
  and and_5 (and_5_out, multiplexer_1_out[0], not_2_out);
  and and_6 (and_6_out, multiplexer_1_out[1], not_2_out);
  and and_7 (and_7_out, multiplexer_1_out[2], not_2_out);
  or or_2 (or_2_out, and_5_out, and_6_out, and_7_out);
  DecoderHex decoderhex_3 (
    .I0(and_5_out), .I1(and_6_out), .I2(and_7_out), .I3(1'b0), .A(decoderhex_3_a), .B(decoderhex_3_b),
    .C(decoderhex_3_c), .D(decoderhex_3_d), .E(decoderhex_3_e), .F(decoderhex_3_f), .G(decoderhex_3_g),
    .H(decoderhex_3_h));
  and and_8 (and_8_out, multiplexer_1_out[3], or_2_out);
  _7_Segment_Display u_7_segment_display_5 (.g(and_8_out));  // open: f, a, b, e, d, c, dp
  _7_Segment_Display u_7_segment_display_6 (
    .g(decoderhex_3_g), .f(decoderhex_3_f), .a(decoderhex_3_a), .b(decoderhex_3_b), .e(decoderhex_3_e),
    .d(decoderhex_3_d), .c(decoderhex_3_c), .dp(decoderhex_3_h));

  // Notes on the sheet:
  //   B
  //   A
  //   溢出检测
  //   正数+正数
  //   负数+负数
  //   Bout
  //   Bout输出为1说明A绝对值<B绝对值
  //   Bout输出为0说明A绝对值>B绝对值
  //   LED指示溢出
  //   此时符号位取决于B，数值为B的绝对值减A的绝对值
  //   此时符号位取决于A，数值为A的绝对值减B的绝对值
  //   选择信号00为正数+正数 01为负数加负数
  //   选择信号10为有一负数且A的绝对值大于B的绝对值 11为有一负数且A的绝对值小于B的绝对值
  //   输出0时不显示负号
endmodule

module DecoderHex (
  input  I0,
  input  I1,
  input  I2,
  input  I3,
  output A,
  output B,
  output C,
  output D,
  output E,
  output F,
  output G,
  output H
);

  wire decoder_1_out0, decoder_1_out1, decoder_1_out2, decoder_1_out3, decoder_1_out4, decoder_1_out5,
       decoder_1_out6, decoder_1_out7, decoder_1_out8, decoder_1_out9, decoder_1_out10, decoder_1_out11,
       decoder_1_out12, decoder_1_out13, decoder_1_out14, decoder_1_out15;

  Decoder #(.select(4)) decoder_1 (
    .out0(decoder_1_out0), .out1(decoder_1_out1), .out2(decoder_1_out2), .out3(decoder_1_out3),
    .out4(decoder_1_out4), .out5(decoder_1_out5), .out6(decoder_1_out6), .out7(decoder_1_out7),
    .out8(decoder_1_out8), .out9(decoder_1_out9), .out10(decoder_1_out10), .out11(decoder_1_out11),
    .out12(decoder_1_out12), .out13(decoder_1_out13), .out14(decoder_1_out14), .out15(decoder_1_out15),
    .sel({I3, I2, I1, I0}), .en(1'b1));
  or or_1 (A, decoder_1_out0, decoder_1_out2, decoder_1_out3, decoder_1_out5, decoder_1_out6, decoder_1_out7, decoder_1_out8, decoder_1_out9, decoder_1_out10, decoder_1_out12, decoder_1_out14, decoder_1_out15);
  or or_2 (B, decoder_1_out0, decoder_1_out1, decoder_1_out2, decoder_1_out3, decoder_1_out4, decoder_1_out7, decoder_1_out8, decoder_1_out9, decoder_1_out10, decoder_1_out13);
  or or_3 (C, decoder_1_out0, decoder_1_out1, decoder_1_out3, decoder_1_out4, decoder_1_out5, decoder_1_out6, decoder_1_out7, decoder_1_out8, decoder_1_out9, decoder_1_out10, decoder_1_out11, decoder_1_out13);
  or or_4 (D, decoder_1_out0, decoder_1_out2, decoder_1_out3, decoder_1_out5, decoder_1_out6, decoder_1_out8, decoder_1_out9, decoder_1_out11, decoder_1_out12, decoder_1_out13, decoder_1_out14);
  or or_5 (E, decoder_1_out0, decoder_1_out2, decoder_1_out6, decoder_1_out8, decoder_1_out10, decoder_1_out11, decoder_1_out12, decoder_1_out13, decoder_1_out14, decoder_1_out15);
  or or_6 (F, decoder_1_out0, decoder_1_out4, decoder_1_out5, decoder_1_out6, decoder_1_out8, decoder_1_out9, decoder_1_out10, decoder_1_out11, decoder_1_out12, decoder_1_out14, decoder_1_out15);
  or or_7 (G, decoder_1_out2, decoder_1_out3, decoder_1_out4, decoder_1_out5, decoder_1_out6, decoder_1_out8, decoder_1_out9, decoder_1_out10, decoder_1_out11, decoder_1_out13, decoder_1_out14, decoder_1_out15);

  assign H = 1'b0;

  // Notes on the sheet:
  //   A
  //   B
  //   C
  //   D
  //   E
  //   F
  //   G
endmodule
