// Logisim project twosComplementAdder.circ as structural Verilog: 1 circuit, main circuit main
module main (
  input  A3,
  input  A2,
  input  A1,
  input  A0,
  input  B3,
  input  B2,
  input  B1,
  input  B0,
  input  in_9,
  output S0,
  output S1,
  output S2,
  output S3,
  output ovfl
);

  wire and_1_out, and_2_out;

  FA4bit fa4bit_1 (
    .Cin(in_9), .B0(B0), .A0(A0), .B1(B1), .A1(A1), .B2(B2), .A2(A2), .B3(B3), .A3(A3), .S0(S0), .S1(S1),
    .S2(S2), .S3(S3));  // open: Cout
  and and_1 (and_1_out, ~A3, ~B3, S3);  // AND_Gate
  and and_2 (and_2_out, A3, B3, ~S3);  // AND_Gate
  LED led_1 (.in(ovfl));
  or or_1 (ovfl, and_1_out, and_2_out);
endmodule
