// Logisim project DFF.circ as structural Verilog: 6 circuits, main circuit DFF
module DFF (
  input  clk,
  input  D,
  output Q
);

  wire dlatch_1_q, not_1_out;

  not not_1 (not_1_out, clk);
  Dlatch dlatch_1 (.WE(not_1_out), .D(D), .Q(dlatch_1_q));  // open: Qn
  Dlatch dlatch_2 (.WE(clk), .D(dlatch_1_q), .Q(Q));  // open: Qn
endmodule

module DFFrst (
  input  rst,
  input  clk,
  input  D,
  output Q
);

  wire dlatchrst_1_q, not_1_out;

  not not_1 (not_1_out, clk);
  DlatchRst dlatchrst_1 (.Rst(rst), .WE(not_1_out), .D(D), .Q(dlatchrst_1_q));  // open: Qn
  DlatchRst dlatchrst_2 (.Rst(rst), .WE(clk), .D(dlatchrst_1_q), .Q(Q));  // open: Qn
endmodule

module bitFlipDFF (
  input  rst,
  output Q
);

  wire clk_out, not_1_out;

  Clock clk (.out(clk_out));
  not not_1 (not_1_out, Q);
  DFFrst dffrst_1 (.rst(rst), .clk(clk_out), .D(not_1_out), .Q(Q));
endmodule

module DFF_negedge (
  input  D,
  output Q
);

  wire clk_out, dlatch_1_q, not_1_out;

  Clock clk (.out(clk_out));
  Dlatch dlatch_1 (.WE(clk_out), .D(D), .Q(dlatch_1_q));  // open: Qn
  not not_1 (not_1_out, clk_out);
  Dlatch dlatch_2 (.WE(not_1_out), .D(dlatch_1_q), .Q(Q));  // open: Qn
endmodule

module DFF_en (
  input  clk,
  input  D,
  input  en,
  output Q
);

  wire and_1_out, and_2_out, or_1_out;

  and and_1 (and_1_out, ~en, Q);  // AND_Gate
  and and_2 (and_2_out, D, en);
  or or_1 (or_1_out, and_2_out, and_1_out);
  DFF dff_1 (.clk(clk), .D(or_1_out), .Q(Q));
endmodule

module DFF_en_rst (
  input  rst,
  input  clk,
  input  D,
  input  en,
  output Q
);

  wire and_1_out, and_2_out, or_1_out;

  and and_1 (and_1_out, D, en);
  and and_2 (and_2_out, ~en, Q);  // AND_Gate
  or or_1 (or_1_out, and_1_out, and_2_out);
  DFFrst dffrst_1 (.rst(rst), .clk(clk), .D(or_1_out), .Q(Q));
endmodule
