// Logisim project Dlatch.circ as structural Verilog: 3 circuits, main circuit DlatchRst
module DlatchRst (
  input  Rst,
  input  WE,
  input  D,
  output Q,
  output Qn
);

  wire and_1_out, and_2_out, and_3_out, not_1_out, not_2_out, or_1_out;

  not not_1 (not_1_out, D);
  not not_2 (not_2_out, Rst);
  and and_1 (and_1_out, not_1_out, WE);
  and and_2 (and_2_out, WE, D);
  or or_1 (or_1_out, Rst, and_1_out);
  and and_3 (and_3_out, and_2_out, not_2_out);
  SRlatch srlatch_1 (.R(or_1_out), .S(and_3_out), .Q(Q), .Qn(Qn));
endmodule

module Dlatch (
  input  WE,
  input  D,
  output Q,
  output Qn
);

  wire and_1_out, and_2_out, not_1_out;

  not not_1 (not_1_out, D);
  and and_1 (and_1_out, not_1_out, WE);
  and and_2 (and_2_out, WE, D);
  SRlatch srlatch_1 (.R(and_1_out), .S(and_2_out), .Q(Q), .Qn(Qn));
endmodule

module bitFlipDlatch (
  input  Rst,
  input  WE,
  output Q
);

  wire not_1_out;

  not not_1 (not_1_out, Q);
  DlatchRst dlatchrst_1 (.Rst(Rst), .WE(WE), .D(not_1_out), .Q(Q));  // open: Qn
endmodule
