// Logisim project Register4bit.circ as structural Verilog: 8 circuits, main circuit register4bit
module register4bit (
  input  D0,
  input  D1,
  input  D2,
  input  D3,
  input  rst,
  input  clk,
  input  en,
  output Q0,
  output Q1,
  output Q2,
  output Q3
);

  DFF_en_rst dff_en_rst_1 (.rst(rst), .clk(clk), .D(D0), .en(en), .Q(Q0));
  DFF_en_rst dff_en_rst_2 (.rst(rst), .clk(clk), .D(D1), .en(en), .Q(Q1));
  DFF_en_rst dff_en_rst_3 (.rst(rst), .clk(clk), .D(D2), .en(en), .Q(Q2));
  DFF_en_rst dff_en_rst_4 (.rst(rst), .clk(clk), .D(D3), .en(en), .Q(Q3));
endmodule

module reg4bitDigitalHex (
  input  rst,
  input  en
);

  wire clk_out, digitaldecoderhex_1_a, digitaldecoderhex_1_b, digitaldecoderhex_1_c, digitaldecoderhex_1_d,
       digitaldecoderhex_1_e, digitaldecoderhex_1_f, digitaldecoderhex_1_g, digitaldecoderhex_1_h,
       dipswitch_1_p1, dipswitch_1_p2, dipswitch_1_p3, dipswitch_1_p4, register4bit_1_q0, register4bit_1_q1,
       register4bit_1_q2, register4bit_1_q3;

  // DipSwitch #(.number(4)) dipswitch_1: pin names not known; wires that end beside it: dipswitch_1_p1, dipswitch_1_p2, dipswitch_1_p3, dipswitch_1_p4
  Clock clk (.out(clk_out));
  register4bit register4bit_1 (
    .D0(dipswitch_1_p1), .D1(dipswitch_1_p2), .D2(dipswitch_1_p3), .D3(dipswitch_1_p4), .rst(rst), .clk(en),
    .en(clk_out), .Q0(register4bit_1_q0), .Q1(register4bit_1_q1), .Q2(register4bit_1_q2),
    .Q3(register4bit_1_q3));
  DigitalDecoderHex digitaldecoderhex_1 (
    .I0(register4bit_1_q0), .I1(register4bit_1_q1), .I2(register4bit_1_q2), .I3(register4bit_1_q3),
    .A(digitaldecoderhex_1_a), .B(digitaldecoderhex_1_b), .C(digitaldecoderhex_1_c),
    .D(digitaldecoderhex_1_d), .E(digitaldecoderhex_1_e), .F(digitaldecoderhex_1_f),
    .G(digitaldecoderhex_1_g), .H(digitaldecoderhex_1_h));
  _7_Segment_Display u_7_segment_display_1 (
    .g(digitaldecoderhex_1_g), .f(digitaldecoderhex_1_f), .a(digitaldecoderhex_1_a),
    .b(digitaldecoderhex_1_b), .e(digitaldecoderhex_1_e), .d(digitaldecoderhex_1_d),
    .c(digitaldecoderhex_1_c), .dp(digitaldecoderhex_1_h));
endmodule

module DigitalDecoderHex (
  input  I0,
  input  I1,
  input  I2,
  input  I3,
  output A,
  output B,
  output C,
  output D,
  output E,
  output F,
  output G,
  output H
);

  wire decoder_1_out0, decoder_1_out1, decoder_1_out2, decoder_1_out3, decoder_1_out4, decoder_1_out5,
       decoder_1_out6, decoder_1_out7, decoder_1_out8, decoder_1_out9, decoder_1_out10, decoder_1_out11,
       decoder_1_out12, decoder_1_out13, decoder_1_out14, decoder_1_out15;

  Decoder #(.select(4)) decoder_1 (
    .out0(decoder_1_out0), .out1(decoder_1_out1), .out2(decoder_1_out2), .out3(decoder_1_out3),
    .out4(decoder_1_out4), .out5(decoder_1_out5), .out6(decoder_1_out6), .out7(decoder_1_out7),
    .out8(decoder_1_out8), .out9(decoder_1_out9), .out10(decoder_1_out10), .out11(decoder_1_out11),
    .out12(decoder_1_out12), .out13(decoder_1_out13), .out14(decoder_1_out14), .out15(decoder_1_out15),
    .sel({I3, I2, I1, I0}), .en(1'b1));
  or or_1 (A, decoder_1_out0, decoder_1_out2, decoder_1_out3, decoder_1_out5, decoder_1_out6, decoder_1_out7, decoder_1_out8, decoder_1_out9, decoder_1_out10, decoder_1_out12, decoder_1_out14, decoder_1_out15);
  or or_2 (B, decoder_1_out0, decoder_1_out1, decoder_1_out2, decoder_1_out3, decoder_1_out4, decoder_1_out7, decoder_1_out8, decoder_1_out9, decoder_1_out10, decoder_1_out13);
  or or_3 (C, decoder_1_out0, decoder_1_out1, decoder_1_out3, decoder_1_out4, decoder_1_out5, decoder_1_out6, decoder_1_out7, decoder_1_out8, decoder_1_out9, decoder_1_out10, decoder_1_out11, decoder_1_out13);
  or or_4 (D, decoder_1_out0, decoder_1_out2, decoder_1_out3, decoder_1_out5, decoder_1_out6, decoder_1_out8, decoder_1_out9, decoder_1_out11, decoder_1_out12, decoder_1_out13, decoder_1_out14);
  or or_5 (E, decoder_1_out0, decoder_1_out2, decoder_1_out6, decoder_1_out8, decoder_1_out10, decoder_1_out11, decoder_1_out12, decoder_1_out13, decoder_1_out14, decoder_1_out15);
  or or_6 (F, decoder_1_out0, decoder_1_out4, decoder_1_out5, decoder_1_out6, decoder_1_out8, decoder_1_out9, decoder_1_out10, decoder_1_out11, decoder_1_out12, decoder_1_out14, decoder_1_out15);
  or or_7 (G, decoder_1_out2, decoder_1_out3, decoder_1_out4, decoder_1_out5, decoder_1_out6, decoder_1_out8, decoder_1_out9, decoder_1_out10, decoder_1_out11, decoder_1_out13, decoder_1_out14, decoder_1_out15);

  assign H = 1'b0;

  // Notes on the sheet:
  //   A
  //   B
  //   C
  //   D
  //   E
  //   F
  //   G
endmodule

module counter4bit (
  input  rst,
  input  en
);

  wire clk_out, digitaldecoderhex_1_a, digitaldecoderhex_1_b, digitaldecoderhex_1_c, digitaldecoderhex_1_d,
       digitaldecoderhex_1_e, digitaldecoderhex_1_f, digitaldecoderhex_1_g, digitaldecoderhex_1_h,
       fa4bit_1_s0, fa4bit_1_s1, fa4bit_1_s2, fa4bit_1_s3, register4bit_1_q0, register4bit_1_q1,
       register4bit_1_q2, register4bit_1_q3;

  Clock clk (.out(clk_out));
  register4bit register4bit_1 (
    .D0(fa4bit_1_s0), .D1(fa4bit_1_s1), .D2(fa4bit_1_s2), .D3(fa4bit_1_s3), .rst(rst), .clk(en),
    .en(clk_out), .Q0(register4bit_1_q0), .Q1(register4bit_1_q1), .Q2(register4bit_1_q2),
    .Q3(register4bit_1_q3));
  FA4bit fa4bit_1 (
    .B0(1'b1), .A0(register4bit_1_q0), .B1(1'b0), .A1(register4bit_1_q1), .B2(1'b0), .A2(register4bit_1_q2),
    .B3(1'b0), .A3(register4bit_1_q3), .S0(fa4bit_1_s0), .S1(fa4bit_1_s1), .S2(fa4bit_1_s2), .S3(fa4bit_1_s3));  // open: Cin, Cout
  DigitalDecoderHex digitaldecoderhex_1 (
    .I0(fa4bit_1_s0), .I1(fa4bit_1_s1), .I2(fa4bit_1_s2), .I3(fa4bit_1_s3), .A(digitaldecoderhex_1_a),
    .B(digitaldecoderhex_1_b), .C(digitaldecoderhex_1_c), .D(digitaldecoderhex_1_d),
    .E(digitaldecoderhex_1_e), .F(digitaldecoderhex_1_f), .G(digitaldecoderhex_1_g), .H(digitaldecoderhex_1_h));
  _7_Segment_Display u_7_segment_display_1 (
    .g(digitaldecoderhex_1_g), .f(digitaldecoderhex_1_f), .a(digitaldecoderhex_1_a),
    .b(digitaldecoderhex_1_b), .e(digitaldecoderhex_1_e), .d(digitaldecoderhex_1_d),
    .c(digitaldecoderhex_1_c), .dp(digitaldecoderhex_1_h));
endmodule

module FA4bit (
  input  Cin,
  input  B0,
  input  A0,
  input  B1,
  input  A1,
  input  B2,
  input  A2,
  input  B3,
  input  A3,
  output S0,
  output S1,
  output S2,
  output S3,
  output Cout
);

  wire fa_1_cout, fa_2_cout, fa_3_cout;

  FA fa_1 (.A(A0), .B(B0), .Cin(Cin), .Sum(S0), .Cout(fa_1_cout));
  FA fa_2 (.A(A1), .B(B1), .Cin(fa_1_cout), .Sum(S1), .Cout(fa_2_cout));
  FA fa_3 (.A(A2), .B(B2), .Cin(fa_2_cout), .Sum(S2), .Cout(fa_3_cout));
  FA fa_4 (.A(A3), .B(B3), .Cin(fa_3_cout), .Sum(S3), .Cout(Cout));
endmodule

module FA8bit (
  input  Cin,
  input  B0,
  input  A0,
  input  B1,
  input  A1,
  input  B2,
  input  A2,
  input  B3,
  input  A3,
  input  B4,
  input  A4,
  input  B5,
  input  A5,
  input  B6,
  input  A6,
  input  B7,
  input  A7,
  output S0,
  output S1,
  output S2,
  output S3,
  output S4,
  output S5,
  output S6,
  output S7,
  output Cout
);

  wire fa_1_cout, fa_2_cout, fa_3_cout, fa_4_cout, fa_5_cout, fa_6_cout, fa_7_cout;

  FA fa_1 (.A(A0), .B(B0), .Cin(Cin), .Sum(S0), .Cout(fa_1_cout));
  FA fa_2 (.A(A1), .B(B1), .Cin(fa_1_cout), .Sum(S1), .Cout(fa_2_cout));
  FA fa_3 (.A(A2), .B(B2), .Cin(fa_2_cout), .Sum(S2), .Cout(fa_3_cout));
  FA fa_4 (.A(A3), .B(B3), .Cin(fa_3_cout), .Sum(S3), .Cout(fa_4_cout));
  FA fa_5 (.A(A4), .B(B4), .Cin(fa_4_cout), .Sum(S4), .Cout(fa_5_cout));
  FA fa_6 (.A(A5), .B(B5), .Cin(fa_5_cout), .Sum(S5), .Cout(fa_6_cout));
  FA fa_7 (.A(A6), .B(B6), .Cin(fa_6_cout), .Sum(S6), .Cout(fa_7_cout));
  FA fa_8 (.A(A7), .B(B7), .Cin(fa_7_cout), .Sum(S7), .Cout(Cout));
endmodule

module register8bit (
  input  D0,
  input  D1,
  input  D2,
  input  D3,
  input  D4,
  input  D5,
  input  D6,
  input  D7,
  input  rst,
  input  en,
  input  clk,
  output Q0,
  output Q1,
  output Q2,
  output Q3,
  output Q4,
  output Q5,
  output Q6,
  output Q7
);

  wire and_1_out, and_2_out, and_3_out, and_4_out, and_5_out, and_6_out, and_7_out, and_8_out, or_1_out;

  or or_1 (or_1_out, rst, en);
  and and_1 (and_1_out, ~rst, D0);  // AND_Gate
  DFF_en dff_en_1 (.clk(clk), .D(and_1_out), .en(or_1_out), .Q(Q0));
  and and_2 (and_2_out, ~rst, D1);  // AND_Gate
  DFF_en dff_en_2 (.clk(clk), .D(and_2_out), .en(or_1_out), .Q(Q1));
  and and_3 (and_3_out, ~rst, D2);  // AND_Gate
  DFF_en dff_en_3 (.clk(clk), .D(and_3_out), .en(or_1_out), .Q(Q2));
  and and_4 (and_4_out, ~rst, D3);  // AND_Gate
  DFF_en dff_en_4 (.clk(clk), .D(and_4_out), .en(or_1_out), .Q(Q3));
  and and_5 (and_5_out, ~rst, D4);  // AND_Gate
  DFF_en dff_en_5 (.clk(clk), .D(and_5_out), .en(or_1_out), .Q(Q4));
  and and_6 (and_6_out, ~rst, D5);  // AND_Gate
  DFF_en dff_en_6 (.clk(clk), .D(and_6_out), .en(or_1_out), .Q(Q5));
  and and_7 (and_7_out, ~rst, D6);  // AND_Gate
  DFF_en dff_en_7 (.clk(clk), .D(and_7_out), .en(or_1_out), .Q(Q6));
  and and_8 (and_8_out, ~rst, D7);  // AND_Gate
  DFF_en dff_en_8 (.clk(clk), .D(and_8_out), .en(or_1_out), .Q(Q7));
endmodule

module counter1to10 (
  input  rst,
  output [7:0] Dout
);

  wire clk_out, fa8bit_1_s0, fa8bit_1_s1, fa8bit_1_s2, fa8bit_1_s3, fa8bit_1_s4, fa8bit_1_s5, fa8bit_1_s6,
       fa8bit_1_s7, fa8bit_2_s0, fa8bit_2_s1, fa8bit_2_s2, fa8bit_2_s3, fa8bit_2_s4, fa8bit_2_s5,
       fa8bit_2_s6, fa8bit_2_s7, nand_1_out, register8bit_1_q0, register8bit_1_q1, register8bit_1_q2,
       register8bit_1_q3, register8bit_1_q4, register8bit_1_q5, register8bit_1_q6, register8bit_1_q7;

  Clock clk (.out(clk_out));
  nand nand_1 (nand_1_out, register8bit_1_q3, register8bit_1_q1);
  register8bit register8bit_1 (
    .D0(fa8bit_1_s0), .D1(fa8bit_1_s1), .D2(fa8bit_1_s2), .D3(fa8bit_1_s3), .D4(fa8bit_1_s4),
    .D5(fa8bit_1_s5), .D6(fa8bit_1_s6), .D7(fa8bit_1_s7), .rst(rst), .en(nand_1_out), .clk(clk_out),
    .Q0(register8bit_1_q0), .Q1(register8bit_1_q1), .Q2(register8bit_1_q2), .Q3(register8bit_1_q3),
    .Q4(register8bit_1_q4), .Q5(register8bit_1_q5), .Q6(register8bit_1_q6), .Q7(register8bit_1_q7));
  FA8bit fa8bit_1 (
    .Cin(1'b0), .B0(1'b1), .A0(register8bit_1_q0), .B1(1'b0), .A1(register8bit_1_q1), .B2(1'b0),
    .A2(register8bit_1_q2), .B3(1'b0), .A3(register8bit_1_q3), .B4(1'b0), .A4(register8bit_1_q4), .B5(1'b0),
    .A5(register8bit_1_q5), .B6(1'b0), .A6(register8bit_1_q6), .B7(1'b0), .A7(register8bit_1_q7),
    .S0(fa8bit_1_s0), .S1(fa8bit_1_s1), .S2(fa8bit_1_s2), .S3(fa8bit_1_s3), .S4(fa8bit_1_s4),
    .S5(fa8bit_1_s5), .S6(fa8bit_1_s6), .S7(fa8bit_1_s7));  // open: Cout
  FA8bit fa8bit_2 (
    .B0(fa8bit_1_s0), .A0(Dout[0]), .B1(fa8bit_1_s1), .A1(Dout[1]), .B2(fa8bit_1_s2), .A2(Dout[2]),
    .B3(fa8bit_1_s3), .A3(Dout[3]), .B4(fa8bit_1_s4), .A4(Dout[4]), .B5(fa8bit_1_s5), .A5(Dout[5]),
    .B6(fa8bit_1_s6), .A6(Dout[6]), .B7(fa8bit_1_s7), .A7(Dout[7]), .S0(fa8bit_2_s0), .S1(fa8bit_2_s1),
    .S2(fa8bit_2_s2), .S3(fa8bit_2_s3), .S4(fa8bit_2_s4), .S5(fa8bit_2_s5), .S6(fa8bit_2_s6), .S7(fa8bit_2_s7));  // open: Cin, Cout
  register8bit register8bit_2 (
    .D0(fa8bit_2_s0), .D1(fa8bit_2_s1), .D2(fa8bit_2_s2), .D3(fa8bit_2_s3), .D4(fa8bit_2_s4),
    .D5(fa8bit_2_s5), .D6(fa8bit_2_s6), .D7(fa8bit_2_s7), .rst(rst), .en(nand_1_out), .clk(clk_out),
    .Q0(Dout[0]), .Q1(Dout[1]), .Q2(Dout[2]), .Q3(Dout[3]), .Q4(Dout[4]), .Q5(Dout[5]), .Q6(Dout[6]),
    .Q7(Dout[7]));

  // Notes on the sheet:
  //   当前要加的数
  //   加1电路
  //   累加计算电路
  //   当前累加结果
endmodule
