// Logisim project SRlatch.circ as structural Verilog: 1 circuit, main circuit SRlatch
module SRlatch (
  input  R,
  input  S,
  output Q,
  output Qn
);

  nor nor_1 (Q, R, Qn);
  nor nor_2 (Qn, Q, S);
endmodule
