// Logisim project SnRnlatch.circ as structural Verilog: 1 circuit, main circuit main
module main (
  input  R,
  input  S,
  output Q,
  output Qn
);

  wire and_1_out, and_2_out, dipswitch_1_p1;

  // DipSwitch #(.number(1)) dipswitch_1: pin names not known; wires that end beside it: dipswitch_1_p1
  and and_1 (and_1_out, R, dipswitch_1_p1);
  and and_2 (and_2_out, dipswitch_1_p1, S);
  nand nand_1 (Q, and_1_out, Qn);
  nand nand_2 (Qn, Q, and_2_out);
endmodule
