// Logisim project myClock.circ as structural Verilog: 4 circuits, main circuit main
module main (
  input  rst,
  input  en
);

  wire and_1_out, and_2_out, clk_out, decimalcounter0_5_1_carry, decimalcounter0_5_1_q0,
       decimalcounter0_5_1_q1, decimalcounter0_5_1_q2, decimalcounter0_5_1_q3, decimalcounter0_5_2_q0,
       decimalcounter0_5_2_q1, decimalcounter0_5_2_q2, decimalcounter0_5_2_q3, decimalcounter_1_carry,
       decimalcounter_1_q0, decimalcounter_1_q1, decimalcounter_1_q2, decimalcounter_1_q3,
       decimalcounter_2_carry, decimalcounter_2_q0, decimalcounter_2_q1, decimalcounter_2_q2,
       decimalcounter_2_q3, digitaldecoderhex_1_a, digitaldecoderhex_1_b, digitaldecoderhex_1_c,
       digitaldecoderhex_1_d, digitaldecoderhex_1_e, digitaldecoderhex_1_f, digitaldecoderhex_1_g,
       digitaldecoderhex_1_h, digitaldecoderhex_2_a, digitaldecoderhex_2_b, digitaldecoderhex_2_c,
       digitaldecoderhex_2_d, digitaldecoderhex_2_e, digitaldecoderhex_2_f, digitaldecoderhex_2_g,
       digitaldecoderhex_2_h, digitaldecoderhex_3_a, digitaldecoderhex_3_b, digitaldecoderhex_3_c,
       digitaldecoderhex_3_d, digitaldecoderhex_3_e, digitaldecoderhex_3_f, digitaldecoderhex_3_g,
       digitaldecoderhex_3_h, digitaldecoderhex_4_a, digitaldecoderhex_4_b, digitaldecoderhex_4_c,
       digitaldecoderhex_4_d, digitaldecoderhex_4_e, digitaldecoderhex_4_f, digitaldecoderhex_4_g,
       digitaldecoderhex_4_h;

  Clock clk (.out(clk_out));
  and and_1 (and_1_out, decimalcounter0_5_1_carry, decimalcounter_1_carry, decimalcounter_2_carry);
  decimalCounter decimalcounter_1 (
    .rst(rst), .clk(clk_out), .en(en), .Q0(decimalcounter_1_q0), .Q1(decimalcounter_1_q1),
    .Q2(decimalcounter_1_q2), .Q3(decimalcounter_1_q3), .carry(decimalcounter_1_carry));
  decimalCounter0_5 decimalcounter0_5_1 (
    .rst(rst), .clk(clk_out), .en(decimalcounter_1_carry), .Q0(decimalcounter0_5_1_q0),
    .Q1(decimalcounter0_5_1_q1), .Q2(decimalcounter0_5_1_q2), .Q3(decimalcounter0_5_1_q3),
    .carry(decimalcounter0_5_1_carry));
  and and_2 (and_2_out, decimalcounter0_5_1_carry, decimalcounter_1_carry);
  decimalCounter decimalcounter_2 (
    .rst(rst), .clk(clk_out), .en(and_2_out), .Q0(decimalcounter_2_q0), .Q1(decimalcounter_2_q1),
    .Q2(decimalcounter_2_q2), .Q3(decimalcounter_2_q3), .carry(decimalcounter_2_carry));
  decimalCounter0_5 decimalcounter0_5_2 (
    .rst(rst), .clk(clk_out), .en(and_1_out), .Q0(decimalcounter0_5_2_q0), .Q1(decimalcounter0_5_2_q1),
    .Q2(decimalcounter0_5_2_q2), .Q3(decimalcounter0_5_2_q3));  // open: carry
  DigitalDecoderHex digitaldecoderhex_1 (
    .I0(decimalcounter_1_q0), .I1(decimalcounter_1_q1), .I2(decimalcounter_1_q2), .I3(decimalcounter_1_q3),
    .A(digitaldecoderhex_1_a), .B(digitaldecoderhex_1_b), .C(digitaldecoderhex_1_c),
    .D(digitaldecoderhex_1_d), .E(digitaldecoderhex_1_e), .F(digitaldecoderhex_1_f),
    .G(digitaldecoderhex_1_g), .H(digitaldecoderhex_1_h));
  _7_Segment_Display u_7_segment_display_1 (
    .g(digitaldecoderhex_1_g), .f(digitaldecoderhex_1_f), .a(digitaldecoderhex_1_a),
    .b(digitaldecoderhex_1_b), .e(digitaldecoderhex_1_e), .d(digitaldecoderhex_1_d),
    .c(digitaldecoderhex_1_c), .dp(digitaldecoderhex_1_h));
  DigitalDecoderHex digitaldecoderhex_2 (
    .I0(decimalcounter0_5_1_q0), .I1(decimalcounter0_5_1_q1), .I2(decimalcounter0_5_1_q2),
    .I3(decimalcounter0_5_1_q3), .A(digitaldecoderhex_2_a), .B(digitaldecoderhex_2_b),
    .C(digitaldecoderhex_2_c), .D(digitaldecoderhex_2_d), .E(digitaldecoderhex_2_e),
    .F(digitaldecoderhex_2_f), .G(digitaldecoderhex_2_g), .H(digitaldecoderhex_2_h));
  _7_Segment_Display u_7_segment_display_2 (
    .g(digitaldecoderhex_2_g), .f(digitaldecoderhex_2_f), .a(digitaldecoderhex_2_a),
    .b(digitaldecoderhex_2_b), .e(digitaldecoderhex_2_e), .d(digitaldecoderhex_2_d),
    .c(digitaldecoderhex_2_c), .dp(digitaldecoderhex_2_h));
  DigitalDecoderHex digitaldecoderhex_3 (
    .I0(decimalcounter_2_q0), .I1(decimalcounter_2_q1), .I2(decimalcounter_2_q2), .I3(decimalcounter_2_q3),
    .A(digitaldecoderhex_3_a), .B(digitaldecoderhex_3_b), .C(digitaldecoderhex_3_c),
    .D(digitaldecoderhex_3_d), .E(digitaldecoderhex_3_e), .F(digitaldecoderhex_3_f),
    .G(digitaldecoderhex_3_g), .H(digitaldecoderhex_3_h));
  _7_Segment_Display u_7_segment_display_3 (
    .g(digitaldecoderhex_3_g), .f(digitaldecoderhex_3_f), .a(digitaldecoderhex_3_a),
    .b(digitaldecoderhex_3_b), .e(digitaldecoderhex_3_e), .d(digitaldecoderhex_3_d),
    .c(digitaldecoderhex_3_c), .dp(digitaldecoderhex_3_h));
  DigitalDecoderHex digitaldecoderhex_4 (
    .I0(decimalcounter0_5_2_q0), .I1(decimalcounter0_5_2_q1), .I2(decimalcounter0_5_2_q2),
    .I3(decimalcounter0_5_2_q3), .A(digitaldecoderhex_4_a), .B(digitaldecoderhex_4_b),
    .C(digitaldecoderhex_4_c), .D(digitaldecoderhex_4_d), .E(digitaldecoderhex_4_e),
    .F(digitaldecoderhex_4_f), .G(digitaldecoderhex_4_g), .H(digitaldecoderhex_4_h));
  _7_Segment_Display u_7_segment_display_4 (
    .g(digitaldecoderhex_4_g), .f(digitaldecoderhex_4_f), .a(digitaldecoderhex_4_a),
    .b(digitaldecoderhex_4_b), .e(digitaldecoderhex_4_e), .d(digitaldecoderhex_4_d),
    .c(digitaldecoderhex_4_c), .dp(digitaldecoderhex_4_h));

  // Notes on the sheet:
  //   秒个位
  //   秒十位
  //   分个位
  //   分十位
endmodule

module decimalCounter (
  input  rst,
  input  clk,
  input  en,
  output Q0,
  output Q1,
  output Q2,
  output Q3,
  output carry
);

  wire not_1_out;
  wire [3:0] fa4bit_1_s0, multiplexer_1_out;

  register4bit register4bit_1 (
    .D0(multiplexer_1_out[0]), .D1(multiplexer_1_out[1]), .D2(multiplexer_1_out[2]),
    .D3(multiplexer_1_out[3]), .rst(rst), .clk(clk), .en(en), .Q0(Q0), .Q1(Q1), .Q2(Q2), .Q3(Q3));
  not not_1 (not_1_out, carry);
  Multiplexer #(.width(4)) multiplexer_1 (.in0(4'b0000), .in1(fa4bit_1_s0), .out(multiplexer_1_out), .sel(not_1_out));
  and and_1 (carry, Q0, Q3);
  FA4bit fa4bit_1 (
    .Cin(1'b0), .B0(1'b1), .A0(Q0), .B1(1'b0), .A1(Q1), .B2(1'b0), .A2(Q2), .B3(1'b0), .A3(Q3),
    .S0(fa4bit_1_s0[0]), .S1(fa4bit_1_s0[1]), .S2(fa4bit_1_s0[2]), .S3(fa4bit_1_s0[3]));  // open: Cout
endmodule

module decimalCounter0_5 (
  input  rst,
  input  clk,
  input  en,
  output Q0,
  output Q1,
  output Q2,
  output Q3,
  output carry
);

  wire not_1_out;
  wire [3:0] fa4bit_1_s0, multiplexer_1_out;

  register4bit register4bit_1 (
    .D0(multiplexer_1_out[0]), .D1(multiplexer_1_out[1]), .D2(multiplexer_1_out[2]),
    .D3(multiplexer_1_out[3]), .rst(rst), .clk(clk), .en(en), .Q0(Q0), .Q1(Q1), .Q2(Q2), .Q3(Q3));
  not not_1 (not_1_out, carry);
  Multiplexer #(.width(4)) multiplexer_1 (.in0(4'b0000), .in1(fa4bit_1_s0), .out(multiplexer_1_out), .sel(not_1_out));
  and and_1 (carry, Q0, Q2);
  FA4bit fa4bit_1 (
    .Cin(1'b0), .B0(1'b1), .A0(Q0), .B1(1'b0), .A1(Q1), .B2(1'b0), .A2(Q2), .B3(1'b0), .A3(Q3),
    .S0(fa4bit_1_s0[0]), .S1(fa4bit_1_s0[1]), .S2(fa4bit_1_s0[2]), .S3(fa4bit_1_s0[3]));  // open: Cout
endmodule

module hexCounter (
  input  rst,
  input  clk,
  input  en,
  output Q0,
  output Q1,
  output Q2,
  output Q3,
  output carry
);

  wire not_1_out;
  wire [3:0] fa4bit_1_s0, multiplexer_1_out;

  register4bit register4bit_1 (
    .D0(multiplexer_1_out[0]), .D1(multiplexer_1_out[1]), .D2(multiplexer_1_out[2]),
    .D3(multiplexer_1_out[3]), .rst(rst), .clk(clk), .en(en), .Q0(Q0), .Q1(Q1), .Q2(Q2), .Q3(Q3));
  not not_1 (not_1_out, carry);
  Multiplexer #(.width(4)) multiplexer_1 (.in0(4'b0000), .in1(fa4bit_1_s0), .out(multiplexer_1_out), .sel(not_1_out));
  and and_1 (carry, Q0, Q1, Q2, Q3);
  FA4bit fa4bit_1 (
    .Cin(1'b0), .B0(1'b1), .A0(Q0), .B1(1'b0), .A1(Q1), .B2(1'b0), .A2(Q2), .B3(1'b0), .A3(Q3),
    .S0(fa4bit_1_s0[0]), .S1(fa4bit_1_s0[1]), .S2(fa4bit_1_s0[2]), .S3(fa4bit_1_s0[3]));  // open: Cout
endmodule
