// Logisim project 4bitComparator.circ as structural Verilog: 1 circuit, main circuit main
module main (
);

  wire and_1_out, dipswitch_1_p1, dipswitch_1_p2, dipswitch_1_p3, dipswitch_1_p4, dipswitch_1_p5,
       dipswitch_1_p6, dipswitch_2_p1, dipswitch_2_p2, xnor_1_out, xnor_2_out, xnor_3_out, xnor_4_out;

  // DipSwitch #(.number(4)) dipswitch_1: pin names not known; wires that end beside it: dipswitch_1_p1, dipswitch_1_p2, dipswitch_1_p3, dipswitch_1_p4, dipswitch_1_p5, dipswitch_1_p6
  // DipSwitch #(.number(4)) dipswitch_2: pin names not known; wires that end beside it: dipswitch_2_p1, dipswitch_2_p2
  xnor xnor_1 (xnor_1_out, dipswitch_1_p4, dipswitch_2_p2);
  xnor xnor_2 (xnor_2_out, dipswitch_1_p3, dipswitch_2_p1);
  xnor xnor_3 (xnor_3_out, dipswitch_1_p2, dipswitch_1_p6);
  xnor xnor_4 (xnor_4_out, dipswitch_1_p1, dipswitch_1_p5);
  and and_1 (and_1_out, xnor_1_out, xnor_2_out, xnor_3_out, xnor_4_out);
  LED led_1 (.in(and_1_out));
endmodule
