// Logisim project Encoder_16_4.circ as structural Verilog: 2 circuits, main circuit main
module main (
);

  wire digitalseghex_1_a, digitalseghex_1_b, digitalseghex_1_c, digitalseghex_1_d, digitalseghex_1_e,
       digitalseghex_1_f, digitalseghex_1_g, digitalseghex_1_h, dipswitch_1_p1, dipswitch_1_p2,
       dipswitch_1_p3, dipswitch_1_p4, dipswitch_1_p5, dipswitch_1_p6, dipswitch_1_p7, dipswitch_1_p8,
       dipswitch_1_p9, dipswitch_1_p10, dipswitch_1_p11, dipswitch_1_p12, dipswitch_1_p13, dipswitch_1_p14,
       dipswitch_1_p15, dipswitch_1_p16, or_1_out, or_2_out, or_3_out, or_4_out;

  // DipSwitch #(.number(16)) dipswitch_1: pin names not known; wires that end beside it: dipswitch_1_p1, dipswitch_1_p2, dipswitch_1_p3, dipswitch_1_p4, dipswitch_1_p5, dipswitch_1_p6, dipswitch_1_p7, dipswitch_1_p8, dipswitch_1_p9, dipswitch_1_p10, dipswitch_1_p11, dipswitch_1_p12, dipswitch_1_p13, dipswitch_1_p14, dipswitch_1_p15, dipswitch_1_p16
  or or_1 (or_1_out, dipswitch_1_p2, dipswitch_1_p4, dipswitch_1_p6, dipswitch_1_p8, dipswitch_1_p10, dipswitch_1_p12, dipswitch_1_p14, dipswitch_1_p16);
  or or_2 (or_2_out, dipswitch_1_p3, dipswitch_1_p4, dipswitch_1_p7, dipswitch_1_p8, dipswitch_1_p11, dipswitch_1_p12, dipswitch_1_p15, dipswitch_1_p16);
  or or_3 (or_3_out, dipswitch_1_p5, dipswitch_1_p6, dipswitch_1_p7, dipswitch_1_p8, dipswitch_1_p13, dipswitch_1_p14, dipswitch_1_p15, dipswitch_1_p16);
  or or_4 (or_4_out, dipswitch_1_p9, dipswitch_1_p10, dipswitch_1_p11, dipswitch_1_p12, dipswitch_1_p13, dipswitch_1_p14, dipswitch_1_p15, dipswitch_1_p16);
  DigitalSegHex digitalseghex_1 (
    .I0(or_1_out), .I1(or_2_out), .I2(or_3_out), .I3(or_4_out), .A(digitalseghex_1_a), .B(digitalseghex_1_b),
    .C(digitalseghex_1_c), .D(digitalseghex_1_d), .E(digitalseghex_1_e), .F(digitalseghex_1_f),
    .G(digitalseghex_1_g), .H(digitalseghex_1_h));
  _7_Segment_Display u_7_segment_display_1 (
    .g(digitalseghex_1_g), .f(digitalseghex_1_f), .a(digitalseghex_1_a), .b(digitalseghex_1_b),
    .e(digitalseghex_1_e), .d(digitalseghex_1_d), .c(digitalseghex_1_c), .dp(digitalseghex_1_h));
endmodule

module DigitalSegHex (
  input  I0,
  input  I1,
  input  I2,
  input  I3,
  output A,
  output B,
  output C,
  output D,
  output E,
  output F,
  output G,
  output H
);

  wire decoder_1_out0, decoder_1_out1, decoder_1_out2, decoder_1_out3, decoder_1_out4, decoder_1_out5,
       decoder_1_out6, decoder_1_out7, decoder_1_out8, decoder_1_out9, decoder_1_out10, decoder_1_out11,
       decoder_1_out12, decoder_1_out13, decoder_1_out14, decoder_1_out15;

  Decoder #(.select(4)) decoder_1 (
    .out0(decoder_1_out0), .out1(decoder_1_out1), .out2(decoder_1_out2), .out3(decoder_1_out3),
    .out4(decoder_1_out4), .out5(decoder_1_out5), .out6(decoder_1_out6), .out7(decoder_1_out7),
    .out8(decoder_1_out8), .out9(decoder_1_out9), .out10(decoder_1_out10), .out11(decoder_1_out11),
    .out12(decoder_1_out12), .out13(decoder_1_out13), .out14(decoder_1_out14), .out15(decoder_1_out15),
    .sel({I3, I2, I1, I0}), .en(1'b1));
  or or_1 (A, decoder_1_out0, decoder_1_out2, decoder_1_out3, decoder_1_out5, decoder_1_out6, decoder_1_out7, decoder_1_out8, decoder_1_out9, decoder_1_out10, decoder_1_out12, decoder_1_out14, decoder_1_out15);
  or or_2 (B, decoder_1_out0, decoder_1_out1, decoder_1_out2, decoder_1_out3, decoder_1_out4, decoder_1_out7, decoder_1_out8, decoder_1_out9, decoder_1_out10, decoder_1_out13);
  or or_3 (C, decoder_1_out0, decoder_1_out1, decoder_1_out3, decoder_1_out4, decoder_1_out5, decoder_1_out6, decoder_1_out7, decoder_1_out8, decoder_1_out9, decoder_1_out10, decoder_1_out11, decoder_1_out13);
  or or_4 (D, decoder_1_out0, decoder_1_out2, decoder_1_out3, decoder_1_out5, decoder_1_out6, decoder_1_out8, decoder_1_out9, decoder_1_out11, decoder_1_out12, decoder_1_out13, decoder_1_out14);
  or or_5 (E, decoder_1_out0, decoder_1_out2, decoder_1_out6, decoder_1_out8, decoder_1_out10, decoder_1_out11, decoder_1_out12, decoder_1_out13, decoder_1_out14, decoder_1_out15);
  or or_6 (F, decoder_1_out0, decoder_1_out4, decoder_1_out5, decoder_1_out6, decoder_1_out8, decoder_1_out9, decoder_1_out10, decoder_1_out11, decoder_1_out12, decoder_1_out14, decoder_1_out15);
  or or_7 (G, decoder_1_out2, decoder_1_out3, decoder_1_out4, decoder_1_out5, decoder_1_out6, decoder_1_out8, decoder_1_out9, decoder_1_out10, decoder_1_out11, decoder_1_out13, decoder_1_out14, decoder_1_out15);

  assign H = 1'b0;
endmodule
