// Logisim project Encoder_16_4_Priority.circ as structural Verilog: 4 circuits, main circuit DigitalSegEncoder_16_4_Priority
module DigitalSegEncoder_16_4_Priority (
);

  wire digitalhex_decoder_1_a, digitalhex_decoder_1_b, digitalhex_decoder_1_c, digitalhex_decoder_1_d,
       digitalhex_decoder_1_e, digitalhex_decoder_1_f, digitalhex_decoder_1_g, dipswitch_1_p1,
       dipswitch_1_p2, dipswitch_1_p3, dipswitch_1_p4, dipswitch_1_p5, dipswitch_1_p6, dipswitch_1_p7,
       dipswitch_1_p8, dipswitch_1_p9, dipswitch_1_p10, dipswitch_1_p11, dipswitch_1_p12, dipswitch_1_p13,
       dipswitch_1_p14, dipswitch_1_p15, dipswitch_1_p16, encoder_16_4_priority_1_y0,
       encoder_16_4_priority_1_y1, encoder_16_4_priority_1_y2, encoder_16_4_priority_1_y3;

  // DipSwitch #(.number(16)) dipswitch_1: pin names not known; wires that end beside it: dipswitch_1_p1, dipswitch_1_p2, dipswitch_1_p3, dipswitch_1_p4, dipswitch_1_p5, dipswitch_1_p6, dipswitch_1_p7, dipswitch_1_p8, dipswitch_1_p9, dipswitch_1_p10, dipswitch_1_p11, dipswitch_1_p12, dipswitch_1_p13, dipswitch_1_p14, dipswitch_1_p15, dipswitch_1_p16, dipswitch_1_p12
  Encoder_16_4_Priority encoder_16_4_priority_1 (
    .A15(dipswitch_1_p16), .A14(dipswitch_1_p15), .A13(dipswitch_1_p14), .A12(dipswitch_1_p13),
    .A11(dipswitch_1_p12), .A10(dipswitch_1_p11), .A9(dipswitch_1_p10), .A8(dipswitch_1_p9),
    .A7(dipswitch_1_p8), .A6(dipswitch_1_p7), .A5(dipswitch_1_p6), .A4(dipswitch_1_p5), .A3(dipswitch_1_p4),
    .A2(dipswitch_1_p3), .A1(dipswitch_1_p2), .A0(dipswitch_1_p1), .Y0(encoder_16_4_priority_1_y0),
    .Y1(encoder_16_4_priority_1_y1), .Y2(encoder_16_4_priority_1_y2), .Y3(encoder_16_4_priority_1_y3));
  DigitalHex_Decoder digitalhex_decoder_1 (
    .A0(encoder_16_4_priority_1_y0), .A1(encoder_16_4_priority_1_y1), .A2(encoder_16_4_priority_1_y2),
    .A3(encoder_16_4_priority_1_y3), .A(digitalhex_decoder_1_a), .B(digitalhex_decoder_1_b),
    .C(digitalhex_decoder_1_c), .D(digitalhex_decoder_1_d), .E(digitalhex_decoder_1_e),
    .F(digitalhex_decoder_1_f), .G(digitalhex_decoder_1_g));
  _7_Segment_Display u_7_segment_display_1 (
    .g(digitalhex_decoder_1_g), .f(digitalhex_decoder_1_f), .a(digitalhex_decoder_1_a),
    .b(digitalhex_decoder_1_b), .e(digitalhex_decoder_1_e), .d(digitalhex_decoder_1_d),
    .c(digitalhex_decoder_1_c), .dp(1'b0));
endmodule

module Encoder_16_4_Priority (
  input  A15,
  input  A14,
  input  A13,
  input  A12,
  input  A11,
  input  A10,
  input  A9,
  input  A8,
  input  A7,
  input  A6,
  input  A5,
  input  A4,
  input  A3,
  input  A2,
  input  A1,
  input  A0,
  output Y0,
  output Y1,
  output Y2,
  output Y3
);

  wire and_1_out, and_2_out, and_3_out, and_4_out, and_5_out, and_6_out, and_7_out, and_8_out, and_9_out,
       and_10_out, and_11_out, encoder_4_2_priority_1_y0, encoder_4_2_priority_1_y1,
       encoder_4_2_priority_2_y0, encoder_4_2_priority_2_y1, encoder_4_2_priority_3_y0,
       encoder_4_2_priority_3_y1, encoder_4_2_priority_4_y0, encoder_4_2_priority_4_y1, or_1_out, or_2_out,
       or_3_out, or_4_out;

  or or_1 (or_1_out, A15, A14, A13, A12);
  or or_2 (or_2_out, A11, A10, A9, A8);
  or or_3 (or_3_out, A7, A6, A5, A4);
  or or_4 (or_4_out, A3, A2, A1, A0);
  Encoder_4_2_Priority encoder_4_2_priority_1 (
    .A3(A15), .A2(A14), .A1(A13), .A0(A12), .Y0(encoder_4_2_priority_1_y0), .Y1(encoder_4_2_priority_1_y1));
  Encoder_4_2_Priority encoder_4_2_priority_2 (
    .A3(A11), .A2(A10), .A1(A9), .A0(A8), .Y0(encoder_4_2_priority_2_y0), .Y1(encoder_4_2_priority_2_y1));
  Encoder_4_2_Priority encoder_4_2_priority_3 (
    .A3(A7), .A2(A6), .A1(A5), .A0(A4), .Y0(encoder_4_2_priority_3_y0), .Y1(encoder_4_2_priority_3_y1));
  Encoder_4_2_Priority encoder_4_2_priority_4 (
    .A3(A3), .A2(A2), .A1(A1), .A0(A0), .Y0(encoder_4_2_priority_4_y0), .Y1(encoder_4_2_priority_4_y1));
  and and_1 (and_1_out, ~or_1_out, or_2_out);  // AND_Gate
  and and_2 (and_2_out, ~or_1_out, ~or_2_out, or_3_out);  // AND_Gate
  and and_3 (and_3_out, ~or_1_out, ~or_2_out, ~or_3_out, or_4_out);  // AND_Gate
  and and_4 (and_4_out, or_1_out, encoder_4_2_priority_1_y1);
  and and_5 (and_5_out, and_1_out, encoder_4_2_priority_2_y1);
  and and_6 (and_6_out, and_2_out, encoder_4_2_priority_3_y1);
  Encoder_4_2_Priority encoder_4_2_priority_5 (
    .A3(or_1_out), .A2(or_2_out), .A1(or_3_out), .A0(or_4_out), .Y0(Y2), .Y1(Y3));
  or or_5 (Y1, and_4_out, and_5_out, and_6_out, and_7_out);
  and and_7 (and_7_out, and_3_out, encoder_4_2_priority_4_y1);
  and and_8 (and_8_out, or_1_out, encoder_4_2_priority_1_y0);
  and and_9 (and_9_out, and_1_out, encoder_4_2_priority_2_y0);
  and and_10 (and_10_out, encoder_4_2_priority_3_y0, and_2_out);
  and and_11 (and_11_out, encoder_4_2_priority_4_y0, and_3_out);
  or or_6 (Y0, and_8_out, and_9_out, and_10_out, and_11_out);

  // Notes on the sheet:
  //   S3
  //   S2
  //   S1
  //   S0
endmodule

module DigitalHex_Decoder (
  input  A0,
  input  A1,
  input  A2,
  input  A3,
  output A,
  output B,
  output C,
  output D,
  output E,
  output F,
  output G
);

  wire decoder_1_out0, decoder_1_out1, decoder_1_out2, decoder_1_out3, decoder_1_out4, decoder_1_out5,
       decoder_1_out6, decoder_1_out7, decoder_1_out8, decoder_1_out9, decoder_1_out10, decoder_1_out11,
       decoder_1_out12, decoder_1_out13, decoder_1_out14, decoder_1_out15;

  Decoder #(.select(4)) decoder_1 (
    .out0(decoder_1_out0), .out1(decoder_1_out1), .out2(decoder_1_out2), .out3(decoder_1_out3),
    .out4(decoder_1_out4), .out5(decoder_1_out5), .out6(decoder_1_out6), .out7(decoder_1_out7),
    .out8(decoder_1_out8), .out9(decoder_1_out9), .out10(decoder_1_out10), .out11(decoder_1_out11),
    .out12(decoder_1_out12), .out13(decoder_1_out13), .out14(decoder_1_out14), .out15(decoder_1_out15),
    .sel({A3, A2, A1, A0}), .en(1'b1));
  or or_1 (A, decoder_1_out0, decoder_1_out2, decoder_1_out3, decoder_1_out5, decoder_1_out6, decoder_1_out7, decoder_1_out8, decoder_1_out9, decoder_1_out10, decoder_1_out12, decoder_1_out14, decoder_1_out15);
  or or_2 (B, decoder_1_out0, decoder_1_out1, decoder_1_out2, decoder_1_out3, decoder_1_out4, decoder_1_out7, decoder_1_out8, decoder_1_out9, decoder_1_out10, decoder_1_out13);
  or or_3 (C, decoder_1_out0, decoder_1_out1, decoder_1_out3, decoder_1_out4, decoder_1_out5, decoder_1_out6, decoder_1_out7, decoder_1_out8, decoder_1_out9, decoder_1_out10, decoder_1_out11, decoder_1_out13);
  or or_4 (D, decoder_1_out0, decoder_1_out2, decoder_1_out3, decoder_1_out5, decoder_1_out6, decoder_1_out8, decoder_1_out9, decoder_1_out11, decoder_1_out12, decoder_1_out13, decoder_1_out14);
  or or_5 (E, decoder_1_out0, decoder_1_out2, decoder_1_out6, decoder_1_out8, decoder_1_out10, decoder_1_out11, decoder_1_out12, decoder_1_out13, decoder_1_out14, decoder_1_out15);
  or or_6 (F, decoder_1_out0, decoder_1_out4, decoder_1_out5, decoder_1_out6, decoder_1_out8, decoder_1_out9, decoder_1_out10, decoder_1_out11, decoder_1_out12, decoder_1_out14, decoder_1_out15);
  or or_7 (G, decoder_1_out2, decoder_1_out3, decoder_1_out4, decoder_1_out5, decoder_1_out6, decoder_1_out8, decoder_1_out9, decoder_1_out10, decoder_1_out11, decoder_1_out13, decoder_1_out14, decoder_1_out15);

  // Notes on the sheet:
  //   A
  //   B
  //   C
  //   D
  //   E
  //   F
  //   G
endmodule

module leading0_1 (
);

  wire digitalhex_decoder_1_a, digitalhex_decoder_1_b, digitalhex_decoder_1_c, digitalhex_decoder_1_d,
       digitalhex_decoder_1_e, digitalhex_decoder_1_f, digitalhex_decoder_1_g, dipswitch_1_p1,
       dipswitch_1_p2, dipswitch_1_p3, dipswitch_1_p4, dipswitch_1_p5, dipswitch_1_p6, dipswitch_1_p7,
       dipswitch_1_p8, dipswitch_1_p9, dipswitch_1_p10, dipswitch_1_p11, dipswitch_1_p12, dipswitch_1_p13,
       dipswitch_1_p14, dipswitch_1_p15, dipswitch_1_p16, encoder_16_4_priority_1_y0,
       encoder_16_4_priority_1_y1, encoder_16_4_priority_1_y2, encoder_16_4_priority_1_y3;

  // DipSwitch #(.number(16)) dipswitch_1: pin names not known; wires that end beside it: dipswitch_1_p1, dipswitch_1_p2, dipswitch_1_p3, dipswitch_1_p4, dipswitch_1_p5, dipswitch_1_p6, dipswitch_1_p7, dipswitch_1_p8, dipswitch_1_p9, dipswitch_1_p10, dipswitch_1_p11, dipswitch_1_p12, dipswitch_1_p13, dipswitch_1_p14, dipswitch_1_p15, dipswitch_1_p16, dipswitch_1_p2
  Encoder_16_4_Priority encoder_16_4_priority_1 (
    .A15(dipswitch_1_p1), .A14(dipswitch_1_p2), .A13(dipswitch_1_p3), .A12(dipswitch_1_p4),
    .A11(dipswitch_1_p5), .A10(dipswitch_1_p6), .A9(dipswitch_1_p7), .A8(dipswitch_1_p8),
    .A7(dipswitch_1_p9), .A6(dipswitch_1_p10), .A5(dipswitch_1_p11), .A4(dipswitch_1_p12),
    .A3(dipswitch_1_p13), .A2(dipswitch_1_p14), .A1(dipswitch_1_p15), .A0(dipswitch_1_p16),
    .Y0(encoder_16_4_priority_1_y0), .Y1(encoder_16_4_priority_1_y1), .Y2(encoder_16_4_priority_1_y2),
    .Y3(encoder_16_4_priority_1_y3));
  DigitalHex_Decoder digitalhex_decoder_1 (
    .A0(encoder_16_4_priority_1_y0), .A1(encoder_16_4_priority_1_y1), .A2(encoder_16_4_priority_1_y2),
    .A3(encoder_16_4_priority_1_y3), .A(digitalhex_decoder_1_a), .B(digitalhex_decoder_1_b),
    .C(digitalhex_decoder_1_c), .D(digitalhex_decoder_1_d), .E(digitalhex_decoder_1_e),
    .F(digitalhex_decoder_1_f), .G(digitalhex_decoder_1_g));
  _7_Segment_Display u_7_segment_display_1 (
    .g(digitalhex_decoder_1_g), .f(digitalhex_decoder_1_f), .a(digitalhex_decoder_1_a),
    .b(digitalhex_decoder_1_b), .e(digitalhex_decoder_1_e), .d(digitalhex_decoder_1_d),
    .c(digitalhex_decoder_1_c), .dp(1'b0));
endmodule
