// Logisim project Encoder_4_2_Priority.circ as structural Verilog: 1 circuit, main circuit Encoder_4_2_Priority
module Encoder_4_2_Priority (
  input  A3,
  input  A2,
  input  A1,
  input  A0,
  output Y0,
  output Y1
);

  wire and_1_out, and_2_out, and_3_out, not_1_out, not_2_out;

  not not_1 (not_1_out, A3);
  not not_2 (not_2_out, A2);
  and and_1 (and_1_out, not_1_out, not_2_out);
  and and_2 (and_2_out, and_1_out, A1);
  and and_3 (and_3_out, not_1_out, A2);
  or or_1 (Y0, and_2_out, A3);
  or or_2 (Y1, and_3_out, A3);
endmodule
