// Logisim project 24_Decoder.circ as structural Verilog: 3 circuits, main circuit main
module main (
  input  A2,
  input  A0,
  input  A1,
  output Y0,
  output Y1,
  output Y2,
  output Y3,
  output Y4,
  output Y5,
  output Y6,
  output Y7
);

  wire decoder_24_1_y0, decoder_24_1_y1, decoder_24_1_y2, decoder_24_1_y3, decoder_24_2_y0, decoder_24_2_y1,
       decoder_24_2_y2, decoder_24_2_y3;

  Decoder_24 decoder_24_1 (
    .A0(A0), .A1(A1), .Y0(decoder_24_1_y0), .Y1(decoder_24_1_y1), .Y2(decoder_24_1_y2), .Y3(decoder_24_1_y3));
  Decoder_24 decoder_24_2 (
    .A0(A0), .A1(A1), .Y0(decoder_24_2_y0), .Y1(decoder_24_2_y1), .Y2(decoder_24_2_y2), .Y3(decoder_24_2_y3));
  and and_1 (Y0, decoder_24_1_y0, ~A2);  // AND_Gate
  and and_2 (Y1, decoder_24_1_y1, ~A2);  // AND_Gate
  and and_3 (Y2, decoder_24_1_y2, ~A2);  // AND_Gate
  and and_4 (Y3, decoder_24_1_y3, ~A2);  // AND_Gate
  and and_5 (Y4, decoder_24_2_y0, A2);
  and and_6 (Y5, decoder_24_2_y1, A2);
  and and_7 (Y6, decoder_24_2_y2, A2);
  and and_8 (Y7, decoder_24_2_y3, A2);

  // Notes on the sheet:
  //   A0
  //   A1
  //   A0
  //   A1
endmodule

module Decoder_24 (
  input  A0,
  input  A1,
  output Y0,
  output Y1,
  output Y2,
  output Y3
);

  and and_1 (Y0, ~A0, ~A1);  // AND_Gate
  and and_2 (Y1, A0, ~A1);  // AND_Gate
  and and_3 (Y2, ~A0, A1);  // AND_Gate
  and and_4 (Y3, A0, A1);
endmodule

module Decoder_38 (
  input  A2,
  input  A0,
  input  A1,
  output Y0,
  output Y1,
  output Y2,
  output Y3,
  output Y4,
  output Y5,
  output Y6,
  output Y7
);

  wire decoder_24_1_y0, decoder_24_1_y1, decoder_24_1_y2, decoder_24_1_y3;

  Decoder_24 decoder_24_1 (
    .A0(A0), .A1(A1), .Y0(decoder_24_1_y0), .Y1(decoder_24_1_y1), .Y2(decoder_24_1_y2), .Y3(decoder_24_1_y3));
  and and_1 (Y0, decoder_24_1_y0, ~A2);  // AND_Gate
  and and_2 (Y1, decoder_24_1_y1, ~A2);  // AND_Gate
  and and_3 (Y2, decoder_24_1_y2, ~A2);  // AND_Gate
  and and_4 (Y3, decoder_24_1_y3, ~A2);  // AND_Gate
  and and_5 (Y4, decoder_24_1_y0, A2);
  and and_6 (Y5, decoder_24_1_y1, A2);
  and and_7 (Y6, decoder_24_1_y2, A2);
  and and_8 (Y7, decoder_24_1_y3, A2);

  // Notes on the sheet:
  //   A0
  //   A1
endmodule
