// Logisim project DigitalSeg.circ as structural Verilog: 1 circuit, main circuit DigitalSeg
module DigitalSeg (
);

  wire decoder_1_out0, decoder_1_out1, decoder_1_out2, decoder_1_out3, decoder_1_out4, decoder_1_out5,
       decoder_1_out6, decoder_1_out7, decoder_1_out8, decoder_1_out9, decoder_1_out10, decoder_1_out11,
       decoder_1_out12, decoder_1_out13, decoder_1_out14, decoder_1_out15, or_1_out, or_2_out, or_3_out,
       or_4_out, or_5_out, or_6_out, or_7_out, or_8_out;
  wire [3:0] dipswitch_1_sw1;

  Decoder #(.select(4)) decoder_1 (
    .out0(decoder_1_out0), .out1(decoder_1_out1), .out2(decoder_1_out2), .out3(decoder_1_out3),
    .out4(decoder_1_out4), .out5(decoder_1_out5), .out6(decoder_1_out6), .out7(decoder_1_out7),
    .out8(decoder_1_out8), .out9(decoder_1_out9), .out10(decoder_1_out10), .out11(decoder_1_out11),
    .out12(decoder_1_out12), .out13(decoder_1_out13), .out14(decoder_1_out14), .out15(decoder_1_out15),
    .sel(dipswitch_1_sw1), .en(1'b1));
  DipSwitch #(.number(4)) dipswitch_1 (
    .sw1(dipswitch_1_sw1[0]), .sw2(dipswitch_1_sw1[1]), .sw3(dipswitch_1_sw1[2]), .sw4(dipswitch_1_sw1[3]));
  or or_1 (or_1_out, decoder_1_out10, decoder_1_out11, decoder_1_out12, decoder_1_out13, decoder_1_out14, decoder_1_out15);
  or or_2 (or_2_out, decoder_1_out0, decoder_1_out2, decoder_1_out3, decoder_1_out5, decoder_1_out6, decoder_1_out7, decoder_1_out8, decoder_1_out9);
  or or_3 (or_3_out, decoder_1_out0, decoder_1_out1, decoder_1_out2, decoder_1_out3, decoder_1_out4, decoder_1_out7, decoder_1_out8, decoder_1_out9);
  or or_4 (or_4_out, decoder_1_out0, decoder_1_out1, decoder_1_out3, decoder_1_out4, decoder_1_out5, decoder_1_out6, decoder_1_out7, decoder_1_out8, decoder_1_out9);
  or or_5 (or_5_out, decoder_1_out0, decoder_1_out2, decoder_1_out3, decoder_1_out5, decoder_1_out6, decoder_1_out8, decoder_1_out9);
  or or_6 (or_6_out, decoder_1_out0, decoder_1_out2, decoder_1_out6, decoder_1_out8);
  or or_7 (or_7_out, decoder_1_out0, decoder_1_out4, decoder_1_out5, decoder_1_out6, decoder_1_out8, decoder_1_out9);
  or or_8 (or_8_out, decoder_1_out2, decoder_1_out3, decoder_1_out4, decoder_1_out5, decoder_1_out6, decoder_1_out8, decoder_1_out9);
  _7_Segment_Display u_7_segment_display_1 (
    .g(or_8_out), .f(or_7_out), .a(or_2_out), .b(or_3_out), .e(or_6_out), .d(or_5_out), .c(or_4_out),
    .dp(or_1_out));

  // Notes on the sheet:
  //   1
  //   2
  //   3
  //   4
  //   5
  //   6
  //   7
  //   8
  //   9
  //   A
  //   B
  //   C
  //   D
  //   E
  //   F
  //   G
  //   H
endmodule
