// Logisim project DigitalSeg_withGate.circ as structural Verilog: 1 circuit, main circuit main
module main (
  input  [3:0] DIN
);

  wire and_1_out, and_2_out, and_3_out, and_4_out, and_5_out, nand_1_out, nand_2_out, nand_3_out, nor_1_out,
       xor_1_out, xor_2_out;

  and and_1 (and_1_out, ~DIN[3], ~DIN[1]);  // AND_Gate
  xor xor_1 (xor_1_out, DIN[2], DIN[0]);
  and and_2 (and_2_out, ~DIN[3], DIN[2]);  // AND_Gate
  xor xor_2 (xor_2_out, DIN[1], DIN[0]);
  nand nand_1 (nand_1_out, ~DIN[3], ~DIN[2], DIN[1], ~DIN[0]);  // NAND_Gate
  and and_3 (and_3_out, ~DIN[3], ~DIN[2], ~DIN[1], DIN[0]);  // AND_Gate
  and and_4 (and_4_out, ~DIN[3], DIN[2], ~DIN[1], ~DIN[0]);  // AND_Gate
  and and_5 (and_5_out, ~DIN[3], DIN[2], DIN[1], DIN[0]);  // AND_Gate
  nand nand_2 (nand_2_out, and_1_out, xor_1_out);
  nand nand_3 (nand_3_out, and_2_out, xor_2_out);
  nor nor_1 (nor_1_out, and_3_out, and_4_out, and_5_out);
  _7_Segment_Display u_7_segment_display_1 (
    .a(nand_2_out), .b(nand_3_out), .d(nor_1_out), .c(nand_1_out), .dp(1'b0));  // open: g, f, e

  // Notes on the sheet:
  //   A
  //   B
  //   C
endmodule
