// Logisim project MUX_4_1.circ as structural Verilog: 1 circuit, main circuit MUX_4_1
module MUX_4_1 (
  input  [2:0] D0,
  input  S0,
  input  S1,
  input  [2:0] D1,
  input  [2:0] D2,
  input  [2:0] D3,
  output [2:0] Y
);

  wire decoder_24_1_y0, decoder_24_1_y1, decoder_24_1_y2, decoder_24_1_y3;
  wire [2:0] and_3_out, and_6_out, and_9_out, and_12_out;

  Decoder_24 decoder_24_1 (
    .A0(S0), .A1(S1), .Y0(decoder_24_1_y0), .Y1(decoder_24_1_y1), .Y2(decoder_24_1_y2), .Y3(decoder_24_1_y3));
  and and_1 (and_3_out[2], D0[2], decoder_24_1_y0);
  and and_2 (and_3_out[1], D0[1], decoder_24_1_y0);
  and and_3 (and_3_out[0], D0[0], decoder_24_1_y0);
  and and_4 (and_6_out[2], D1[2], decoder_24_1_y1);
  and and_5 (and_6_out[1], D1[1], decoder_24_1_y1);
  and and_6 (and_6_out[0], D1[0], decoder_24_1_y1);
  and and_7 (and_9_out[2], D2[2], decoder_24_1_y2);
  and and_8 (and_9_out[1], D2[1], decoder_24_1_y2);
  and and_9 (and_9_out[0], D2[0], decoder_24_1_y2);
  and and_10 (and_12_out[2], D3[2], decoder_24_1_y3);
  and and_11 (and_12_out[1], D3[1], decoder_24_1_y3);
  and and_12 (and_12_out[0], D3[0], decoder_24_1_y3);
  assign Y = and_3_out | and_6_out | and_9_out | and_12_out;  // OR_Gate or_1, 3 bits wide
endmodule
