// Logisim project MUX_DigitalSeg.circ as structural Verilog: 3 circuits, main circuit MUX_DigitalSeg
module MUX_DigitalSeg (
);

  wire decoder_digitahex_1_a, decoder_digitahex_1_b, decoder_digitahex_1_c, decoder_digitahex_1_d,
       decoder_digitahex_1_e, decoder_digitahex_1_f, decoder_digitahex_1_g, decoder_digitahex_1_h,
       decoder_digitaldeci_1_a, decoder_digitaldeci_1_b, decoder_digitaldeci_1_c, decoder_digitaldeci_1_d,
       decoder_digitaldeci_1_e, decoder_digitaldeci_1_f, decoder_digitaldeci_1_g, decoder_digitaldeci_1_h,
       dipswitch_1_p1, dipswitch_1_p2, dipswitch_1_p3, dipswitch_1_p4, dipswitch_1_p5, not_1_out;
  wire [7:0] and_1_out, and_9_out, or_1_out;

  // DipSwitch #(.number(5)) dipswitch_1: pin names not known; wires that end beside it: dipswitch_1_p1, dipswitch_1_p2, dipswitch_1_p3, dipswitch_1_p4, dipswitch_1_p5
  not not_1 (not_1_out, dipswitch_1_p5);
  Decoder_DigitaHex decoder_digitahex_1 (
    .D0(dipswitch_1_p1), .D1(dipswitch_1_p2), .D2(dipswitch_1_p3), .D3(dipswitch_1_p4),
    .A(decoder_digitahex_1_a), .B(decoder_digitahex_1_b), .C(decoder_digitahex_1_c),
    .D(decoder_digitahex_1_d), .E(decoder_digitahex_1_e), .F(decoder_digitahex_1_f),
    .G(decoder_digitahex_1_g), .H(decoder_digitahex_1_h));
  Decoder_DigitalDeci decoder_digitaldeci_1 (
    .D0(dipswitch_1_p1), .D1(dipswitch_1_p2), .D2(dipswitch_1_p3), .D3(dipswitch_1_p4),
    .A(decoder_digitaldeci_1_a), .B(decoder_digitaldeci_1_b), .C(decoder_digitaldeci_1_c),
    .D(decoder_digitaldeci_1_d), .E(decoder_digitaldeci_1_e), .F(decoder_digitaldeci_1_f),
    .G(decoder_digitaldeci_1_g), .H(decoder_digitaldeci_1_h));
  and and_1 (and_1_out[0], dipswitch_1_p5, decoder_digitahex_1_a);
  and and_2 (and_1_out[1], dipswitch_1_p5, decoder_digitahex_1_b);
  and and_3 (and_1_out[2], dipswitch_1_p5, decoder_digitahex_1_c);
  and and_4 (and_1_out[3], dipswitch_1_p5, decoder_digitahex_1_d);
  and and_5 (and_1_out[4], dipswitch_1_p5, decoder_digitahex_1_e);
  and and_6 (and_1_out[5], dipswitch_1_p5, decoder_digitahex_1_f);
  and and_7 (and_1_out[6], dipswitch_1_p5, decoder_digitahex_1_g);
  and and_8 (and_1_out[7], dipswitch_1_p5, decoder_digitahex_1_h);
  and and_9 (and_9_out[0], decoder_digitaldeci_1_a, not_1_out);
  and and_10 (and_9_out[1], decoder_digitaldeci_1_b, not_1_out);
  and and_11 (and_9_out[2], decoder_digitaldeci_1_c, not_1_out);
  and and_12 (and_9_out[3], decoder_digitaldeci_1_d, not_1_out);
  and and_13 (and_9_out[4], decoder_digitaldeci_1_e, not_1_out);
  and and_14 (and_9_out[5], decoder_digitaldeci_1_f, not_1_out);
  and and_15 (and_9_out[6], decoder_digitaldeci_1_g, not_1_out);
  and and_16 (and_9_out[7], decoder_digitaldeci_1_h, not_1_out);
  assign or_1_out = and_1_out | and_9_out;  // OR_Gate or_1, 8 bits wide
  _7_Segment_Display u_7_segment_display_1 (
    .g(or_1_out[6]), .f(or_1_out[5]), .a(or_1_out[0]), .b(or_1_out[1]), .e(or_1_out[4]), .d(or_1_out[3]),
    .c(or_1_out[2]), .dp(or_1_out[7]));
endmodule

module Decoder_DigitaHex (
  input  D0,
  input  D1,
  input  D2,
  input  D3,
  output A,
  output B,
  output C,
  output D,
  output E,
  output F,
  output G,
  output H
);

  wire decoder_1_out0, decoder_1_out1, decoder_1_out2, decoder_1_out3, decoder_1_out4, decoder_1_out5,
       decoder_1_out6, decoder_1_out7, decoder_1_out8, decoder_1_out9, decoder_1_out10, decoder_1_out11,
       decoder_1_out12, decoder_1_out13, decoder_1_out14, decoder_1_out15;

  Decoder #(.select(4)) decoder_1 (
    .out0(decoder_1_out0), .out1(decoder_1_out1), .out2(decoder_1_out2), .out3(decoder_1_out3),
    .out4(decoder_1_out4), .out5(decoder_1_out5), .out6(decoder_1_out6), .out7(decoder_1_out7),
    .out8(decoder_1_out8), .out9(decoder_1_out9), .out10(decoder_1_out10), .out11(decoder_1_out11),
    .out12(decoder_1_out12), .out13(decoder_1_out13), .out14(decoder_1_out14), .out15(decoder_1_out15),
    .sel({D3, D2, D1, D0}), .en(1'b1));
  or or_1 (A, decoder_1_out0, decoder_1_out2, decoder_1_out3, decoder_1_out5, decoder_1_out6, decoder_1_out7, decoder_1_out8, decoder_1_out9, decoder_1_out10, decoder_1_out12, decoder_1_out14, decoder_1_out15);
  or or_2 (B, decoder_1_out0, decoder_1_out1, decoder_1_out2, decoder_1_out3, decoder_1_out4, decoder_1_out7, decoder_1_out8, decoder_1_out9, decoder_1_out10, decoder_1_out13);
  or or_3 (C, decoder_1_out0, decoder_1_out1, decoder_1_out3, decoder_1_out4, decoder_1_out5, decoder_1_out6, decoder_1_out7, decoder_1_out8, decoder_1_out9, decoder_1_out10, decoder_1_out11, decoder_1_out13);
  or or_4 (D, decoder_1_out0, decoder_1_out2, decoder_1_out3, decoder_1_out5, decoder_1_out6, decoder_1_out8, decoder_1_out9, decoder_1_out11, decoder_1_out12, decoder_1_out13, decoder_1_out14);
  or or_5 (E, decoder_1_out0, decoder_1_out2, decoder_1_out6, decoder_1_out8, decoder_1_out10, decoder_1_out11, decoder_1_out12, decoder_1_out13, decoder_1_out14, decoder_1_out15);
  or or_6 (F, decoder_1_out0, decoder_1_out4, decoder_1_out5, decoder_1_out6, decoder_1_out8, decoder_1_out9, decoder_1_out10, decoder_1_out11, decoder_1_out12, decoder_1_out14, decoder_1_out15);
  or or_7 (G, decoder_1_out2, decoder_1_out3, decoder_1_out4, decoder_1_out5, decoder_1_out6, decoder_1_out8, decoder_1_out9, decoder_1_out10, decoder_1_out11, decoder_1_out13, decoder_1_out14, decoder_1_out15);

  assign H = 1'b0;

  // Notes on the sheet:
  //   A
  //   B
  //   C
  //   D
  //   E
  //   F
  //   G
endmodule

module Decoder_DigitalDeci (
  input  D0,
  input  D1,
  input  D2,
  input  D3,
  output A,
  output B,
  output C,
  output D,
  output E,
  output F,
  output G,
  output H
);

  wire decoder_1_out0, decoder_1_out1, decoder_1_out2, decoder_1_out3, decoder_1_out4, decoder_1_out5,
       decoder_1_out6, decoder_1_out7, decoder_1_out8, decoder_1_out9, decoder_1_out10, decoder_1_out11,
       decoder_1_out12, decoder_1_out13, decoder_1_out14, decoder_1_out15;

  Decoder #(.select(4)) decoder_1 (
    .out0(decoder_1_out0), .out1(decoder_1_out1), .out2(decoder_1_out2), .out3(decoder_1_out3),
    .out4(decoder_1_out4), .out5(decoder_1_out5), .out6(decoder_1_out6), .out7(decoder_1_out7),
    .out8(decoder_1_out8), .out9(decoder_1_out9), .out10(decoder_1_out10), .out11(decoder_1_out11),
    .out12(decoder_1_out12), .out13(decoder_1_out13), .out14(decoder_1_out14), .out15(decoder_1_out15),
    .sel({D3, D2, D1, D0}), .en(1'b1));
  or or_1 (H, decoder_1_out10, decoder_1_out11, decoder_1_out12, decoder_1_out13, decoder_1_out14, decoder_1_out15);
  or or_2 (A, decoder_1_out0, decoder_1_out2, decoder_1_out3, decoder_1_out5, decoder_1_out6, decoder_1_out7, decoder_1_out8, decoder_1_out9);
  or or_3 (B, decoder_1_out0, decoder_1_out1, decoder_1_out2, decoder_1_out3, decoder_1_out4, decoder_1_out7, decoder_1_out8, decoder_1_out9);
  or or_4 (C, decoder_1_out0, decoder_1_out1, decoder_1_out3, decoder_1_out4, decoder_1_out5, decoder_1_out6, decoder_1_out7, decoder_1_out8, decoder_1_out9);
  or or_5 (D, decoder_1_out0, decoder_1_out2, decoder_1_out3, decoder_1_out5, decoder_1_out6, decoder_1_out8, decoder_1_out9);
  or or_6 (E, decoder_1_out0, decoder_1_out2, decoder_1_out6, decoder_1_out8);
  or or_7 (F, decoder_1_out0, decoder_1_out4, decoder_1_out5, decoder_1_out6, decoder_1_out8, decoder_1_out9);
  or or_8 (G, decoder_1_out2, decoder_1_out3, decoder_1_out4, decoder_1_out5, decoder_1_out6, decoder_1_out8, decoder_1_out9);

  // Notes on the sheet:
  //   1
  //   2
  //   3
  //   4
  //   5
  //   6
  //   7
  //   8
  //   9
  //   A
  //   B
  //   C
  //   D
  //   E
  //   F
  //   G
  //   H
endmodule
