// Logisim project sCPU_Error.circ as structural Verilog: 2 circuits, main circuit decoder_4_16
module decoder_4_16 (
  input  A3,
  input  A2,
  input  A1,
  input  A0,
  output Y0,
  output Y1,
  output Y2,
  output Y3,
  output Y4,
  output Y5,
  output Y6,
  output Y7,
  output Y8,
  output Y9,
  output Y10,
  output Y11,
  output Y12,
  output Y13,
  output Y14,
  output Y15
);

  and and_1 (Y0, ~A3, ~A2, ~A1, ~A0);  // AND_Gate
  and and_2 (Y1, ~A3, ~A2, ~A1, A0);  // AND_Gate
  and and_3 (Y2, ~A3, ~A2, A1, ~A0);  // AND_Gate
  and and_4 (Y3, ~A3, ~A2, A1, A0);  // AND_Gate
  and and_5 (Y4, ~A3, A2, ~A1, ~A0);  // AND_Gate
  and and_6 (Y5, ~A3, A2, ~A1, A0);  // AND_Gate
  and and_7 (Y6, ~A3, A2, A1, ~A0);  // AND_Gate
  and and_8 (Y7, ~A3, A2, A1, A0);  // AND_Gate
  and and_9 (Y8, A3, ~A2, ~A1, ~A0);  // AND_Gate
  and and_10 (Y9, A3, ~A2, ~A1, A0);  // AND_Gate
  and and_11 (Y10, A3, ~A2, A1, ~A0);  // AND_Gate
  and and_12 (Y11, A3, ~A2, A1, A0);  // AND_Gate
  and and_13 (Y12, A3, A2, ~A1, ~A0);  // AND_Gate
  and and_14 (Y13, A3, A2, ~A1, A0);  // AND_Gate
  and and_15 (Y14, A3, A2, A1, ~A0);  // AND_Gate
  and and_16 (Y15, A3, A2, A1, A0);
endmodule

module PC_ROM (
  input  [3:0] addr,
  output Q7,
  output Q6,
  output Q5,
  output Q4,
  output Q3,
  output Q2,
  output Q1,
  output Q0
);

  wire and_1_out, and_2_out, and_3_out, and_4_out, and_5_out, and_6_out, and_7_out, and_8_out, and_9_out,
       and_10_out, and_11_out, and_12_out, and_13_out, and_14_out, and_15_out, and_16_out, and_17_out,
       and_18_out, and_19_out, and_20_out, and_21_out, and_22_out, and_23_out, and_24_out, and_25_out,
       and_26_out, and_27_out, and_28_out, and_29_out, and_30_out, and_31_out, and_32_out, and_33_out,
       and_34_out, and_35_out, and_36_out, and_37_out, and_38_out, and_39_out, and_40_out, and_41_out,
       and_42_out, and_43_out, and_44_out, and_45_out, and_46_out, and_47_out, and_48_out, and_49_out,
       and_50_out, and_51_out, and_52_out, and_53_out, and_54_out, and_55_out, and_56_out, and_57_out,
       and_58_out, and_59_out, and_60_out, and_61_out, and_62_out, and_63_out, and_64_out, and_65_out,
       and_66_out, and_67_out, and_68_out, and_69_out, and_70_out, and_71_out, and_72_out, and_73_out,
       and_74_out, and_75_out, and_76_out, and_77_out, and_78_out, and_79_out, and_80_out, and_81_out,
       and_82_out, and_83_out, and_84_out, and_85_out, and_86_out, and_87_out, and_88_out, and_89_out,
       and_90_out, and_91_out, and_92_out, and_93_out, and_94_out, and_95_out, and_96_out, and_97_out,
       and_98_out, and_99_out, and_100_out, and_101_out, and_102_out, and_103_out, and_104_out, and_105_out,
       and_106_out, and_107_out, and_108_out, and_109_out, and_110_out, and_111_out, and_112_out,
       and_113_out, and_114_out, and_115_out, and_116_out, and_117_out, and_118_out, and_119_out,
       and_120_out, and_121_out, and_122_out, and_123_out, and_124_out, and_125_out, and_126_out,
       and_127_out, and_128_out, decoder_4_16_1_y0, decoder_4_16_1_y1, decoder_4_16_1_y2, decoder_4_16_1_y3,
       decoder_4_16_1_y4, decoder_4_16_1_y5, decoder_4_16_1_y6, decoder_4_16_1_y7, decoder_4_16_1_y8,
       decoder_4_16_1_y9, decoder_4_16_1_y10, decoder_4_16_1_y11, decoder_4_16_1_y12, decoder_4_16_1_y13,
       decoder_4_16_1_y14, decoder_4_16_1_y15, undriven, undriven_2, undriven_3, undriven_4, undriven_5,
       undriven_6, undriven_7, undriven_8, undriven_9, undriven_10, undriven_11, undriven_12, undriven_13,
       undriven_14, undriven_15, undriven_16, undriven_17, undriven_18, undriven_19, undriven_20,
       undriven_21, undriven_22, undriven_23, undriven_24, undriven_25, undriven_26, undriven_27,
       undriven_28, undriven_29, undriven_30, undriven_31, undriven_32, undriven_33, undriven_34,
       undriven_35, undriven_36, undriven_37, undriven_38, undriven_39, undriven_40, undriven_41,
       undriven_42, undriven_43, undriven_44, undriven_45, undriven_46, undriven_47, undriven_48,
       undriven_49, undriven_50, undriven_51, undriven_52, undriven_53, undriven_54, undriven_55,
       undriven_56, undriven_57, undriven_58, undriven_59, undriven_60, undriven_61, undriven_62,
       undriven_63, undriven_64, undriven_65, undriven_66, undriven_67, undriven_68, undriven_69,
       undriven_70, undriven_71, undriven_72, undriven_73, undriven_74, undriven_75, undriven_76,
       undriven_77, undriven_78, undriven_79, undriven_80, undriven_81, undriven_82, undriven_83,
       undriven_84, undriven_85, undriven_86, undriven_87, undriven_88, undriven_89, undriven_90,
       undriven_91, undriven_92, undriven_93, undriven_94, undriven_95, undriven_96, undriven_97,
       undriven_98, undriven_99, undriven_100, undriven_101, undriven_102, undriven_103, undriven_104,
       undriven_105, undriven_106, undriven_107, undriven_108, undriven_109, undriven_110, undriven_111,
       undriven_112, undriven_113, undriven_114, undriven_115, undriven_116, undriven_117, undriven_118,
       undriven_119, undriven_120, undriven_121, undriven_122, undriven_123, undriven_124, undriven_125,
       undriven_126, undriven_127, undriven_128;

  decoder_4_16 decoder_4_16_1 (
    .A3(addr[3]), .A2(addr[2]), .A1(addr[1]), .A0(addr[0]), .Y0(decoder_4_16_1_y0), .Y1(decoder_4_16_1_y1),
    .Y2(decoder_4_16_1_y2), .Y3(decoder_4_16_1_y3), .Y4(decoder_4_16_1_y4), .Y5(decoder_4_16_1_y5),
    .Y6(decoder_4_16_1_y6), .Y7(decoder_4_16_1_y7), .Y8(decoder_4_16_1_y8), .Y9(decoder_4_16_1_y9),
    .Y10(decoder_4_16_1_y10), .Y11(decoder_4_16_1_y11), .Y12(decoder_4_16_1_y12), .Y13(decoder_4_16_1_y13),
    .Y14(decoder_4_16_1_y14), .Y15(decoder_4_16_1_y15));
  and and_1 (and_1_out, decoder_4_16_1_y0, undriven);
  and and_2 (and_2_out, decoder_4_16_1_y1, undriven_2);
  and and_3 (and_3_out, decoder_4_16_1_y2, undriven_3);
  and and_4 (and_4_out, decoder_4_16_1_y3, undriven_4);
  and and_5 (and_5_out, decoder_4_16_1_y4, undriven_5);
  and and_6 (and_6_out, decoder_4_16_1_y5, undriven_6);
  and and_7 (and_7_out, decoder_4_16_1_y6, undriven_7);
  and and_8 (and_8_out, decoder_4_16_1_y7, undriven_8);
  and and_9 (and_9_out, decoder_4_16_1_y8, undriven_9);
  and and_10 (and_10_out, decoder_4_16_1_y9, undriven_10);
  and and_11 (and_11_out, decoder_4_16_1_y10, undriven_11);
  and and_12 (and_12_out, decoder_4_16_1_y11, undriven_12);
  and and_13 (and_13_out, decoder_4_16_1_y12, undriven_13);
  and and_14 (and_14_out, decoder_4_16_1_y13, undriven_14);
  and and_15 (and_15_out, decoder_4_16_1_y14, undriven_15);
  and and_16 (and_16_out, decoder_4_16_1_y15, undriven_16);
  or or_1 (Q7, and_16_out, and_15_out, and_14_out, and_13_out, and_12_out, and_11_out, and_10_out, and_9_out, and_8_out, and_7_out, and_6_out, and_5_out, and_4_out, and_3_out, and_2_out, and_1_out);
  and and_17 (and_17_out, decoder_4_16_1_y0, undriven_17);
  and and_18 (and_18_out, decoder_4_16_1_y1, undriven_18);
  and and_19 (and_19_out, decoder_4_16_1_y2, undriven_19);
  and and_20 (and_20_out, decoder_4_16_1_y3, undriven_20);
  and and_21 (and_21_out, decoder_4_16_1_y4, undriven_21);
  and and_22 (and_22_out, decoder_4_16_1_y5, undriven_22);
  and and_23 (and_23_out, decoder_4_16_1_y6, undriven_23);
  and and_24 (and_24_out, decoder_4_16_1_y7, undriven_24);
  and and_25 (and_25_out, decoder_4_16_1_y8, undriven_25);
  and and_26 (and_26_out, decoder_4_16_1_y9, undriven_26);
  and and_27 (and_27_out, decoder_4_16_1_y10, undriven_27);
  and and_28 (and_28_out, decoder_4_16_1_y11, undriven_28);
  and and_29 (and_29_out, decoder_4_16_1_y12, undriven_29);
  and and_30 (and_30_out, decoder_4_16_1_y13, undriven_30);
  and and_31 (and_31_out, decoder_4_16_1_y14, undriven_31);
  and and_32 (and_32_out, decoder_4_16_1_y15, undriven_32);
  or or_2 (Q6, and_32_out, and_31_out, and_30_out, and_29_out, and_28_out, and_27_out, and_26_out, and_25_out, and_24_out, and_23_out, and_22_out, and_21_out, and_20_out, and_19_out, and_18_out, and_17_out);
  and and_33 (and_33_out, decoder_4_16_1_y0, undriven_33);
  and and_34 (and_34_out, decoder_4_16_1_y1, undriven_34);
  and and_35 (and_35_out, decoder_4_16_1_y2, undriven_35);
  and and_36 (and_36_out, decoder_4_16_1_y3, undriven_36);
  and and_37 (and_37_out, decoder_4_16_1_y4, undriven_37);
  and and_38 (and_38_out, decoder_4_16_1_y5, undriven_38);
  and and_39 (and_39_out, decoder_4_16_1_y6, undriven_39);
  and and_40 (and_40_out, decoder_4_16_1_y7, undriven_40);
  and and_41 (and_41_out, decoder_4_16_1_y8, undriven_41);
  and and_42 (and_42_out, decoder_4_16_1_y9, undriven_42);
  and and_43 (and_43_out, decoder_4_16_1_y10, undriven_43);
  and and_44 (and_44_out, decoder_4_16_1_y11, undriven_44);
  and and_45 (and_45_out, decoder_4_16_1_y12, undriven_45);
  and and_46 (and_46_out, decoder_4_16_1_y13, undriven_46);
  and and_47 (and_47_out, decoder_4_16_1_y14, undriven_47);
  and and_48 (and_48_out, decoder_4_16_1_y15, undriven_48);
  or or_3 (Q5, and_48_out, and_47_out, and_46_out, and_45_out, and_44_out, and_43_out, and_42_out, and_41_out, and_40_out, and_39_out, and_38_out, and_37_out, and_36_out, and_35_out, and_34_out, and_33_out);
  and and_49 (and_49_out, decoder_4_16_1_y0, undriven_49);
  and and_50 (and_50_out, decoder_4_16_1_y1, undriven_50);
  and and_51 (and_51_out, decoder_4_16_1_y2, undriven_51);
  and and_52 (and_52_out, decoder_4_16_1_y3, undriven_52);
  and and_53 (and_53_out, decoder_4_16_1_y4, undriven_53);
  and and_54 (and_54_out, decoder_4_16_1_y5, undriven_54);
  and and_55 (and_55_out, decoder_4_16_1_y6, undriven_55);
  and and_56 (and_56_out, decoder_4_16_1_y7, undriven_56);
  and and_57 (and_57_out, decoder_4_16_1_y8, undriven_57);
  and and_58 (and_58_out, decoder_4_16_1_y9, undriven_58);
  and and_59 (and_59_out, decoder_4_16_1_y10, undriven_59);
  and and_60 (and_60_out, decoder_4_16_1_y11, undriven_60);
  and and_61 (and_61_out, decoder_4_16_1_y12, undriven_61);
  and and_62 (and_62_out, decoder_4_16_1_y13, undriven_62);
  and and_63 (and_63_out, decoder_4_16_1_y14, undriven_63);
  and and_64 (and_64_out, decoder_4_16_1_y15, undriven_64);
  or or_4 (Q4, and_64_out, and_63_out, and_62_out, and_61_out, and_60_out, and_59_out, and_58_out, and_57_out, and_56_out, and_55_out, and_54_out, and_53_out, and_52_out, and_51_out, and_50_out, and_49_out);
  and and_65 (and_65_out, decoder_4_16_1_y0, undriven_65);
  and and_66 (and_66_out, decoder_4_16_1_y1, undriven_66);
  and and_67 (and_67_out, decoder_4_16_1_y2, undriven_67);
  and and_68 (and_68_out, decoder_4_16_1_y3, undriven_68);
  and and_69 (and_69_out, decoder_4_16_1_y4, undriven_69);
  and and_70 (and_70_out, decoder_4_16_1_y5, undriven_70);
  and and_71 (and_71_out, decoder_4_16_1_y6, undriven_71);
  and and_72 (and_72_out, decoder_4_16_1_y7, undriven_72);
  and and_73 (and_73_out, decoder_4_16_1_y8, undriven_73);
  and and_74 (and_74_out, decoder_4_16_1_y9, undriven_74);
  and and_75 (and_75_out, decoder_4_16_1_y10, undriven_75);
  and and_76 (and_76_out, decoder_4_16_1_y11, undriven_76);
  and and_77 (and_77_out, decoder_4_16_1_y12, undriven_77);
  and and_78 (and_78_out, decoder_4_16_1_y13, undriven_78);
  and and_79 (and_79_out, decoder_4_16_1_y14, undriven_79);
  and and_80 (and_80_out, decoder_4_16_1_y15, undriven_80);
  or or_5 (Q3, and_80_out, and_79_out, and_78_out, and_77_out, and_76_out, and_75_out, and_74_out, and_73_out, and_72_out, and_71_out, and_70_out, and_69_out, and_68_out, and_67_out, and_66_out, and_65_out);
  and and_81 (and_81_out, decoder_4_16_1_y0, undriven_81);
  and and_82 (and_82_out, decoder_4_16_1_y1, undriven_82);
  and and_83 (and_83_out, decoder_4_16_1_y2, undriven_83);
  and and_84 (and_84_out, decoder_4_16_1_y3, undriven_84);
  and and_85 (and_85_out, decoder_4_16_1_y4, undriven_85);
  and and_86 (and_86_out, decoder_4_16_1_y5, undriven_86);
  and and_87 (and_87_out, decoder_4_16_1_y6, undriven_87);
  and and_88 (and_88_out, decoder_4_16_1_y7, undriven_88);
  and and_89 (and_89_out, decoder_4_16_1_y8, undriven_89);
  and and_90 (and_90_out, decoder_4_16_1_y9, undriven_90);
  and and_91 (and_91_out, decoder_4_16_1_y10, undriven_91);
  and and_92 (and_92_out, decoder_4_16_1_y11, undriven_92);
  and and_93 (and_93_out, decoder_4_16_1_y12, undriven_93);
  and and_94 (and_94_out, decoder_4_16_1_y13, undriven_94);
  and and_95 (and_95_out, decoder_4_16_1_y14, undriven_95);
  and and_96 (and_96_out, decoder_4_16_1_y15, undriven_96);
  or or_6 (Q2, and_96_out, and_95_out, and_94_out, and_93_out, and_92_out, and_91_out, and_90_out, and_89_out, and_88_out, and_87_out, and_86_out, and_85_out, and_84_out, and_83_out, and_82_out, and_81_out);
  and and_97 (and_97_out, decoder_4_16_1_y0, undriven_97);
  and and_98 (and_98_out, decoder_4_16_1_y1, undriven_98);
  and and_99 (and_99_out, decoder_4_16_1_y2, undriven_99);
  and and_100 (and_100_out, decoder_4_16_1_y3, undriven_100);
  and and_101 (and_101_out, decoder_4_16_1_y4, undriven_101);
  and and_102 (and_102_out, decoder_4_16_1_y5, undriven_102);
  and and_103 (and_103_out, decoder_4_16_1_y6, undriven_103);
  and and_104 (and_104_out, decoder_4_16_1_y7, undriven_104);
  and and_105 (and_105_out, decoder_4_16_1_y8, undriven_105);
  and and_106 (and_106_out, decoder_4_16_1_y9, undriven_106);
  and and_107 (and_107_out, decoder_4_16_1_y10, undriven_107);
  and and_108 (and_108_out, decoder_4_16_1_y11, undriven_108);
  and and_109 (and_109_out, decoder_4_16_1_y12, undriven_109);
  and and_110 (and_110_out, decoder_4_16_1_y13, undriven_110);
  and and_111 (and_111_out, decoder_4_16_1_y14, undriven_111);
  and and_112 (and_112_out, decoder_4_16_1_y15, undriven_112);
  or or_7 (Q1, and_112_out, and_111_out, and_110_out, and_109_out, and_108_out, and_107_out, and_106_out, and_105_out, and_104_out, and_103_out, and_102_out, and_101_out, and_100_out, and_99_out, and_98_out, and_97_out);
  and and_113 (and_113_out, decoder_4_16_1_y0, undriven_113);
  and and_114 (and_114_out, decoder_4_16_1_y1, undriven_114);
  and and_115 (and_115_out, decoder_4_16_1_y2, undriven_115);
  and and_116 (and_116_out, decoder_4_16_1_y3, undriven_116);
  and and_117 (and_117_out, decoder_4_16_1_y4, undriven_117);
  and and_118 (and_118_out, decoder_4_16_1_y5, undriven_118);
  and and_119 (and_119_out, decoder_4_16_1_y6, undriven_119);
  and and_120 (and_120_out, decoder_4_16_1_y7, undriven_120);
  and and_121 (and_121_out, decoder_4_16_1_y8, undriven_121);
  and and_122 (and_122_out, decoder_4_16_1_y9, undriven_122);
  and and_123 (and_123_out, decoder_4_16_1_y10, undriven_123);
  and and_124 (and_124_out, decoder_4_16_1_y11, undriven_124);
  and and_125 (and_125_out, decoder_4_16_1_y12, undriven_125);
  and and_126 (and_126_out, decoder_4_16_1_y13, undriven_126);
  and and_127 (and_127_out, decoder_4_16_1_y14, undriven_127);
  and and_128 (and_128_out, decoder_4_16_1_y15, undriven_128);
  or or_8 (Q0, and_128_out, and_127_out, and_126_out, and_125_out, and_124_out, and_123_out, and_122_out, and_121_out, and_120_out, and_119_out, and_118_out, and_117_out, and_116_out, and_115_out, and_114_out, and_113_out);
endmodule
