// Logisim project minirv_CPU.circ as structural Verilog: 5 circuits, main circuit FinalminirvCPU
module GPR (
  input  clk,
  input  [31:0] wdata,
  input  [4:0] waddr,
  input  wen,
  input  [4:0] raddr1,
  input  [4:0] raddr2,
  output [31:0] rdata1,
  output [31:0] rdata2
);

  wire decoder_1_out1, decoder_1_out2, decoder_1_out3, decoder_1_out4, decoder_1_out5, decoder_1_out6,
       decoder_1_out7, decoder_1_out8, decoder_1_out9, decoder_1_out10, decoder_1_out11, decoder_1_out12,
       decoder_1_out13, decoder_1_out14, decoder_1_out15;
  wire [31:0] register_1_q, register_2_q, register_3_q, register_4_q, register_5_q, register_6_q,
       register_7_q, register_8_q, register_9_q, register_10_q, register_11_q, register_12_q, register_13_q,
       register_14_q, register_15_q, register_16_q;

  Decoder #(.select(4)) decoder_1 (
    .out1(decoder_1_out1), .out2(decoder_1_out2), .out3(decoder_1_out3), .out4(decoder_1_out4),
    .out5(decoder_1_out5), .out6(decoder_1_out6), .out7(decoder_1_out7), .out8(decoder_1_out8),
    .out9(decoder_1_out9), .out10(decoder_1_out10), .out11(decoder_1_out11), .out12(decoder_1_out12),
    .out13(decoder_1_out13), .out14(decoder_1_out14), .out15(decoder_1_out15), .sel(waddr[3:0]), .en(wen));  // open: out0
  Register #(.width(32)) register_1 (.D(wdata), .en(decoder_1_out1), .clk(clk), .Q(register_1_q), .clr(1'b1));
  Register #(.width(32)) register_2 (.D(wdata), .en(decoder_1_out8), .clk(clk), .Q(register_2_q));  // open: clr
  Register #(.width(32)) register_3 (.D(wdata), .en(decoder_1_out1), .clk(clk), .Q(register_3_q));  // open: clr
  Register #(.width(32)) register_4 (.D(wdata), .en(decoder_1_out9), .clk(clk), .Q(register_4_q));  // open: clr
  Register #(.width(32)) register_5 (.D(wdata), .en(decoder_1_out2), .clk(clk), .Q(register_5_q));  // open: clr
  Register #(.width(32)) register_6 (.D(wdata), .en(decoder_1_out10), .clk(clk), .Q(register_6_q));  // open: clr
  Register #(.width(32)) register_7 (.D(wdata), .en(decoder_1_out3), .clk(clk), .Q(register_7_q));  // open: clr
  Register #(.width(32)) register_8 (.D(wdata), .en(decoder_1_out11), .clk(clk), .Q(register_8_q));  // open: clr
  Register #(.width(32)) register_9 (.D(wdata), .en(decoder_1_out4), .clk(clk), .Q(register_9_q));  // open: clr
  Register #(.width(32)) register_10 (.D(wdata), .en(decoder_1_out12), .clk(clk), .Q(register_10_q));  // open: clr
  Register #(.width(32)) register_11 (.D(wdata), .en(decoder_1_out5), .clk(clk), .Q(register_11_q));  // open: clr
  Register #(.width(32)) register_12 (.D(wdata), .en(decoder_1_out13), .clk(clk), .Q(register_12_q));  // open: clr
  Register #(.width(32)) register_13 (.D(wdata), .en(decoder_1_out6), .clk(clk), .Q(register_13_q));  // open: clr
  Register #(.width(32)) register_14 (.D(wdata), .en(decoder_1_out14), .clk(clk), .Q(register_14_q));  // open: clr
  Register #(.width(32)) register_15 (.D(wdata), .en(decoder_1_out7), .clk(clk), .Q(register_15_q));  // open: clr
  Register #(.width(32)) register_16 (.D(wdata), .en(decoder_1_out15), .clk(clk), .Q(register_16_q));  // open: clr
  Multiplexer #(.select(4), .width(32)) multiplexer_1 (
    .in0(register_1_q), .in1(register_3_q), .in2(register_5_q), .in3(register_7_q), .in4(register_9_q),
    .in5(register_11_q), .in6(register_13_q), .in7(register_15_q), .in8(register_2_q), .in9(register_4_q),
    .in10(register_6_q), .in11(register_8_q), .in12(register_10_q), .in13(register_12_q),
    .in14(register_14_q), .in15(register_16_q), .out(rdata1), .sel(raddr1[3:0]));
  Multiplexer #(.select(4), .width(32)) multiplexer_2 (
    .in0(register_1_q), .in1(register_3_q), .in2(register_5_q), .in3(register_7_q), .in4(register_9_q),
    .in5(register_11_q), .in6(register_13_q), .in7(register_15_q), .in8(register_2_q), .in9(register_4_q),
    .in10(register_6_q), .in11(register_8_q), .in12(register_10_q), .in13(register_12_q),
    .in14(register_14_q), .in15(register_16_q), .out(rdata2), .sel(raddr2[3:0]));

  // Notes on the sheet:
  //   x8
  //   x0
  //   x1
  //   x9
  //   x2
  //   x10
  //   x3
  //   x11
  //   x4
  //   x12
  //   x5
  //   x13
  //   x6
  //   x14
  //   x15
  //   x7
endmodule

module main (
  output [31:0] PCout
);

  wire add, addi, clk, comparator_1_eq, comparator_2_eq, comparator_3_eq, comparator_4_eq, comparator_5_eq,
       comparator_6_eq, comparator_7_eq, comparator_8_eq, comparator_9_eq, comparator_10_eq,
       comparator_12_eq, comparator_13_eq, comparator_14_eq, comparator_15_eq, decoder_1_out0,
       decoder_1_out1, decoder_1_out2, decoder_1_out3, jalr, lbu, lui, lw, not_1_out, or_2_out, or_4_out,
       or_5_out, or_6_out, or_7_out, or_8_out, or_9_out, sb, sw;
  wire [0:0] jalrTarAddr;
  wire [1:0] byteSel, or_3_out;
  wire [2:0] funt3;
  wire [4:0] rd;
  wire [6:0] opcode;
  wire [7:0] multiplexer_7_out;
  wire [31:0] addResult, imm12SignExt, imm12SwSbExt, multiplexer_1_out, multiplexer_2_out, multiplexer_3_out,
       multiplexer_4_out, multiplexer_5_out, PCadd4, rdata1, rdata2, rdataLBU, rdataRAM, swsbaddr;
  wire [31:2] multiplexer_6_out;
  wire [31:15] imm20LuiExt;

  Adder #(.width(32)) adder_1 (.a(PCout), .b(32'h4), .out(PCadd4));  // open: cin, cout
  or or_1 (or_3_out[1], addi, lw, lbu, add);
  Multiplexer #(.width(32)) multiplexer_1 (.in0(rdataRAM), .in1(rdataLBU), .out(multiplexer_1_out), .sel(lbu));
  or or_2 (or_2_out, addi, add, lw, lui, jalr, lbu);
  Clock u_clk (.out(clk));
  not not_1 (not_1_out, jalr);
  Multiplexer #(.width(32)) multiplexer_2 (
    .in0({addResult[31:1], jalrTarAddr[0]}), .in1(PCadd4), .out(multiplexer_2_out), .sel(not_1_out));
  or or_3 (or_3_out[0], lui, lbu, lw);
  Multiplexer #(.select(2), .width(32)) multiplexer_3 (
    .in0(PCadd4), .in1({imm20LuiExt, funt3, {12{1'b0}}}), .in2(addResult), .in3(multiplexer_1_out),
    .out(multiplexer_3_out), .sel(or_3_out));
  Multiplexer #(.width(32)) multiplexer_4 (.in0(imm12SignExt), .in1(rdata2), .out(multiplexer_4_out), .sel(add));
  and and_1 (jalrTarAddr[0], 1'b0, addResult[0]);
  Adder #(.width(32)) adder_2 (.a(rdata1), .b(multiplexer_4_out), .out(addResult));  // open: cin, cout
  Adder #(.width(32)) adder_3 (.a(rdata1), .b(imm12SwSbExt), .out(swsbaddr));  // open: cin, cout
  PC pc_1 (.PCin(multiplexer_2_out), .clk(clk), .PCout(PCout));
  GPR gpr_1 (
    .clk(clk), .wdata(multiplexer_3_out), .waddr(rd), .wen(or_2_out), .raddr1(imm20LuiExt[19:15]),
    .raddr2(imm20LuiExt[24:20]), .rdata1(rdata1), .rdata2(rdata2));
  insROM insrom_1 (.addr(PCout[5:2]), .insOut({imm20LuiExt, funt3, rd, opcode}));
  Comparator #(.mode("unsigned"), .width(7)) comparator_1 (
    .a(opcode), .b(7'b0010011), .eq(comparator_1_eq));  // open: gt, lt
  Comparator #(.mode("unsigned"), .width(3)) comparator_2 (
    .a(funt3), .b(3'b000), .eq(comparator_2_eq));  // open: gt, lt
  Comparator #(.mode("unsigned"), .width(7)) comparator_3 (
    .a(opcode), .b(7'b1100111), .eq(comparator_3_eq));  // open: gt, lt
  Comparator #(.mode("unsigned"), .width(3)) comparator_4 (
    .a(funt3), .b(3'b000), .eq(comparator_4_eq));  // open: gt, lt
  Comparator #(.mode("unsigned"), .width(7)) comparator_5 (
    .a(opcode), .b(7'b0000011), .eq(comparator_5_eq));  // open: gt, lt
  Comparator #(.mode("unsigned"), .width(3)) comparator_6 (
    .a(funt3), .b(3'b010), .eq(comparator_6_eq));  // open: gt, lt
  Comparator #(.mode("unsigned"), .width(7)) comparator_7 (
    .a(opcode), .b(7'b0100011), .eq(comparator_7_eq));  // open: gt, lt
  Comparator #(.mode("unsigned"), .width(3)) comparator_8 (
    .a(funt3), .b(3'b010), .eq(comparator_8_eq));  // open: gt, lt
  and and_2 (addi, comparator_1_eq, comparator_2_eq);
  and and_3 (jalr, comparator_3_eq, comparator_4_eq);
  and and_4 (lw, comparator_5_eq, comparator_6_eq);
  and and_5 (sw, comparator_7_eq, comparator_8_eq);
  assign imm12SwSbExt = {{20{imm20LuiExt[31]}}, {imm20LuiExt[31:25], rd}};  // Bit_Extender bit_extender_1
  assign imm12SignExt = {{20{imm20LuiExt[31]}}, imm20LuiExt[31:20]};  // Bit_Extender bit_extender_2
  Comparator #(.mode("unsigned"), .width(7)) comparator_9 (
    .a(opcode), .b(7'b0110011), .eq(comparator_9_eq));  // open: gt, lt
  Comparator #(.mode("unsigned"), .width(3)) comparator_10 (
    .a(funt3), .b(3'b000), .eq(comparator_10_eq));  // open: gt, lt
  Comparator #(.mode("unsigned"), .width(7)) comparator_11 (.a(opcode), .b(7'b0110111), .eq(lui));  // open: gt, lt
  Comparator #(.mode("unsigned"), .width(7)) comparator_12 (
    .a(opcode), .b(7'b0000011), .eq(comparator_12_eq));  // open: gt, lt
  Comparator #(.mode("unsigned"), .width(3)) comparator_13 (
    .a(funt3), .b(3'b100), .eq(comparator_13_eq));  // open: gt, lt
  Comparator #(.mode("unsigned"), .width(7)) comparator_14 (
    .a(opcode), .b(7'b0100011), .eq(comparator_14_eq));  // open: gt, lt
  Comparator #(.mode("unsigned"), .width(3)) comparator_15 (
    .a(funt3), .b(3'b000), .eq(comparator_15_eq));  // open: gt, lt
  and and_6 (add, comparator_9_eq, comparator_10_eq);
  and and_7 (lbu, comparator_12_eq, comparator_13_eq);
  and and_8 (sb, comparator_14_eq, comparator_15_eq);
  Multiplexer #(.width(32)) multiplexer_5 (
    .in0(rdata2), .in1({rdata2[7:0], rdata2[7:0], rdata2[7:0], rdata2[7:0]}), .out(multiplexer_5_out),
    .sel(sb));
  Decoder #(.enable("false"), .select(2)) decoder_1 (
    .out0(decoder_1_out0), .out1(decoder_1_out1), .out2(decoder_1_out2), .out3(decoder_1_out3), .sel(byteSel));
  or or_4 (or_4_out, lw, lbu);
  or or_5 (or_5_out, decoder_1_out0, sw);
  or or_6 (or_6_out, decoder_1_out1, sw);
  or or_7 (or_7_out, decoder_1_out2, sw);
  or or_8 (or_8_out, decoder_1_out3, sw);
  Multiplexer #(.width(32)) multiplexer_6 (
    .in0(swsbaddr), .in1(addResult), .out({multiplexer_6_out, byteSel}), .sel(or_4_out));
  RAM #(.addrWidth(5), .asyncread("true"), .byteenables("byteEnables"), .dataWidth(32), .\type ("nonvolatile")) ram_1 (
    .addr(multiplexer_6_out[6:2]), .we(or_9_out), .oe(1'b1), .clk(clk), .din(multiplexer_5_out),
    .dout(rdataRAM), .be3(or_8_out), .be2(or_7_out), .be1(or_6_out), .be0(or_5_out));
  or or_9 (or_9_out, sw, sb);
  Multiplexer #(.select(2), .width(8)) multiplexer_7 (
    .in0(rdataRAM[7:0]), .in1(rdataRAM[15:8]), .in2(rdataRAM[23:16]), .in3(rdataRAM[31:24]),
    .out(multiplexer_7_out), .sel(byteSel));
  assign rdataLBU = {{24{1'b0}}, multiplexer_7_out};  // Bit_Extender bit_extender_3

  // Other names for the same wires on the sheet: rs2[4:0] = imm20LuiExt[24:20]; imm20LuiExt[14:12] = funt3;
  //   jalrTarAddr[31:1] = addResult[31:1]; rs1[4:0] = imm20LuiExt[19:15]
endmodule

module PC (
  input  [31:0] PCin,
  input  clk,
  output [31:0] PCout
);

  Register #(.width(32)) register_1 (.D(PCin), .en(1'b1), .clk(clk), .Q(PCout));  // open: clr
endmodule

module insROM (
  input  [3:0] addr,
  output [31:0] insOut
);

  Multiplexer #(.select(4), .width(32)) multiplexer_1 (
    .in0(32'h400793), .in1(32'h7a503), .in2(32'h9000593), .in3(32'hb781a3), .in4(32'hab00593),
    .in5(32'hb78123), .in6(32'hcd00593), .in7(32'hb780a3), .in8(32'hef00593), .in9(32'hb78023),
    .in10(32'h7a503), .in11(32'h2c00067), .in12({32{1'b0}}), .in13({32{1'b0}}), .in14({32{1'b0}}),
    .in15({32{1'b0}}), .out(insOut), .sel(addr));
endmodule

module FinalminirvCPU (
  input  rst,
  output [63:0] out_2,
  output [31:0] PCout
);

  wire add, addi, and_10_out, clk, comparator_1_eq, comparator_2_eq, comparator_3_eq, comparator_4_eq,
       comparator_5_eq, comparator_6_eq, comparator_7_eq, comparator_8_eq, comparator_9_eq, comparator_10_eq,
       comparator_12_eq, comparator_13_eq, comparator_14_eq, comparator_15_eq, comparator_16_eq,
       comparator_17_eq, comparator_18_eq, comparator_19_eq, comparator_19_lt, decoder_1_out0,
       decoder_1_out1, decoder_1_out2, decoder_1_out3, isMem, isVGA, jalr, lbu, lui, lw, not_1_out, or_2_out,
       or_4_out, or_5_out, or_6_out, or_7_out, or_8_out, or_9_out, or_10_out, rgb_video_1_p2, sb, sw;
  wire [0:0] jalrTarAddr;
  wire [1:0] byteSel, or_3_out;
  wire [2:0] funt3;
  wire [4:0] rd;
  wire [6:0] opcode;
  wire [7:0] multiplexer_7_out;
  wire [31:0] addResult, imm12SignExt, imm12SwSbExt, multiplexer_1_out, multiplexer_2_out, multiplexer_3_out,
       multiplexer_4_out, multiplexer_5_out, PCadd4, rdata1, rdata2, rdataLBU, rdataRAM, swsbaddr;
  wire [31:2] memoryAccAddr;
  wire [31:15] imm20LuiExt;

  Counter #(.max('hffffffffffffffff), .width(64)) counter_1 (
    .clr(rst), .up(1'b1), .count(1'b1), .clk(clk), .Q(out_2));  // open: load, D, carry
  Adder #(.width(32)) adder_1 (.a(PCout), .b(32'h4), .out(PCadd4));  // open: cin, cout
  or or_1 (or_3_out[1], addi, lw, lbu, add);
  Multiplexer #(.width(32)) multiplexer_1 (.in0(rdataRAM), .in1(rdataLBU), .out(multiplexer_1_out), .sel(lbu));
  or or_2 (or_2_out, addi, add, lw, lui, jalr, lbu);
  // RGB_Video #(.cursor("No Cursor"), .height(256), .width(256)) rgb_video_1: pin names not known; wires that end beside it: clk, rgb_video_1_p2, memoryAccAddr[9:2], memoryAccAddr[17:10], rdata2[23:0]
  Clock u_clk (.out(clk));
  and and_1 (rgb_video_1_p2, isVGA, sw);
  not not_1 (not_1_out, jalr);
  Multiplexer #(.width(32)) multiplexer_2 (
    .in0({addResult[31:1], jalrTarAddr[0]}), .in1(PCadd4), .out(multiplexer_2_out), .sel(not_1_out));
  or or_3 (or_3_out[0], lui, lbu, lw);
  Multiplexer #(.select(2), .width(32)) multiplexer_3 (
    .in0(PCadd4), .in1({imm20LuiExt, funt3, {12{1'b0}}}), .in2(addResult), .in3(multiplexer_1_out),
    .out(multiplexer_3_out), .sel(or_3_out));
  Multiplexer #(.width(32)) multiplexer_4 (.in0(imm12SignExt), .in1(rdata2), .out(multiplexer_4_out), .sel(add));
  and and_2 (jalrTarAddr[0], 1'b0, addResult[0]);
  Adder #(.width(32)) adder_2 (.a(rdata1), .b(multiplexer_4_out), .out(addResult));  // open: cin, cout
  Adder #(.width(32)) adder_3 (.a(rdata1), .b(imm12SwSbExt), .out(swsbaddr));  // open: cin, cout
  PC pc_1 (.PCin(multiplexer_2_out), .clk(clk), .PCout(PCout));
  GPR gpr_1 (
    .clk(clk), .wdata(multiplexer_3_out), .waddr(rd), .wen(or_2_out), .raddr1(imm20LuiExt[19:15]),
    .raddr2(imm20LuiExt[24:20]), .rdata1(rdata1), .rdata2(rdata2));
  ROM #(.addrWidth(18), .dataWidth(32)) rom_1 (.addr(PCout[19:2]), .data({imm20LuiExt, funt3, rd, opcode}));
  Comparator #(.mode("unsigned"), .width(7)) comparator_1 (
    .a(opcode), .b(7'b0010011), .eq(comparator_1_eq));  // open: gt, lt
  Comparator #(.mode("unsigned"), .width(3)) comparator_2 (
    .a(funt3), .b(3'b000), .eq(comparator_2_eq));  // open: gt, lt
  Comparator #(.mode("unsigned"), .width(7)) comparator_3 (
    .a(opcode), .b(7'b1100111), .eq(comparator_3_eq));  // open: gt, lt
  Comparator #(.mode("unsigned"), .width(3)) comparator_4 (
    .a(funt3), .b(3'b000), .eq(comparator_4_eq));  // open: gt, lt
  Comparator #(.mode("unsigned"), .width(7)) comparator_5 (
    .a(opcode), .b(7'b0000011), .eq(comparator_5_eq));  // open: gt, lt
  Comparator #(.mode("unsigned"), .width(3)) comparator_6 (
    .a(funt3), .b(3'b010), .eq(comparator_6_eq));  // open: gt, lt
  Comparator #(.mode("unsigned"), .width(7)) comparator_7 (
    .a(opcode), .b(7'b0100011), .eq(comparator_7_eq));  // open: gt, lt
  Comparator #(.mode("unsigned"), .width(3)) comparator_8 (
    .a(funt3), .b(3'b010), .eq(comparator_8_eq));  // open: gt, lt
  and and_3 (addi, comparator_1_eq, comparator_2_eq);
  and and_4 (jalr, comparator_3_eq, comparator_4_eq);
  and and_5 (lw, comparator_5_eq, comparator_6_eq);
  and and_6 (sw, comparator_7_eq, comparator_8_eq);
  assign imm12SwSbExt = {{20{imm20LuiExt[31]}}, {imm20LuiExt[31:25], rd}};  // Bit_Extender bit_extender_1
  assign imm12SignExt = {{20{imm20LuiExt[31]}}, imm20LuiExt[31:20]};  // Bit_Extender bit_extender_2
  Comparator #(.mode("unsigned"), .width(7)) comparator_9 (
    .a(opcode), .b(7'b0110011), .eq(comparator_9_eq));  // open: gt, lt
  Comparator #(.mode("unsigned"), .width(3)) comparator_10 (
    .a(funt3), .b(3'b000), .eq(comparator_10_eq));  // open: gt, lt
  Comparator #(.mode("unsigned"), .width(7)) comparator_11 (.a(opcode), .b(7'b0110111), .eq(lui));  // open: gt, lt
  Comparator #(.mode("unsigned"), .width(7)) comparator_12 (
    .a(opcode), .b(7'b0000011), .eq(comparator_12_eq));  // open: gt, lt
  Comparator #(.mode("unsigned"), .width(3)) comparator_13 (
    .a(funt3), .b(3'b100), .eq(comparator_13_eq));  // open: gt, lt
  Comparator #(.mode("unsigned"), .width(7)) comparator_14 (
    .a(opcode), .b(7'b0100011), .eq(comparator_14_eq));  // open: gt, lt
  Comparator #(.mode("unsigned"), .width(3)) comparator_15 (
    .a(funt3), .b(3'b000), .eq(comparator_15_eq));  // open: gt, lt
  and and_7 (add, comparator_9_eq, comparator_10_eq);
  and and_8 (lbu, comparator_12_eq, comparator_13_eq);
  and and_9 (sb, comparator_14_eq, comparator_15_eq);
  Multiplexer #(.width(32)) multiplexer_5 (
    .in0(rdata2), .in1({rdata2[7:0], rdata2[7:0], rdata2[7:0], rdata2[7:0]}), .out(multiplexer_5_out),
    .sel(sb));
  Decoder #(.enable("false"), .select(2)) decoder_1 (
    .out0(decoder_1_out0), .out1(decoder_1_out1), .out2(decoder_1_out2), .out3(decoder_1_out3), .sel(byteSel));
  or or_4 (or_4_out, lw, lbu);
  Multiplexer #(.width(32)) multiplexer_6 (
    .in0(swsbaddr), .in1(addResult), .out({memoryAccAddr, byteSel}), .sel(or_4_out));
  or or_5 (or_5_out, sw, sb);
  RAM #(.addrWidth(18), .asyncread("true"), .byteenables("byteEnables"), .dataWidth(32), .\type ("nonvolatile")) ram_1 (
    .addr(memoryAccAddr[19:2]), .we(and_10_out), .oe(1'b1), .clk(clk), .din(multiplexer_5_out),
    .dout(rdataRAM), .be3(or_9_out), .be2(or_8_out), .be1(or_7_out), .be0(or_6_out));
  and and_10 (and_10_out, or_5_out, isMem);
  or or_6 (or_6_out, decoder_1_out0, sw);
  or or_7 (or_7_out, decoder_1_out1, sw);
  or or_8 (or_8_out, decoder_1_out2, sw);
  or or_9 (or_9_out, decoder_1_out3, sw);
  Comparator #(.mode("unsigned"), .width(4)) comparator_16 (
    .a(memoryAccAddr[23:20]), .b(4'b0000), .eq(comparator_16_eq));  // open: gt, lt
  Comparator #(.mode("unsigned"), .width(4)) comparator_17 (
    .a(memoryAccAddr[27:24]), .b(4'b0000), .eq(comparator_17_eq));  // open: gt, lt
  Comparator #(.mode("unsigned"), .width(4)) comparator_18 (
    .a(memoryAccAddr[31:28]), .b(4'b0010), .eq(comparator_18_eq));  // open: gt, lt
  Comparator #(.mode("unsigned"), .width(20)) comparator_19 (
    .a({memoryAccAddr[19:2], byteSel}), .b(20'h40000), .eq(comparator_19_eq), .lt(comparator_19_lt));  // open: gt
  or or_10 (or_10_out, comparator_19_eq, comparator_19_lt);
  and and_11 (isVGA, or_10_out, comparator_16_eq, comparator_17_eq, comparator_18_eq);
  Multiplexer #(.select(2), .width(8)) multiplexer_7 (
    .in0(rdataRAM[7:0]), .in1(rdataRAM[15:8]), .in2(rdataRAM[23:16]), .in3(rdataRAM[31:24]),
    .out(multiplexer_7_out), .sel(byteSel));
  not not_2 (isMem, isVGA);
  assign rdataLBU = {{24{1'b0}}, multiplexer_7_out};  // Bit_Extender bit_extender_3

  // Other names for the same wires on the sheet: rs2[4:0] = imm20LuiExt[24:20]; memoryAccAddr[1:0] = byteSel;
  //   X[7:0] = memoryAccAddr[9:2]; Y[7:0] = memoryAccAddr[17:10]; imm20LuiExt[14:12] = funt3;
  //   jalrTarAddr[31:1] = addResult[31:1]; rs1[4:0] = imm20LuiExt[19:15]

  // Notes on the sheet:
  //   contents of rom_1 (hex, n*v repeats v):
  //   413 93137 10113 10b7 dbc08093 80e7 fe012823 fea10923 fea12423 fe914203 fe4109a3 ff012783 f787b3
  //   f787b3 4b6b7 f0068693 fdc10113 d787b3 10000713 f12423 10593 100793 b00513 2112023 12023 12223 e12623
  //   e12823 f10a23 10b7 a8408093 80e7 2012083 2410113 8067 ff410113 112423 10b7 a7c08093 80e7 513 1800093
  //   80e7 812083 513 c10113 8067 852583 feb12823 fe812e23 3437 a0840413 ff014183 3401b3 1c183 ff114203
  //   440233 24203 4181b3 ff214203 440233 24203 4181b3 ff314203 440233 24203 4181b3 3237 a0020213 320233
  //   24203 ffc12403 420233 420233 410233 11b7 85c18193 fe312823 14800193 fe312623 fec22203 20067 1052703
  //   52683 452783 fe810113 e12423 112a23 fed12823 fef12623 13737 c0070713 fe012223 ff314203 fe4102a3
  //   fef14203 fe410223 fe412203 470233 24203 fe4105a3 ff214203 fe4102a3 fee14203 fe410223 fe412203 470233
  //   24203 fe410523 ff114203 fe4102a3 fed14203 fe410223 fe412203 470233 24203 fe4104a3 ff014203 fe4102a3
  //   fec14203 fe410223 fe412203 470233 24203 fe410423 fe812703 c52603 fee12823 fe812e23 3437 a0840413
  //   ff014183 3401b3 1c183 ff114203 440233 24203 4181b3 ff214203 440233 24203 4181b3 ff314203 440233
  //   24203 4181b3 3237 a0020213 320233 24203 ffc12403 420233 420233 410233 66800193 fe312823 28000193
  //   fe312623 fec22203 20067 c68733 10000513 fe812e23 fe912c23 fee12823 50413 ff012483 fe812423 feb14183
  //   3181b3 fe312423 fe914183 3181b3 fe912423 feb14203 420233 fe412423 fe914203 4181b3 3181b3 fe312a23
  //   fe912423 33237 b0020213 feb14183 4181b3 1c183 fe3103a3 fea14183 4181b3 1c183 fe310323 fe914183
  //   4181b3 1c183 fe3102a3 fe814183 4181b3 1c183 fe310223 ff412183 fe412203 440233 120213 fe412423
  //   feb14203 420233 fe412423 fe914203 4181b3 3237 b0820213 320233 ff812483 ffc12403 24203 420233 420233
  //   410233 11b7 86018193 fe312823 38800193 fe312623 fec22203 20067 812703 10000513 812823 e78733
  //   fe812e23 fe912c23 fee12823 50413 ff012483 fe812423 feb14183 3181b3 fe312423 fe914183 3181b3 fe912423
  //   feb14203 420233 fe412423 fe914203 4181b3 3181b3 fe312a23 fe912423 33237 b0020213 feb14183 4181b3
  //   1c183 fe3103a3 fea14183 4181b3 1c183 fe310323 fe914183 4181b3 1c183 fe3102a3 fe814183 4181b3 1c183
  //   fe310223 ff412183 fe412203 440233 120213 fe412423 feb14203 420233 fe412423 fe914203 4181b3 3237
  //   b0820213 320233 ff812483 ffc12403 24203 420233 420233 410233 11b7 86418193 fe312823 49800193
  //   fe312623 fec22203 20067 8*f787b3 d787b3 f787b3 f787b3 20000437 f40433 812783 c60633 c60633 fef12423
  //   feb14183 3181b3 fe312423 fe914183 fff78213 fe412423 feb14203 420233 fe412423 fe914203 4181b3 3237
  //   b1820213 418233 24203 420233 420233 410233 65800193 fe312823 53c00193 fe312623 fec22203 20067 912623
  //   493 40513 c12223 b12023 10b7 de008093 80e7 12583 412603 812783 148493 40040413 c585b3 fef12823
  //   fe912623 fe812e23 fe912c23 4b437 d0040413 ff014183 340233 100193 320023 fec14183 3401b3 18023 24183
  //   ff114483 940233 100493 920023 fed14483 9404b3 48023 24483 9181b3 ff214483 940233 100493 920023
  //   fee14483 9404b3 48023 24483 9181b3 ff314483 940233 100493 920023 fef14483 9404b3 48023 24483 9181b3
  //   3237 a0020213 320233 24203 ff812483 ffc12403 420233 420233 410233 65400193 fe312823 54400193
  //   fe312623 fec22203 20067 c12483 1012403 1412083 1810113 8067 10000713 fec12823 fee12623 fe812e23
  //   fe912c23 4b437 d0040413 ff014183 340233 100193 320023 fec14183 3401b3 18023 24183 ff114483 940233
  //   100493 920023 fed14483 9404b3 48023 24483 9181b3 ff214483 940233 100493 920023 fee14483 9404b3 48023
  //   24483 9181b3 ff314483 940233 100493 920023 fef14483 9404b3 48023 24483 9181b3 3237 a0020213 320233
  //   24203 ff812483 ffc12403 420233 420233 410233 74c00193 fe312823 28000193 fe312623 fec22203 20067
  //   812703 fee12823 fec12623 fe812e23 fe912c23 4b437 d0040413 ff014183 340233 100193 320023 fec14183
  //   3401b3 18023 24183 ff114483 940233 100493 920023 fed14483 9404b3 48023 24483 9181b3 ff214483 940233
  //   100493 920023 fee14483 9404b3 48023 24483 9181b3 ff314483 940233 100493 920023 fef14483 9404b3 48023
  //   24483 9181b3 3237 a0020213 320233 24203 ff812483 ffc12403 420233 420233 410233 11b7 83418193
  //   fe312823 38800193 fe312623 fec22203 20067 1412083 40637 20000537 1810113 1237 de020213 20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
endmodule
