// Logisim project sCPU.circ as structural Verilog: 12 circuits, main circuit sCPU
module sCPU (
  input  rst,
  output [7:0] insOut,
  output [7:0] pcOut
);

  wire and_1_out, and_2_out, and_3_out, and_4_out, and_5_out, and_6_out, clk_out, comparator8bit_1_out_3,
       decoder_2_4_1_y0, decoder_2_4_1_y2, decoder_2_4_1_y3, isio, not_1_out, not_2_out, not_3_out, or_1_out;
  wire [1:0] multiplexer_3_out, multiplexer_4_out;
  wire [7:0] adder_1_out, adder_2_out, bit_extender_1_out, button_1_out, dipswitch_1_p1, gpr_wr_1_rdata1,
       gpr_wr_1_rdata2, iodata, multiplexer_1_out, multiplexer_2_out, multiplexer_5_out, multiplexer_6_out,
       multiplexer_8_out, multiplexer_9_out, register_1_q, register_2_q;

  assign bit_extender_1_out = {{4{insOut[5]}}, insOut[5:2]};  // Bit_Extender bit_extender_1
  Adder adder_1 (.a(pcOut), .b(multiplexer_1_out), .out(adder_1_out));  // open: cin, cout
  Multiplexer #(.width(8)) multiplexer_1 (
    .in0(8'h1), .in1(bit_extender_1_out), .out(multiplexer_1_out), .sel(and_1_out));
  Clock clk (.out(clk_out));
  and and_1 (and_1_out, ~comparator8bit_1_out_3, decoder_2_4_1_y3);  // AND_Gate
  PC pc_1 (.clk(clk_out), .rst(rst), .PCin(adder_1_out), .PCout(pcOut));
  insRom_outDisplay insrom_outdisplay_1 (.addr(pcOut), .ROMout(insOut));
  Multiplexer #(.select(2), .width(8)) multiplexer_2 (
    .in0({{6{1'b0}}, insOut[1:0]}), .in1({4'b0000, insOut[1:0], 2'b00}), .in2({2'b00, insOut[1:0], 4'b0000}),
    .in3({insOut[1:0], {6{1'b0}}}), .out(multiplexer_2_out), .sel(insOut[3:2]));
  decoder_2_4 decoder_2_4_1 (
    .A1(insOut[7]), .A0(insOut[6]), .Y0(decoder_2_4_1_y0), .Y1(isio), .Y2(decoder_2_4_1_y2),
    .Y3(decoder_2_4_1_y3));
  Multiplexer #(.width(2)) multiplexer_3 (
    .in0(insOut[3:2]), .in1(2'b00), .out(multiplexer_3_out), .sel(decoder_2_4_1_y3));
  Multiplexer #(.width(2)) multiplexer_4 (.in0(insOut[1:0]), .in1(insOut[5:4]), .out(multiplexer_4_out), .sel(isio));
  not not_1 (not_1_out, insOut[3]);
  and and_2 (and_2_out, not_1_out, isio);
  or or_1 (or_1_out, decoder_2_4_1_y0, and_2_out, decoder_2_4_1_y2);
  and and_3 (and_3_out, decoder_2_4_1_y0, ~decoder_2_4_1_y2);  // AND_Gate
  not not_2 (not_2_out, insOut[3]);
  Multiplexer #(.width(8)) multiplexer_5 (
    .in0(multiplexer_2_out), .in1(adder_2_out), .out(multiplexer_5_out), .sel(and_3_out));
  and and_4 (and_4_out, isio, not_2_out);
  Multiplexer #(.width(8)) multiplexer_6 (
    .in0(multiplexer_5_out), .in1(iodata), .out(multiplexer_6_out), .sel(and_4_out));
  // DipSwitch dipswitch_1: pin names not known; wires that end beside it: dipswitch_1_p1[0], dipswitch_1_p1[1], dipswitch_1_p1[2], dipswitch_1_p1[3], dipswitch_1_p1[4], dipswitch_1_p1[5], dipswitch_1_p1[6], dipswitch_1_p1[7]
  Button button_1 (.out(button_1_out[0]));
  Button button_2 (.out(button_1_out[1]));
  Button button_3 (.out(button_1_out[2]));
  Button button_4 (.out(button_1_out[3]));
  Button button_5 (.out(button_1_out[4]));
  Button button_6 (.out(button_1_out[5]));
  Button button_7 (.out(button_1_out[6]));
  Button button_8 (.out(button_1_out[7]));
  not not_3 (not_3_out, insOut[0]);
  GPR_WR gpr_wr_1 (
    .wdata(multiplexer_6_out), .waddr(insOut[5:4]), .wen(or_1_out), .raddr1(multiplexer_3_out),
    .raddr2(multiplexer_4_out), .rst(rst), .clk(clk_out), .rdata1(gpr_wr_1_rdata1), .rdata2(gpr_wr_1_rdata2));
  Multiplexer #(.width(8)) multiplexer_7 (.in0(dipswitch_1_p1), .in1(button_1_out), .out(iodata), .sel(insOut[0]));
  Adder adder_2 (.a(gpr_wr_1_rdata1), .b(gpr_wr_1_rdata2), .out(adder_2_out));  // open: cin, cout
  and and_5 (and_5_out, isio, not_3_out, insOut[3]);
  Multiplexer #(.width(8)) multiplexer_8 (
    .in0({8{1'b0}}), .in1(gpr_wr_1_rdata2), .out(multiplexer_8_out), .sel(and_5_out));
  and and_6 (and_6_out, isio, insOut[0], insOut[3]);
  Multiplexer #(.width(8)) multiplexer_9 (
    .in0({8{1'b0}}), .in1(gpr_wr_1_rdata2), .out(multiplexer_9_out), .sel(and_6_out));
  // Probe on gpr_wr_1_rdata1
  // Probe on gpr_wr_1_rdata2
  Register register_1 (.D(multiplexer_8_out), .en(and_5_out), .clk(clk_out), .Q(register_1_q));  // open: clr
  Register register_2 (.D(multiplexer_9_out), .en(and_6_out), .clk(clk_out), .Q(register_2_q));  // open: clr
  LedBar ledbar_1 (
    .led0(register_1_q[7]), .led1(register_1_q[6]), .led2(register_1_q[5]), .led3(register_1_q[4]),
    .led4(register_1_q[3]), .led5(register_1_q[2]), .led6(register_1_q[1]), .led7(register_1_q[0]));
  Hex_Digit_Display #(.decimalPoint("false")) hex_digit_display_1 (.value(register_2_q[7:4]));
  comparator8bit comparator8bit_1 (.A(gpr_wr_1_rdata1), .B(gpr_wr_1_rdata2), .out_3(comparator8bit_1_out_3));
  Hex_Digit_Display #(.decimalPoint("false")) hex_digit_display_2 (.value(register_2_q[3:0]));

  // Other names for the same wires on the sheet: idx[2:0] = insOut[2:0]; isout = insOut[3]; imm[1:0] = insOut[1:0]

  // Notes on the sheet:
  //   is_branch
  //   offset
  //   s
  //   rd
  //   add
  //   io
  //   li
  //   bner0
  //   0 li, 1 add
  //   add或li或io输入使能wen
endmodule

module insROM (
  input  [3:0] addr,
  output [7:0] ROMout
);

  wire decoder4_16_1_y0, decoder4_16_1_y1, decoder4_16_1_y2, decoder4_16_1_y3, decoder4_16_1_y4,
       decoder4_16_1_y5, decoder4_16_1_y6, decoder4_16_1_y7, decoder4_16_1_y8, decoder4_16_1_y9,
       decoder4_16_1_y10, decoder4_16_1_y11, decoder4_16_1_y12, decoder4_16_1_y13, decoder4_16_1_y14,
       decoder4_16_1_y15;
  wire [7:0] and_1_out, and_2_out, and_3_out, and_4_out, and_5_out, and_6_out, and_7_out, and_8_out,
       and_9_out, and_10_out, and_11_out, and_12_out, and_13_out, and_14_out, and_15_out, and_16_out,
       bit_extender_1_out, bit_extender_2_out, bit_extender_3_out, bit_extender_4_out, bit_extender_5_out,
       bit_extender_6_out, bit_extender_7_out, bit_extender_8_out, bit_extender_9_out, bit_extender_10_out,
       bit_extender_11_out, bit_extender_12_out, bit_extender_13_out, bit_extender_14_out,
       bit_extender_15_out, bit_extender_16_out;

  decoder4_16 decoder4_16_1 (
    .A3(addr[3]), .A2(addr[2]), .A1(addr[1]), .A0(addr[0]), .Y0(decoder4_16_1_y0), .Y1(decoder4_16_1_y1),
    .Y2(decoder4_16_1_y2), .Y3(decoder4_16_1_y3), .Y4(decoder4_16_1_y4), .Y5(decoder4_16_1_y5),
    .Y6(decoder4_16_1_y6), .Y7(decoder4_16_1_y7), .Y8(decoder4_16_1_y8), .Y9(decoder4_16_1_y9),
    .Y10(decoder4_16_1_y10), .Y11(decoder4_16_1_y11), .Y12(decoder4_16_1_y12), .Y13(decoder4_16_1_y13),
    .Y14(decoder4_16_1_y14), .Y15(decoder4_16_1_y15));
  assign bit_extender_1_out = {{7{decoder4_16_1_y0}}, decoder4_16_1_y0};  // Bit_Extender bit_extender_1
  assign bit_extender_2_out = {{7{decoder4_16_1_y1}}, decoder4_16_1_y1};  // Bit_Extender bit_extender_2
  assign bit_extender_3_out = {{7{decoder4_16_1_y2}}, decoder4_16_1_y2};  // Bit_Extender bit_extender_3
  assign bit_extender_4_out = {{7{decoder4_16_1_y3}}, decoder4_16_1_y3};  // Bit_Extender bit_extender_4
  assign bit_extender_5_out = {{7{decoder4_16_1_y4}}, decoder4_16_1_y4};  // Bit_Extender bit_extender_5
  assign bit_extender_6_out = {{7{decoder4_16_1_y5}}, decoder4_16_1_y5};  // Bit_Extender bit_extender_6
  assign bit_extender_7_out = {{7{decoder4_16_1_y6}}, decoder4_16_1_y6};  // Bit_Extender bit_extender_7
  assign bit_extender_8_out = {{7{decoder4_16_1_y7}}, decoder4_16_1_y7};  // Bit_Extender bit_extender_8
  assign bit_extender_9_out = {{7{decoder4_16_1_y8}}, decoder4_16_1_y8};  // Bit_Extender bit_extender_9
  assign bit_extender_10_out = {{7{decoder4_16_1_y9}}, decoder4_16_1_y9};  // Bit_Extender bit_extender_10
  assign bit_extender_11_out = {{7{decoder4_16_1_y10}}, decoder4_16_1_y10};  // Bit_Extender bit_extender_11
  assign bit_extender_12_out = {{7{decoder4_16_1_y11}}, decoder4_16_1_y11};  // Bit_Extender bit_extender_12
  assign bit_extender_13_out = {{7{decoder4_16_1_y12}}, decoder4_16_1_y12};  // Bit_Extender bit_extender_13
  assign bit_extender_14_out = {{7{decoder4_16_1_y13}}, decoder4_16_1_y13};  // Bit_Extender bit_extender_14
  assign bit_extender_15_out = {{7{decoder4_16_1_y14}}, decoder4_16_1_y14};  // Bit_Extender bit_extender_15
  assign bit_extender_16_out = {{7{decoder4_16_1_y15}}, decoder4_16_1_y15};  // Bit_Extender bit_extender_16
  assign and_1_out = 8'h86 & bit_extender_1_out;  // AND_Gate and_1, 8 bits wide
  assign and_2_out = 8'h92 & bit_extender_2_out;  // AND_Gate and_2, 8 bits wide
  assign and_3_out = 8'h1 & bit_extender_3_out;  // AND_Gate and_3, 8 bits wide
  assign and_4_out = 8'h90 & bit_extender_4_out;  // AND_Gate and_4, 8 bits wide
  assign and_5_out = 8'ha0 & bit_extender_5_out;  // AND_Gate and_5, 8 bits wide
  assign and_6_out = 8'hb1 & bit_extender_6_out;  // AND_Gate and_6, 8 bits wide
  assign and_7_out = 8'h17 & bit_extender_7_out;  // AND_Gate and_7, 8 bits wide
  assign and_8_out = 8'h29 & bit_extender_8_out;  // AND_Gate and_8, 8 bits wide
  assign and_9_out = 8'hf9 & bit_extender_9_out;  // AND_Gate and_9, 8 bits wide
  assign and_10_out = 8'h68 & bit_extender_10_out;  // AND_Gate and_10, 8 bits wide
  assign and_11_out = 8'hc3 & bit_extender_11_out;  // AND_Gate and_11, 8 bits wide
  assign and_12_out = {8{1'b0}} & bit_extender_12_out;  // AND_Gate and_12, 8 bits wide
  assign and_13_out = {8{1'b0}} & bit_extender_13_out;  // AND_Gate and_13, 8 bits wide
  assign and_14_out = {8{1'b0}} & bit_extender_14_out;  // AND_Gate and_14, 8 bits wide
  assign and_15_out = {8{1'b0}} & bit_extender_15_out;  // AND_Gate and_15, 8 bits wide
  assign and_16_out = {8{1'b0}} & bit_extender_16_out;  // AND_Gate and_16, 8 bits wide
  assign ROMout = and_1_out | and_2_out | and_3_out | and_4_out | and_5_out | and_6_out | and_7_out | and_8_out | and_9_out | and_10_out | and_11_out | and_12_out | and_13_out | and_14_out | and_15_out | and_16_out;  // OR_Gate or_1, 8 bits wide
endmodule

module decoder4_16 (
  input  A3,
  input  A2,
  input  A1,
  input  A0,
  output Y0,
  output Y1,
  output Y2,
  output Y3,
  output Y4,
  output Y5,
  output Y6,
  output Y7,
  output Y8,
  output Y9,
  output Y10,
  output Y11,
  output Y12,
  output Y13,
  output Y14,
  output Y15
);

  and and_1 (Y0, ~A3, ~A2, ~A1, ~A0);  // AND_Gate
  and and_2 (Y1, ~A3, ~A2, ~A1, A0);  // AND_Gate
  and and_3 (Y2, ~A3, ~A2, A1, ~A0);  // AND_Gate
  and and_4 (Y3, ~A3, ~A2, A1, A0);  // AND_Gate
  and and_5 (Y4, ~A3, A2, ~A1, ~A0);  // AND_Gate
  and and_6 (Y5, ~A3, A2, ~A1, A0);  // AND_Gate
  and and_7 (Y6, ~A3, A2, A1, ~A0);  // AND_Gate
  and and_8 (Y7, ~A3, A2, A1, A0);  // AND_Gate
  and and_9 (Y8, A3, ~A2, ~A1, ~A0);  // AND_Gate
  and and_10 (Y9, A3, ~A2, ~A1, A0);  // AND_Gate
  and and_11 (Y10, A3, ~A2, A1, ~A0);  // AND_Gate
  and and_12 (Y11, A3, ~A2, A1, A0);  // AND_Gate
  and and_13 (Y12, A3, A2, ~A1, ~A0);  // AND_Gate
  and and_14 (Y13, A3, A2, ~A1, A0);  // AND_Gate
  and and_15 (Y14, A3, A2, A1, ~A0);  // AND_Gate
  and and_16 (Y15, A3, A2, A1, A0);
endmodule

module PC (
  input  clk,
  input  rst,
  input  [7:0] PCin,
  output [7:0] PCout
);

  D_Flip_Flop d_ff_1 (.D(PCin[0]), .clk(clk), .Q(PCout[0]), .reset(rst));  // open: Qn, preset
  D_Flip_Flop d_ff_2 (.D(PCin[1]), .clk(clk), .Q(PCout[1]), .reset(rst));  // open: Qn, preset
  D_Flip_Flop d_ff_3 (.D(PCin[2]), .clk(clk), .Q(PCout[2]), .reset(rst));  // open: Qn, preset
  D_Flip_Flop d_ff_4 (.D(PCin[3]), .clk(clk), .Q(PCout[3]), .reset(rst));  // open: Qn, preset
  D_Flip_Flop d_ff_5 (.D(PCin[4]), .clk(clk), .Q(PCout[4]), .reset(rst));  // open: Qn, preset
  D_Flip_Flop d_ff_6 (.D(PCin[5]), .clk(clk), .Q(PCout[5]), .reset(rst));  // open: Qn, preset
  D_Flip_Flop d_ff_7 (.D(PCin[6]), .clk(clk), .Q(PCout[6]), .reset(rst));  // open: Qn, preset
  D_Flip_Flop d_ff_8 (.D(PCin[7]), .clk(clk), .Q(PCout[7]), .reset(rst));  // open: Qn, preset
endmodule

module decoder_2_4 (
  input  A1,
  input  A0,
  output Y0,
  output Y1,
  output Y2,
  output Y3
);

  and and_1 (Y0, ~A1, ~A0);  // AND_Gate
  and and_2 (Y1, ~A1, A0);  // AND_Gate
  and and_3 (Y2, A1, ~A0);  // AND_Gate
  and and_4 (Y3, A1, A0);
endmodule

module GPR (
  input  D7,
  input  D6,
  input  D5,
  input  D4,
  input  D3,
  input  D2,
  input  D1,
  input  D0,
  input  [1:0] addr,
  input  en,
  input  clk,
  output Q7,
  output Q6,
  output Q5,
  output Q4,
  output Q3,
  output Q2,
  output Q1,
  output Q0
);

  wire and_1_out, and_2_out, and_5_out, and_6_out, and_7_out, and_8_out, and_9_out, and_10_out, and_11_out,
       and_12_out, and_13_out, and_14_out, and_15_out, and_16_out, and_17_out, and_18_out, and_19_out,
       and_20_out, and_21_out, and_22_out, and_23_out, and_24_out, and_25_out, and_26_out, and_27_out,
       and_28_out, and_29_out, and_30_out, and_31_out, and_32_out, and_33_out, and_34_out, and_35_out,
       and_36_out, decoder_2_4_1_y0, decoder_2_4_1_y1, decoder_2_4_1_y2, decoder_2_4_1_y3, dff_en_1_q,
       dff_en_2_q, dff_en_3_q, dff_en_4_q, dff_en_5_q, dff_en_6_q, dff_en_7_q, dff_en_8_q, dff_en_9_q,
       dff_en_10_q, dff_en_11_q, dff_en_12_q, dff_en_13_q, dff_en_14_q, dff_en_15_q, dff_en_16_q,
       dff_en_17_q, dff_en_18_q, dff_en_19_q, dff_en_20_q, dff_en_21_q, dff_en_22_q, dff_en_23_q,
       dff_en_24_q, dff_en_25_q, dff_en_26_q, dff_en_27_q, dff_en_28_q, dff_en_29_q, dff_en_30_q,
       dff_en_31_q, dff_en_32_q;

  decoder_2_4 decoder_2_4_1 (
    .A1(addr[1]), .A0(addr[0]), .Y0(decoder_2_4_1_y0), .Y1(decoder_2_4_1_y1), .Y2(decoder_2_4_1_y2),
    .Y3(decoder_2_4_1_y3));
  and and_1 (and_1_out, decoder_2_4_1_y0, en);
  and and_2 (and_2_out, decoder_2_4_1_y1, en);
  and and_3 (decoder_2_4_1_y2, decoder_2_4_1_y2, en);
  and and_4 (decoder_2_4_1_y3, en, decoder_2_4_1_y3);
  and and_5 (and_5_out, decoder_2_4_1_y0, dff_en_1_q);
  DFF_en dff_en_1 (.clk(clk), .D(D7), .en(and_1_out), .Q(dff_en_1_q));
  and and_6 (and_6_out, decoder_2_4_1_y1, dff_en_2_q);
  DFF_en dff_en_2 (.clk(clk), .D(D7), .en(and_2_out), .Q(dff_en_2_q));
  and and_7 (and_7_out, decoder_2_4_1_y2, dff_en_3_q);
  DFF_en dff_en_3 (.clk(clk), .D(D7), .en(decoder_2_4_1_y2), .Q(dff_en_3_q));
  and and_8 (and_8_out, decoder_2_4_1_y3, dff_en_4_q);
  DFF_en dff_en_4 (.clk(clk), .D(D7), .en(decoder_2_4_1_y3), .Q(dff_en_4_q));
  or or_1 (Q7, and_8_out, and_7_out, and_6_out, and_5_out);
  and and_9 (and_9_out, decoder_2_4_1_y0, dff_en_5_q);
  DFF_en dff_en_5 (.clk(clk), .D(D6), .en(and_1_out), .Q(dff_en_5_q));
  and and_10 (and_10_out, decoder_2_4_1_y1, dff_en_6_q);
  DFF_en dff_en_6 (.clk(clk), .D(D6), .en(and_2_out), .Q(dff_en_6_q));
  and and_11 (and_11_out, decoder_2_4_1_y2, dff_en_7_q);
  DFF_en dff_en_7 (.clk(clk), .D(D6), .en(decoder_2_4_1_y2), .Q(dff_en_7_q));
  and and_12 (and_12_out, decoder_2_4_1_y3, dff_en_8_q);
  DFF_en dff_en_8 (.clk(clk), .D(D6), .en(decoder_2_4_1_y3), .Q(dff_en_8_q));
  or or_2 (Q6, and_12_out, and_11_out, and_10_out, and_9_out);
  and and_13 (and_13_out, decoder_2_4_1_y0, dff_en_9_q);
  DFF_en dff_en_9 (.clk(clk), .D(D5), .en(and_1_out), .Q(dff_en_9_q));
  and and_14 (and_14_out, decoder_2_4_1_y1, dff_en_10_q);
  DFF_en dff_en_10 (.clk(clk), .D(D5), .en(and_2_out), .Q(dff_en_10_q));
  and and_15 (and_15_out, decoder_2_4_1_y2, dff_en_11_q);
  DFF_en dff_en_11 (.clk(clk), .D(D5), .en(decoder_2_4_1_y2), .Q(dff_en_11_q));
  and and_16 (and_16_out, decoder_2_4_1_y3, dff_en_12_q);
  DFF_en dff_en_12 (.clk(clk), .D(D5), .en(decoder_2_4_1_y3), .Q(dff_en_12_q));
  or or_3 (Q5, and_16_out, and_15_out, and_14_out, and_13_out);
  and and_17 (and_17_out, decoder_2_4_1_y0, dff_en_13_q);
  DFF_en dff_en_13 (.clk(clk), .D(D4), .en(and_1_out), .Q(dff_en_13_q));
  and and_18 (and_18_out, decoder_2_4_1_y1, dff_en_14_q);
  DFF_en dff_en_14 (.clk(clk), .D(D4), .en(and_2_out), .Q(dff_en_14_q));
  and and_19 (and_19_out, decoder_2_4_1_y2, dff_en_15_q);
  DFF_en dff_en_15 (.clk(clk), .D(D4), .en(decoder_2_4_1_y2), .Q(dff_en_15_q));
  and and_20 (and_20_out, decoder_2_4_1_y3, dff_en_16_q);
  DFF_en dff_en_16 (.clk(clk), .D(D4), .en(decoder_2_4_1_y3), .Q(dff_en_16_q));
  or or_4 (Q4, and_20_out, and_19_out, and_18_out, and_17_out);
  and and_21 (and_21_out, decoder_2_4_1_y0, dff_en_17_q);
  DFF_en dff_en_17 (.clk(clk), .D(D3), .en(and_1_out), .Q(dff_en_17_q));
  and and_22 (and_22_out, decoder_2_4_1_y1, dff_en_18_q);
  DFF_en dff_en_18 (.clk(clk), .D(D3), .en(and_2_out), .Q(dff_en_18_q));
  and and_23 (and_23_out, decoder_2_4_1_y2, dff_en_19_q);
  DFF_en dff_en_19 (.clk(clk), .D(D3), .en(decoder_2_4_1_y2), .Q(dff_en_19_q));
  and and_24 (and_24_out, decoder_2_4_1_y3, dff_en_20_q);
  DFF_en dff_en_20 (.clk(clk), .D(D3), .en(decoder_2_4_1_y3), .Q(dff_en_20_q));
  or or_5 (Q3, and_24_out, and_23_out, and_22_out, and_21_out);
  and and_25 (and_25_out, decoder_2_4_1_y0, dff_en_21_q);
  DFF_en dff_en_21 (.clk(clk), .D(D2), .en(and_1_out), .Q(dff_en_21_q));
  and and_26 (and_26_out, decoder_2_4_1_y1, dff_en_22_q);
  DFF_en dff_en_22 (.clk(clk), .D(D2), .en(and_2_out), .Q(dff_en_22_q));
  and and_27 (and_27_out, decoder_2_4_1_y2, dff_en_23_q);
  DFF_en dff_en_23 (.clk(clk), .D(D2), .en(decoder_2_4_1_y2), .Q(dff_en_23_q));
  and and_28 (and_28_out, decoder_2_4_1_y3, dff_en_24_q);
  DFF_en dff_en_24 (.clk(clk), .D(D2), .en(decoder_2_4_1_y3), .Q(dff_en_24_q));
  or or_6 (Q2, and_28_out, and_27_out, and_26_out, and_25_out);
  and and_29 (and_29_out, decoder_2_4_1_y0, dff_en_25_q);
  DFF_en dff_en_25 (.clk(clk), .D(D1), .en(and_1_out), .Q(dff_en_25_q));
  and and_30 (and_30_out, decoder_2_4_1_y1, dff_en_26_q);
  DFF_en dff_en_26 (.clk(clk), .D(D1), .en(and_2_out), .Q(dff_en_26_q));
  and and_31 (and_31_out, decoder_2_4_1_y2, dff_en_27_q);
  DFF_en dff_en_27 (.clk(clk), .D(D1), .en(decoder_2_4_1_y2), .Q(dff_en_27_q));
  and and_32 (and_32_out, decoder_2_4_1_y3, dff_en_28_q);
  DFF_en dff_en_28 (.clk(clk), .D(D1), .en(decoder_2_4_1_y3), .Q(dff_en_28_q));
  or or_7 (Q1, and_32_out, and_31_out, and_30_out, and_29_out);
  and and_33 (and_33_out, decoder_2_4_1_y0, dff_en_29_q);
  DFF_en dff_en_29 (.clk(clk), .D(D0), .en(and_1_out), .Q(dff_en_29_q));
  and and_34 (and_34_out, decoder_2_4_1_y1, dff_en_30_q);
  DFF_en dff_en_30 (.clk(clk), .D(D0), .en(and_2_out), .Q(dff_en_30_q));
  and and_35 (and_35_out, decoder_2_4_1_y2, dff_en_31_q);
  DFF_en dff_en_31 (.clk(clk), .D(D0), .en(decoder_2_4_1_y2), .Q(dff_en_31_q));
  and and_36 (and_36_out, decoder_2_4_1_y3, dff_en_32_q);
  DFF_en dff_en_32 (.clk(clk), .D(D0), .en(decoder_2_4_1_y3), .Q(dff_en_32_q));
  or or_8 (Q0, and_36_out, and_35_out, and_34_out, and_33_out);
endmodule

module GPR_rst (
  input  D7,
  input  D6,
  input  D5,
  input  D4,
  input  D3,
  input  D2,
  input  D1,
  input  D0,
  input  rst,
  input  [1:0] addr,
  input  en,
  input  clk,
  output Q7,
  output Q6,
  output Q5,
  output Q4,
  output Q3,
  output Q2,
  output Q1,
  output Q0
);

  wire and_1_out, and_2_out, and_3_out, and_4_out, and_5_out, and_6_out, and_7_out, and_8_out, and_9_out,
       and_10_out, and_11_out, and_12_out, and_13_out, and_14_out, and_15_out, and_16_out, and_17_out,
       and_18_out, and_19_out, and_20_out, and_21_out, and_22_out, and_23_out, and_24_out, and_25_out,
       and_26_out, and_27_out, and_28_out, and_29_out, and_30_out, and_31_out, and_32_out, and_33_out,
       and_34_out, and_35_out, and_36_out, decoder_2_4_1_y0, decoder_2_4_1_y1, decoder_2_4_1_y2,
       decoder_2_4_1_y3, dff_en_rst_1_q, dff_en_rst_2_q, dff_en_rst_3_q, dff_en_rst_4_q, dff_en_rst_5_q,
       dff_en_rst_6_q, dff_en_rst_7_q, dff_en_rst_8_q, dff_en_rst_9_q, dff_en_rst_10_q, dff_en_rst_11_q,
       dff_en_rst_12_q, dff_en_rst_13_q, dff_en_rst_14_q, dff_en_rst_15_q, dff_en_rst_16_q, dff_en_rst_17_q,
       dff_en_rst_18_q, dff_en_rst_19_q, dff_en_rst_20_q, dff_en_rst_21_q, dff_en_rst_22_q, dff_en_rst_23_q,
       dff_en_rst_24_q, dff_en_rst_25_q, dff_en_rst_26_q, dff_en_rst_27_q, dff_en_rst_28_q, dff_en_rst_29_q,
       dff_en_rst_30_q, dff_en_rst_31_q, dff_en_rst_32_q;

  decoder_2_4 decoder_2_4_1 (
    .A1(addr[1]), .A0(addr[0]), .Y0(decoder_2_4_1_y0), .Y1(decoder_2_4_1_y1), .Y2(decoder_2_4_1_y2),
    .Y3(decoder_2_4_1_y3));
  and and_1 (and_1_out, decoder_2_4_1_y0, en);
  and and_2 (and_2_out, decoder_2_4_1_y1, en);
  and and_3 (and_3_out, decoder_2_4_1_y2, en);
  and and_4 (and_4_out, en, decoder_2_4_1_y3);
  DFF_en_rst dff_en_rst_1 (.rst(rst), .clk(clk), .D(D7), .en(and_1_out), .Q(dff_en_rst_1_q));
  DFF_en_rst dff_en_rst_2 (.rst(rst), .clk(clk), .D(D7), .en(and_2_out), .Q(dff_en_rst_2_q));
  DFF_en_rst dff_en_rst_3 (.rst(rst), .clk(clk), .D(D7), .en(and_3_out), .Q(dff_en_rst_3_q));
  DFF_en_rst dff_en_rst_4 (.rst(rst), .clk(clk), .D(D7), .en(and_4_out), .Q(dff_en_rst_4_q));
  and and_5 (and_5_out, decoder_2_4_1_y0, dff_en_rst_1_q);
  and and_6 (and_6_out, decoder_2_4_1_y1, dff_en_rst_2_q);
  and and_7 (and_7_out, decoder_2_4_1_y2, dff_en_rst_3_q);
  and and_8 (and_8_out, decoder_2_4_1_y3, dff_en_rst_4_q);
  or or_1 (Q7, and_8_out, and_7_out, and_6_out, and_5_out);
  DFF_en_rst dff_en_rst_5 (.rst(rst), .clk(clk), .D(D6), .en(and_1_out), .Q(dff_en_rst_5_q));
  and and_9 (and_9_out, decoder_2_4_1_y0, dff_en_rst_5_q);
  DFF_en_rst dff_en_rst_6 (.rst(rst), .clk(clk), .D(D6), .en(and_2_out), .Q(dff_en_rst_6_q));
  and and_10 (and_10_out, decoder_2_4_1_y1, dff_en_rst_6_q);
  DFF_en_rst dff_en_rst_7 (.rst(rst), .clk(clk), .D(D6), .en(and_3_out), .Q(dff_en_rst_7_q));
  and and_11 (and_11_out, decoder_2_4_1_y2, dff_en_rst_7_q);
  DFF_en_rst dff_en_rst_8 (.rst(rst), .clk(clk), .D(D6), .en(and_4_out), .Q(dff_en_rst_8_q));
  and and_12 (and_12_out, decoder_2_4_1_y3, dff_en_rst_8_q);
  or or_2 (Q6, and_12_out, and_11_out, and_10_out, and_9_out);
  DFF_en_rst dff_en_rst_9 (.rst(rst), .clk(clk), .D(D5), .en(and_1_out), .Q(dff_en_rst_9_q));
  and and_13 (and_13_out, decoder_2_4_1_y0, dff_en_rst_9_q);
  DFF_en_rst dff_en_rst_10 (.rst(rst), .clk(clk), .D(D5), .en(and_2_out), .Q(dff_en_rst_10_q));
  and and_14 (and_14_out, decoder_2_4_1_y1, dff_en_rst_10_q);
  DFF_en_rst dff_en_rst_11 (.rst(rst), .clk(clk), .D(D5), .en(and_3_out), .Q(dff_en_rst_11_q));
  and and_15 (and_15_out, decoder_2_4_1_y2, dff_en_rst_11_q);
  DFF_en_rst dff_en_rst_12 (.rst(rst), .clk(clk), .D(D5), .en(and_4_out), .Q(dff_en_rst_12_q));
  and and_16 (and_16_out, decoder_2_4_1_y3, dff_en_rst_12_q);
  or or_3 (Q5, and_16_out, and_15_out, and_14_out, and_13_out);
  DFF_en_rst dff_en_rst_13 (.rst(rst), .clk(clk), .D(D4), .en(and_1_out), .Q(dff_en_rst_13_q));
  DFF_en_rst dff_en_rst_14 (.rst(rst), .clk(clk), .D(D4), .en(and_2_out), .Q(dff_en_rst_14_q));
  DFF_en_rst dff_en_rst_15 (.rst(rst), .clk(clk), .D(D4), .en(and_3_out), .Q(dff_en_rst_15_q));
  DFF_en_rst dff_en_rst_16 (.rst(rst), .clk(clk), .D(D4), .en(and_4_out), .Q(dff_en_rst_16_q));
  and and_17 (and_17_out, decoder_2_4_1_y0, dff_en_rst_13_q);
  and and_18 (and_18_out, decoder_2_4_1_y1, dff_en_rst_14_q);
  and and_19 (and_19_out, decoder_2_4_1_y2, dff_en_rst_15_q);
  and and_20 (and_20_out, decoder_2_4_1_y3, dff_en_rst_16_q);
  or or_4 (Q4, and_20_out, and_19_out, and_18_out, and_17_out);
  DFF_en_rst dff_en_rst_17 (.rst(rst), .clk(clk), .D(D3), .en(and_1_out), .Q(dff_en_rst_17_q));
  DFF_en_rst dff_en_rst_18 (.rst(rst), .clk(clk), .D(D3), .en(and_2_out), .Q(dff_en_rst_18_q));
  DFF_en_rst dff_en_rst_19 (.rst(rst), .clk(clk), .D(D3), .en(and_3_out), .Q(dff_en_rst_19_q));
  DFF_en_rst dff_en_rst_20 (.rst(rst), .clk(clk), .D(D3), .en(and_4_out), .Q(dff_en_rst_20_q));
  and and_21 (and_21_out, decoder_2_4_1_y0, dff_en_rst_17_q);
  and and_22 (and_22_out, decoder_2_4_1_y1, dff_en_rst_18_q);
  and and_23 (and_23_out, decoder_2_4_1_y2, dff_en_rst_19_q);
  and and_24 (and_24_out, decoder_2_4_1_y3, dff_en_rst_20_q);
  or or_5 (Q3, and_24_out, and_23_out, and_22_out, and_21_out);
  DFF_en_rst dff_en_rst_21 (.rst(rst), .clk(clk), .D(D2), .en(and_1_out), .Q(dff_en_rst_21_q));
  and and_25 (and_25_out, decoder_2_4_1_y0, dff_en_rst_21_q);
  DFF_en_rst dff_en_rst_22 (.rst(rst), .clk(clk), .D(D2), .en(and_2_out), .Q(dff_en_rst_22_q));
  and and_26 (and_26_out, decoder_2_4_1_y1, dff_en_rst_22_q);
  DFF_en_rst dff_en_rst_23 (.rst(rst), .clk(clk), .D(D2), .en(and_3_out), .Q(dff_en_rst_23_q));
  and and_27 (and_27_out, decoder_2_4_1_y2, dff_en_rst_23_q);
  DFF_en_rst dff_en_rst_24 (.rst(rst), .clk(clk), .D(D2), .en(and_4_out), .Q(dff_en_rst_24_q));
  and and_28 (and_28_out, decoder_2_4_1_y3, dff_en_rst_24_q);
  or or_6 (Q2, and_28_out, and_27_out, and_26_out, and_25_out);
  DFF_en_rst dff_en_rst_25 (.rst(rst), .clk(clk), .D(D1), .en(and_1_out), .Q(dff_en_rst_25_q));
  and and_29 (and_29_out, decoder_2_4_1_y0, dff_en_rst_25_q);
  DFF_en_rst dff_en_rst_26 (.rst(rst), .clk(clk), .D(D1), .en(and_2_out), .Q(dff_en_rst_26_q));
  and and_30 (and_30_out, decoder_2_4_1_y1, dff_en_rst_26_q);
  DFF_en_rst dff_en_rst_27 (.rst(rst), .clk(clk), .D(D1), .en(and_3_out), .Q(dff_en_rst_27_q));
  and and_31 (and_31_out, decoder_2_4_1_y2, dff_en_rst_27_q);
  DFF_en_rst dff_en_rst_28 (.rst(rst), .clk(clk), .D(D1), .en(and_4_out), .Q(dff_en_rst_28_q));
  and and_32 (and_32_out, decoder_2_4_1_y3, dff_en_rst_28_q);
  or or_7 (Q1, and_32_out, and_31_out, and_30_out, and_29_out);
  DFF_en_rst dff_en_rst_29 (.rst(rst), .clk(clk), .D(D0), .en(and_1_out), .Q(dff_en_rst_29_q));
  DFF_en_rst dff_en_rst_30 (.rst(rst), .clk(clk), .D(D0), .en(and_2_out), .Q(dff_en_rst_30_q));
  DFF_en_rst dff_en_rst_31 (.rst(rst), .clk(clk), .D(D0), .en(and_3_out), .Q(dff_en_rst_31_q));
  DFF_en_rst dff_en_rst_32 (.rst(rst), .clk(clk), .D(D0), .en(and_4_out), .Q(dff_en_rst_32_q));
  and and_33 (and_33_out, decoder_2_4_1_y0, dff_en_rst_29_q);
  and and_34 (and_34_out, decoder_2_4_1_y1, dff_en_rst_30_q);
  and and_35 (and_35_out, decoder_2_4_1_y2, dff_en_rst_31_q);
  and and_36 (and_36_out, decoder_2_4_1_y3, dff_en_rst_32_q);
  or or_8 (Q0, and_36_out, and_35_out, and_34_out, and_33_out);

  // Notes on the sheet:
  //   r0
  //   r1
  //   r2
  //   r3
endmodule

module sCPU_onlyli (
  input  rst,
  input  en,
  output [7:0] GPRout
);

  wire and_1_out, clk_out;
  wire [3:0] hexcounter_1_q0, pc_1_p5;
  wire [7:0] insrom_1_romout;

  Clock clk (.out(clk_out));
  hexCounter hexcounter_1 (
    .rst(rst), .clk(clk_out), .en(en), .Q0(hexcounter_1_q0[0]), .Q1(hexcounter_1_q0[1]),
    .Q2(hexcounter_1_q0[2]), .Q3(hexcounter_1_q0[3]));  // open: carry
  // PC pc_1: pin names not known; wires that end beside it: hexcounter_1_q0, rst, en, clk_out, pc_1_p5
  insROM insrom_1 (.addr(pc_1_p5), .ROMout(insrom_1_romout));
  and and_1 (and_1_out, insrom_1_romout[7], ~insrom_1_romout[6]);  // AND_Gate
  GPR_rst gpr_rst_1 (
    .D3(insrom_1_romout[3]), .D2(insrom_1_romout[2]), .D1(insrom_1_romout[1]), .D0(insrom_1_romout[0]),
    .rst(rst), .addr(insrom_1_romout[5:4]), .en(and_1_out), .clk(clk_out), .Q7(GPRout[7]), .Q6(GPRout[6]),
    .Q5(GPRout[5]), .Q4(GPRout[4]), .Q3(GPRout[3]), .Q2(GPRout[2]), .Q1(GPRout[1]), .Q0(GPRout[0]));  // open: D7, D6, D5, D4
endmodule

module GPR_WR (
  input  [7:0] wdata,
  input  [1:0] waddr,
  input  wen,
  input  [1:0] raddr1,
  input  [1:0] raddr2,
  input  rst,
  input  clk,
  output [7:0] rdata1,
  output [7:0] rdata2
);

  wire and_1_out, and_2_out, and_3_out, and_4_out, and_5_out, and_6_out, and_7_out, and_8_out, and_9_out,
       and_10_out, and_11_out, and_12_out, and_13_out, and_14_out, and_15_out, and_16_out, and_17_out,
       and_18_out, and_19_out, and_20_out, and_21_out, and_22_out, and_23_out, and_24_out, and_25_out,
       and_26_out, and_27_out, and_28_out, and_29_out, and_30_out, and_31_out, and_32_out, and_33_out,
       and_34_out, and_35_out, and_36_out, and_37_out, and_38_out, and_39_out, and_40_out, and_41_out,
       and_42_out, and_43_out, and_44_out, and_45_out, and_46_out, and_47_out, and_48_out, and_49_out,
       and_50_out, and_51_out, and_52_out, and_53_out, and_54_out, and_55_out, and_56_out, and_57_out,
       and_58_out, and_59_out, and_60_out, and_61_out, and_62_out, and_63_out, and_64_out, and_65_out,
       and_66_out, and_67_out, and_68_out, decoder_2_4_1_y0, decoder_2_4_1_y1, decoder_2_4_1_y2,
       decoder_2_4_1_y3, decoder_2_4_2_y0, decoder_2_4_2_y1, decoder_2_4_2_y2, decoder_2_4_2_y3,
       decoder_2_4_3_y0, decoder_2_4_3_y1, decoder_2_4_3_y2, decoder_2_4_3_y3, dff_en_rst_1_q,
       dff_en_rst_2_q, dff_en_rst_3_q, dff_en_rst_4_q, dff_en_rst_5_q, dff_en_rst_6_q, dff_en_rst_7_q,
       dff_en_rst_8_q, dff_en_rst_9_q, dff_en_rst_10_q, dff_en_rst_11_q, dff_en_rst_12_q, dff_en_rst_13_q,
       dff_en_rst_14_q, dff_en_rst_15_q, dff_en_rst_16_q, dff_en_rst_17_q, dff_en_rst_18_q, dff_en_rst_19_q,
       dff_en_rst_20_q, dff_en_rst_21_q, dff_en_rst_22_q, dff_en_rst_23_q, dff_en_rst_24_q, dff_en_rst_25_q,
       dff_en_rst_26_q, dff_en_rst_27_q, dff_en_rst_28_q, dff_en_rst_29_q, dff_en_rst_30_q, dff_en_rst_31_q,
       dff_en_rst_32_q;

  decoder_2_4 decoder_2_4_1 (
    .A1(waddr[1]), .A0(waddr[0]), .Y0(decoder_2_4_1_y0), .Y1(decoder_2_4_1_y1), .Y2(decoder_2_4_1_y2),
    .Y3(decoder_2_4_1_y3));
  decoder_2_4 decoder_2_4_2 (
    .A1(raddr1[1]), .A0(raddr1[0]), .Y0(decoder_2_4_2_y0), .Y1(decoder_2_4_2_y1), .Y2(decoder_2_4_2_y2),
    .Y3(decoder_2_4_2_y3));
  decoder_2_4 decoder_2_4_3 (
    .A1(raddr2[1]), .A0(raddr2[0]), .Y0(decoder_2_4_3_y0), .Y1(decoder_2_4_3_y1), .Y2(decoder_2_4_3_y2),
    .Y3(decoder_2_4_3_y3));
  and and_1 (and_1_out, decoder_2_4_1_y0, wen);
  and and_2 (and_2_out, decoder_2_4_1_y1, wen);
  and and_3 (and_3_out, decoder_2_4_1_y2, wen);
  and and_4 (and_4_out, wen, decoder_2_4_1_y3);
  DFF_en_rst dff_en_rst_1 (.rst(rst), .clk(clk), .D(wdata[7]), .en(and_1_out), .Q(dff_en_rst_1_q));
  DFF_en_rst dff_en_rst_2 (.rst(rst), .clk(clk), .D(wdata[7]), .en(and_2_out), .Q(dff_en_rst_2_q));
  DFF_en_rst dff_en_rst_3 (.rst(rst), .clk(clk), .D(wdata[7]), .en(and_3_out), .Q(dff_en_rst_3_q));
  DFF_en_rst dff_en_rst_4 (.rst(rst), .clk(clk), .D(wdata[7]), .en(and_4_out), .Q(dff_en_rst_4_q));
  and and_5 (and_5_out, dff_en_rst_1_q, decoder_2_4_2_y0);
  and and_6 (and_6_out, dff_en_rst_2_q, decoder_2_4_2_y1);
  and and_7 (and_7_out, dff_en_rst_3_q, decoder_2_4_2_y2);
  and and_8 (and_8_out, dff_en_rst_4_q, decoder_2_4_2_y3);
  or or_1 (rdata1[7], and_8_out, and_7_out, and_6_out, and_5_out);
  and and_9 (and_9_out, dff_en_rst_1_q, decoder_2_4_3_y0);
  and and_10 (and_10_out, dff_en_rst_2_q, decoder_2_4_3_y1);
  and and_11 (and_11_out, dff_en_rst_3_q, decoder_2_4_3_y2);
  and and_12 (and_12_out, dff_en_rst_4_q, decoder_2_4_3_y3);
  or or_2 (rdata2[7], and_12_out, and_11_out, and_10_out, and_9_out);
  DFF_en_rst dff_en_rst_5 (.rst(rst), .clk(clk), .D(wdata[6]), .en(and_1_out), .Q(dff_en_rst_5_q));
  DFF_en_rst dff_en_rst_6 (.rst(rst), .clk(clk), .D(wdata[6]), .en(and_2_out), .Q(dff_en_rst_6_q));
  DFF_en_rst dff_en_rst_7 (.rst(rst), .clk(clk), .D(wdata[6]), .en(and_3_out), .Q(dff_en_rst_7_q));
  DFF_en_rst dff_en_rst_8 (.rst(rst), .clk(clk), .D(wdata[6]), .en(and_4_out), .Q(dff_en_rst_8_q));
  and and_13 (and_13_out, dff_en_rst_5_q, decoder_2_4_2_y0);
  and and_14 (and_14_out, dff_en_rst_6_q, decoder_2_4_2_y1);
  and and_15 (and_15_out, dff_en_rst_7_q, decoder_2_4_2_y2);
  and and_16 (and_16_out, dff_en_rst_8_q, decoder_2_4_2_y3);
  or or_3 (rdata1[6], and_16_out, and_15_out, and_14_out, and_13_out);
  and and_17 (and_17_out, dff_en_rst_5_q, decoder_2_4_3_y0);
  and and_18 (and_18_out, dff_en_rst_6_q, decoder_2_4_3_y1);
  and and_19 (and_19_out, dff_en_rst_7_q, decoder_2_4_3_y2);
  and and_20 (and_20_out, dff_en_rst_8_q, decoder_2_4_3_y3);
  or or_4 (rdata2[6], and_20_out, and_19_out, and_18_out, and_17_out);
  DFF_en_rst dff_en_rst_9 (.rst(rst), .clk(clk), .D(wdata[5]), .en(and_1_out), .Q(dff_en_rst_9_q));
  and and_21 (and_21_out, dff_en_rst_9_q, decoder_2_4_2_y0);
  DFF_en_rst dff_en_rst_10 (.rst(rst), .clk(clk), .D(wdata[5]), .en(and_2_out), .Q(dff_en_rst_10_q));
  and and_22 (and_22_out, dff_en_rst_10_q, decoder_2_4_2_y1);
  DFF_en_rst dff_en_rst_11 (.rst(rst), .clk(clk), .D(wdata[5]), .en(and_3_out), .Q(dff_en_rst_11_q));
  and and_23 (and_23_out, dff_en_rst_11_q, decoder_2_4_2_y2);
  DFF_en_rst dff_en_rst_12 (.rst(rst), .clk(clk), .D(wdata[5]), .en(and_4_out), .Q(dff_en_rst_12_q));
  and and_24 (and_24_out, dff_en_rst_12_q, decoder_2_4_2_y3);
  and and_25 (and_25_out, dff_en_rst_9_q, decoder_2_4_3_y0);
  and and_26 (and_26_out, dff_en_rst_10_q, decoder_2_4_3_y1);
  and and_27 (and_27_out, dff_en_rst_11_q, decoder_2_4_3_y2);
  and and_28 (and_28_out, dff_en_rst_12_q, decoder_2_4_3_y3);
  or or_5 (rdata1[5], and_24_out, and_23_out, and_22_out, and_21_out);
  or or_6 (rdata2[5], and_28_out, and_27_out, and_26_out, and_25_out);
  DFF_en_rst dff_en_rst_13 (.rst(rst), .clk(clk), .D(wdata[4]), .en(and_1_out), .Q(dff_en_rst_13_q));
  and and_29 (and_29_out, dff_en_rst_13_q, decoder_2_4_2_y0);
  DFF_en_rst dff_en_rst_14 (.rst(rst), .clk(clk), .D(wdata[4]), .en(and_2_out), .Q(dff_en_rst_14_q));
  and and_30 (and_30_out, dff_en_rst_14_q, decoder_2_4_2_y1);
  DFF_en_rst dff_en_rst_15 (.rst(rst), .clk(clk), .D(wdata[4]), .en(and_3_out), .Q(dff_en_rst_15_q));
  and and_31 (and_31_out, dff_en_rst_15_q, decoder_2_4_2_y2);
  DFF_en_rst dff_en_rst_16 (.rst(rst), .clk(clk), .D(wdata[4]), .en(and_4_out), .Q(dff_en_rst_16_q));
  and and_32 (and_32_out, dff_en_rst_16_q, decoder_2_4_2_y3);
  and and_33 (and_33_out, dff_en_rst_13_q, decoder_2_4_3_y0);
  and and_34 (and_34_out, dff_en_rst_14_q, decoder_2_4_3_y1);
  and and_35 (and_35_out, dff_en_rst_15_q, decoder_2_4_3_y2);
  and and_36 (and_36_out, dff_en_rst_16_q, decoder_2_4_3_y3);
  or or_7 (rdata1[4], and_32_out, and_31_out, and_30_out, and_29_out);
  or or_8 (rdata2[4], and_36_out, and_35_out, and_34_out, and_33_out);
  DFF_en_rst dff_en_rst_17 (.rst(rst), .clk(clk), .D(wdata[3]), .en(and_1_out), .Q(dff_en_rst_17_q));
  and and_37 (and_37_out, dff_en_rst_17_q, decoder_2_4_2_y0);
  DFF_en_rst dff_en_rst_18 (.rst(rst), .clk(clk), .D(wdata[3]), .en(and_2_out), .Q(dff_en_rst_18_q));
  and and_38 (and_38_out, dff_en_rst_18_q, decoder_2_4_2_y1);
  DFF_en_rst dff_en_rst_19 (.rst(rst), .clk(clk), .D(wdata[3]), .en(and_3_out), .Q(dff_en_rst_19_q));
  and and_39 (and_39_out, dff_en_rst_19_q, decoder_2_4_2_y2);
  DFF_en_rst dff_en_rst_20 (.rst(rst), .clk(clk), .D(wdata[3]), .en(and_4_out), .Q(dff_en_rst_20_q));
  and and_40 (and_40_out, dff_en_rst_20_q, decoder_2_4_2_y3);
  or or_9 (rdata1[3], and_40_out, and_39_out, and_38_out, and_37_out);
  and and_41 (and_41_out, dff_en_rst_17_q, decoder_2_4_3_y0);
  and and_42 (and_42_out, dff_en_rst_18_q, decoder_2_4_3_y1);
  and and_43 (and_43_out, dff_en_rst_19_q, decoder_2_4_3_y2);
  buf and_44 (and_44_out, dff_en_rst_20_q);  // AND_Gate
  or or_10 (rdata2[3], and_44_out, and_43_out, and_42_out, and_41_out);
  DFF_en_rst dff_en_rst_21 (.rst(rst), .clk(clk), .D(wdata[2]), .en(and_1_out), .Q(dff_en_rst_21_q));
  and and_45 (and_45_out, dff_en_rst_21_q, decoder_2_4_2_y0);
  DFF_en_rst dff_en_rst_22 (.rst(rst), .clk(clk), .D(wdata[2]), .en(and_2_out), .Q(dff_en_rst_22_q));
  and and_46 (and_46_out, dff_en_rst_22_q, decoder_2_4_2_y1);
  DFF_en_rst dff_en_rst_23 (.rst(rst), .clk(clk), .D(wdata[2]), .en(and_3_out), .Q(dff_en_rst_23_q));
  and and_47 (and_47_out, dff_en_rst_23_q, decoder_2_4_2_y2);
  DFF_en_rst dff_en_rst_24 (.rst(rst), .clk(clk), .D(wdata[2]), .en(and_4_out), .Q(dff_en_rst_24_q));
  and and_48 (and_48_out, dff_en_rst_24_q, decoder_2_4_2_y3);
  or or_11 (rdata1[2], and_48_out, and_47_out, and_46_out, and_45_out);
  and and_49 (and_49_out, dff_en_rst_21_q, decoder_2_4_3_y0);
  and and_50 (and_50_out, dff_en_rst_22_q, decoder_2_4_3_y1);
  and and_51 (and_51_out, dff_en_rst_23_q, decoder_2_4_3_y2);
  and and_52 (and_52_out, dff_en_rst_24_q, decoder_2_4_3_y3);
  or or_12 (rdata2[2], and_52_out, and_51_out, and_50_out, and_49_out);
  DFF_en_rst dff_en_rst_25 (.rst(rst), .clk(clk), .D(wdata[1]), .en(and_1_out), .Q(dff_en_rst_25_q));
  and and_53 (and_53_out, dff_en_rst_25_q, decoder_2_4_2_y0);
  DFF_en_rst dff_en_rst_26 (.rst(rst), .clk(clk), .D(wdata[1]), .en(and_2_out), .Q(dff_en_rst_26_q));
  and and_54 (and_54_out, dff_en_rst_26_q, decoder_2_4_2_y1);
  DFF_en_rst dff_en_rst_27 (.rst(rst), .clk(clk), .D(wdata[1]), .en(and_3_out), .Q(dff_en_rst_27_q));
  and and_55 (and_55_out, dff_en_rst_27_q, decoder_2_4_2_y2);
  DFF_en_rst dff_en_rst_28 (.rst(rst), .clk(clk), .D(wdata[1]), .en(and_4_out), .Q(dff_en_rst_28_q));
  and and_56 (and_56_out, dff_en_rst_28_q, decoder_2_4_2_y3);
  or or_13 (rdata1[1], and_56_out, and_55_out, and_54_out, and_53_out);
  and and_57 (and_57_out, dff_en_rst_25_q, decoder_2_4_3_y0);
  and and_58 (and_58_out, dff_en_rst_26_q, decoder_2_4_3_y1);
  and and_59 (and_59_out, dff_en_rst_27_q, decoder_2_4_3_y2);
  and and_60 (and_60_out, dff_en_rst_28_q, decoder_2_4_3_y3);
  or or_14 (rdata2[1], and_60_out, and_59_out, and_58_out, and_57_out);
  DFF_en_rst dff_en_rst_29 (.rst(rst), .clk(clk), .D(wdata[0]), .en(and_1_out), .Q(dff_en_rst_29_q));
  DFF_en_rst dff_en_rst_30 (.rst(rst), .clk(clk), .D(wdata[0]), .en(and_2_out), .Q(dff_en_rst_30_q));
  DFF_en_rst dff_en_rst_31 (.rst(rst), .clk(clk), .D(wdata[0]), .en(and_3_out), .Q(dff_en_rst_31_q));
  DFF_en_rst dff_en_rst_32 (.rst(rst), .clk(clk), .D(wdata[0]), .en(and_4_out), .Q(dff_en_rst_32_q));
  and and_61 (and_61_out, dff_en_rst_29_q, decoder_2_4_2_y0);
  and and_62 (and_62_out, dff_en_rst_30_q, decoder_2_4_2_y1);
  and and_63 (and_63_out, dff_en_rst_31_q, decoder_2_4_2_y2);
  and and_64 (and_64_out, dff_en_rst_32_q, decoder_2_4_2_y3);
  or or_15 (rdata1[0], and_64_out, and_63_out, and_62_out, and_61_out);
  and and_65 (and_65_out, dff_en_rst_29_q, decoder_2_4_3_y0);
  and and_66 (and_66_out, dff_en_rst_30_q, decoder_2_4_3_y1);
  and and_67 (and_67_out, dff_en_rst_31_q, decoder_2_4_3_y2);
  and and_68 (and_68_out, dff_en_rst_32_q, decoder_2_4_3_y3);
  or or_16 (rdata2[0], and_68_out, and_67_out, and_66_out, and_65_out);

  // Notes on the sheet:
  //   r0
  //   r1
  //   r2
  //   r3
endmodule

module comparator8bit (
  input  [7:0] A,
  input  [7:0] B,
  output out_3
);

  wire xnor_1_out, xnor_2_out, xnor_3_out, xnor_4_out, xnor_5_out, xnor_6_out, xnor_7_out, xnor_8_out;

  xnor xnor_1 (xnor_1_out, A[7], B[7]);
  xnor xnor_2 (xnor_2_out, A[6], B[6]);
  xnor xnor_3 (xnor_3_out, A[5], B[5]);
  xnor xnor_4 (xnor_4_out, A[4], B[4]);
  xnor xnor_5 (xnor_5_out, A[3], B[3]);
  xnor xnor_6 (xnor_6_out, A[2], B[2]);
  xnor xnor_7 (xnor_7_out, A[1], B[1]);
  xnor xnor_8 (xnor_8_out, A[0], B[0]);
  and and_1 (out_3, xnor_1_out, xnor_2_out, xnor_3_out, xnor_4_out, xnor_5_out, xnor_6_out, xnor_7_out, xnor_8_out);
endmodule

module insROM_oddsum (
  input  [3:0] addr,
  output [7:0] ROMout
);

  wire decoder4_16_1_y0, decoder4_16_1_y1, decoder4_16_1_y2, decoder4_16_1_y3, decoder4_16_1_y4,
       decoder4_16_1_y5, decoder4_16_1_y6, decoder4_16_1_y7, decoder4_16_1_y8, decoder4_16_1_y9,
       decoder4_16_1_y10, decoder4_16_1_y11, decoder4_16_1_y12, decoder4_16_1_y13, decoder4_16_1_y14,
       decoder4_16_1_y15;
  wire [7:0] and_1_out, and_2_out, and_3_out, and_4_out, and_5_out, and_6_out, and_7_out, and_8_out,
       and_9_out, and_10_out, and_11_out, and_12_out, and_13_out, and_14_out, and_15_out, and_16_out,
       bit_extender_1_out, bit_extender_2_out, bit_extender_3_out, bit_extender_4_out, bit_extender_5_out,
       bit_extender_6_out, bit_extender_7_out, bit_extender_8_out, bit_extender_9_out, bit_extender_10_out,
       bit_extender_11_out, bit_extender_12_out, bit_extender_13_out, bit_extender_14_out,
       bit_extender_15_out, bit_extender_16_out;

  decoder4_16 decoder4_16_1 (
    .A3(addr[3]), .A2(addr[2]), .A1(addr[1]), .A0(addr[0]), .Y0(decoder4_16_1_y0), .Y1(decoder4_16_1_y1),
    .Y2(decoder4_16_1_y2), .Y3(decoder4_16_1_y3), .Y4(decoder4_16_1_y4), .Y5(decoder4_16_1_y5),
    .Y6(decoder4_16_1_y6), .Y7(decoder4_16_1_y7), .Y8(decoder4_16_1_y8), .Y9(decoder4_16_1_y9),
    .Y10(decoder4_16_1_y10), .Y11(decoder4_16_1_y11), .Y12(decoder4_16_1_y12), .Y13(decoder4_16_1_y13),
    .Y14(decoder4_16_1_y14), .Y15(decoder4_16_1_y15));
  assign bit_extender_1_out = {{7{decoder4_16_1_y0}}, decoder4_16_1_y0};  // Bit_Extender bit_extender_1
  assign bit_extender_2_out = {{7{decoder4_16_1_y1}}, decoder4_16_1_y1};  // Bit_Extender bit_extender_2
  assign bit_extender_3_out = {{7{decoder4_16_1_y2}}, decoder4_16_1_y2};  // Bit_Extender bit_extender_3
  assign bit_extender_4_out = {{7{decoder4_16_1_y3}}, decoder4_16_1_y3};  // Bit_Extender bit_extender_4
  assign bit_extender_5_out = {{7{decoder4_16_1_y4}}, decoder4_16_1_y4};  // Bit_Extender bit_extender_5
  assign bit_extender_6_out = {{7{decoder4_16_1_y5}}, decoder4_16_1_y5};  // Bit_Extender bit_extender_6
  assign bit_extender_7_out = {{7{decoder4_16_1_y6}}, decoder4_16_1_y6};  // Bit_Extender bit_extender_7
  assign bit_extender_8_out = {{7{decoder4_16_1_y7}}, decoder4_16_1_y7};  // Bit_Extender bit_extender_8
  assign bit_extender_9_out = {{7{decoder4_16_1_y8}}, decoder4_16_1_y8};  // Bit_Extender bit_extender_9
  assign bit_extender_10_out = {{7{decoder4_16_1_y9}}, decoder4_16_1_y9};  // Bit_Extender bit_extender_10
  assign bit_extender_11_out = {{7{decoder4_16_1_y10}}, decoder4_16_1_y10};  // Bit_Extender bit_extender_11
  assign bit_extender_12_out = {{7{decoder4_16_1_y11}}, decoder4_16_1_y11};  // Bit_Extender bit_extender_12
  assign bit_extender_13_out = {{7{decoder4_16_1_y12}}, decoder4_16_1_y12};  // Bit_Extender bit_extender_13
  assign bit_extender_14_out = {{7{decoder4_16_1_y13}}, decoder4_16_1_y13};  // Bit_Extender bit_extender_14
  assign bit_extender_15_out = {{7{decoder4_16_1_y14}}, decoder4_16_1_y14};  // Bit_Extender bit_extender_15
  assign bit_extender_16_out = {{7{decoder4_16_1_y15}}, decoder4_16_1_y15};  // Bit_Extender bit_extender_16
  assign and_1_out = 8'h89 & bit_extender_1_out;  // AND_Gate and_1, 8 bits wide
  assign and_2_out = 8'h91 & bit_extender_2_out;  // AND_Gate and_2, 8 bits wide
  assign and_3_out = 8'ha1 & bit_extender_3_out;  // AND_Gate and_3, 8 bits wide
  assign and_4_out = 8'hb2 & bit_extender_4_out;  // AND_Gate and_4, 8 bits wide
  assign and_5_out = 8'h17 & bit_extender_5_out;  // AND_Gate and_5, 8 bits wide
  assign and_6_out = 8'h29 & bit_extender_6_out;  // AND_Gate and_6, 8 bits wide
  assign and_7_out = 8'hd1 & bit_extender_7_out;  // AND_Gate and_7, 8 bits wide
  assign and_8_out = 8'hdf & bit_extender_8_out;  // AND_Gate and_8, 8 bits wide
  assign and_9_out = {8{1'b0}} & bit_extender_9_out;  // AND_Gate and_9, 8 bits wide
  assign and_10_out = {8{1'b0}} & bit_extender_10_out;  // AND_Gate and_10, 8 bits wide
  assign and_11_out = {8{1'b0}} & bit_extender_11_out;  // AND_Gate and_11, 8 bits wide
  assign and_12_out = {8{1'b0}} & bit_extender_12_out;  // AND_Gate and_12, 8 bits wide
  assign and_13_out = {8{1'b0}} & bit_extender_13_out;  // AND_Gate and_13, 8 bits wide
  assign and_14_out = {8{1'b0}} & bit_extender_14_out;  // AND_Gate and_14, 8 bits wide
  assign and_15_out = {8{1'b0}} & bit_extender_15_out;  // AND_Gate and_15, 8 bits wide
  assign and_16_out = {8{1'b0}} & bit_extender_16_out;  // AND_Gate and_16, 8 bits wide
  assign ROMout = and_1_out | and_2_out | and_3_out | and_4_out | and_5_out | and_6_out | and_7_out | and_8_out | and_9_out | and_10_out | and_11_out | and_12_out | and_13_out | and_14_out | and_15_out | and_16_out;  // OR_Gate or_1, 8 bits wide
endmodule

module insRom_outDisplay (
  input  [7:0] addr,
  output [7:0] ROMout
);

  wire decoder4_16_1_y0, decoder4_16_1_y1, decoder4_16_1_y2, decoder4_16_1_y3, decoder4_16_1_y4,
       decoder4_16_1_y5, decoder4_16_1_y6, decoder4_16_1_y7, decoder4_16_1_y8, decoder4_16_1_y9,
       decoder4_16_1_y10, decoder4_16_1_y11, decoder4_16_1_y12, decoder4_16_1_y13, decoder4_16_1_y14,
       decoder4_16_1_y15;
  wire [7:0] and_1_out, and_2_out, and_3_out, and_4_out, and_5_out, and_6_out, and_7_out, and_8_out,
       and_9_out, and_10_out, and_11_out, and_12_out, and_13_out, and_14_out, and_15_out, and_16_out,
       bit_extender_1_out, bit_extender_2_out, bit_extender_3_out, bit_extender_4_out, bit_extender_5_out,
       bit_extender_6_out, bit_extender_7_out, bit_extender_8_out, bit_extender_9_out, bit_extender_10_out,
       bit_extender_11_out, bit_extender_12_out, bit_extender_13_out, bit_extender_14_out,
       bit_extender_15_out, bit_extender_16_out;

  decoder4_16 decoder4_16_1 (
    .A3(addr[3]), .A2(addr[2]), .A1(addr[1]), .A0(addr[0]), .Y0(decoder4_16_1_y0), .Y1(decoder4_16_1_y1),
    .Y2(decoder4_16_1_y2), .Y3(decoder4_16_1_y3), .Y4(decoder4_16_1_y4), .Y5(decoder4_16_1_y5),
    .Y6(decoder4_16_1_y6), .Y7(decoder4_16_1_y7), .Y8(decoder4_16_1_y8), .Y9(decoder4_16_1_y9),
    .Y10(decoder4_16_1_y10), .Y11(decoder4_16_1_y11), .Y12(decoder4_16_1_y12), .Y13(decoder4_16_1_y13),
    .Y14(decoder4_16_1_y14), .Y15(decoder4_16_1_y15));
  assign bit_extender_1_out = {{7{decoder4_16_1_y0}}, decoder4_16_1_y0};  // Bit_Extender bit_extender_1
  assign bit_extender_2_out = {{7{decoder4_16_1_y1}}, decoder4_16_1_y1};  // Bit_Extender bit_extender_2
  assign bit_extender_3_out = {{7{decoder4_16_1_y2}}, decoder4_16_1_y2};  // Bit_Extender bit_extender_3
  assign bit_extender_4_out = {{7{decoder4_16_1_y3}}, decoder4_16_1_y3};  // Bit_Extender bit_extender_4
  assign bit_extender_5_out = {{7{decoder4_16_1_y4}}, decoder4_16_1_y4};  // Bit_Extender bit_extender_5
  assign bit_extender_6_out = {{7{decoder4_16_1_y5}}, decoder4_16_1_y5};  // Bit_Extender bit_extender_6
  assign bit_extender_7_out = {{7{decoder4_16_1_y6}}, decoder4_16_1_y6};  // Bit_Extender bit_extender_7
  assign bit_extender_8_out = {{7{decoder4_16_1_y7}}, decoder4_16_1_y7};  // Bit_Extender bit_extender_8
  assign bit_extender_9_out = {{7{decoder4_16_1_y8}}, decoder4_16_1_y8};  // Bit_Extender bit_extender_9
  assign bit_extender_10_out = {{7{decoder4_16_1_y9}}, decoder4_16_1_y9};  // Bit_Extender bit_extender_10
  assign bit_extender_11_out = {{7{decoder4_16_1_y10}}, decoder4_16_1_y10};  // Bit_Extender bit_extender_11
  assign bit_extender_12_out = {{7{decoder4_16_1_y11}}, decoder4_16_1_y11};  // Bit_Extender bit_extender_12
  assign bit_extender_13_out = {{7{decoder4_16_1_y12}}, decoder4_16_1_y12};  // Bit_Extender bit_extender_13
  assign bit_extender_14_out = {{7{decoder4_16_1_y13}}, decoder4_16_1_y13};  // Bit_Extender bit_extender_14
  assign bit_extender_15_out = {{7{decoder4_16_1_y14}}, decoder4_16_1_y14};  // Bit_Extender bit_extender_15
  assign bit_extender_16_out = {{7{decoder4_16_1_y15}}, decoder4_16_1_y15};  // Bit_Extender bit_extender_16
  assign and_1_out = 8'h90 & bit_extender_1_out;  // AND_Gate and_1, 8 bits wide
  assign and_2_out = 8'ha0 & bit_extender_2_out;  // AND_Gate and_2, 8 bits wide
  assign and_3_out = 8'hb1 & bit_extender_3_out;  // AND_Gate and_3, 8 bits wide
  assign and_4_out = 8'h17 & bit_extender_4_out;  // AND_Gate and_4, 8 bits wide
  assign and_5_out = 8'h29 & bit_extender_5_out;  // AND_Gate and_5, 8 bits wide
  assign and_6_out = 8'h58 & bit_extender_6_out;  // AND_Gate and_6, 8 bits wide
  assign and_7_out = 8'h69 & bit_extender_7_out;  // AND_Gate and_7, 8 bits wide
  assign and_8_out = 8'h41 & bit_extender_8_out;  // AND_Gate and_8, 8 bits wide
  assign and_9_out = {8{1'b1}} & bit_extender_9_out;  // AND_Gate and_9, 8 bits wide
  assign and_10_out = 8'h40 & bit_extender_10_out;  // AND_Gate and_10, 8 bits wide
  assign and_11_out = 8'he5 & bit_extender_11_out;  // AND_Gate and_11, 8 bits wide
  assign and_12_out = 8'hc3 & bit_extender_12_out;  // AND_Gate and_12, 8 bits wide
  assign and_13_out = {8{1'b0}} & bit_extender_13_out;  // AND_Gate and_13, 8 bits wide
  assign and_14_out = {8{1'b0}} & bit_extender_14_out;  // AND_Gate and_14, 8 bits wide
  assign and_15_out = {8{1'b0}} & bit_extender_15_out;  // AND_Gate and_15, 8 bits wide
  assign and_16_out = {8{1'b0}} & bit_extender_16_out;  // AND_Gate and_16, 8 bits wide
  assign ROMout = and_1_out | and_2_out | and_3_out | and_4_out | and_5_out | and_6_out | and_7_out | and_8_out | and_9_out | and_10_out | and_11_out | and_12_out | and_13_out | and_14_out | and_15_out | and_16_out;  // OR_Gate or_1, 8 bits wide
endmodule
